// Logisim project kekw2.2.circ as structural Verilog: 9 circuits, main circuit Main
module Main (
  input  getScore
);

  wire A, addPartToQ, and_1_out, and_3_out, and_4_out, and_5_out, and_6_out, and_7_out, and_8_out,
       and_10_out, and_13_out, and_14_out, and_15_out, and_20_out, and_21_out, and_22_out, and_24_out,
       beatTail, bitshrink_1_a, bitshrink_1_d, bitshrink_1_pause, bitshrink_1_s, bitshrink_1_w,
       cdm_8_mark5_1_p1, cdm_8_mark5_1_p2, cdm_8_mark5_1_p4, cdm_8_mark5_1_p5, cdm_8_mark5_1_p6,
       cdm_8_mark5_1_p7, CI, clock_1_out, code, counter_1_carry, counter_2_carry, counter_3_carry,
       counter_5_carry, D, data, decoder_3_out0, decoder_3_out1, Down, DownT, EnG, gameClock, gameOver,
       I_Oadr, I_Osel, in_out_prime, Left, LeftT, LoadPartToTail, not_1_out, not_2_out, not_3_out, not_4_out,
       not_5_out, not_6_out, not_7_out, not_8_out, not_10_out, or_1_out, or_2_out, or_3_out, or_4_out,
       or_5_out, or_6_out, or_7_out, or_8_out, or_10_out, or_11_out, or_12_out, or_14_out, or_15_out,
       or_16_out, Pause, procGotPart, pull_resistor_2_node, RAM, Restart, Right, RightT, S, Start, Turn, Up,
       UpT, W;
  wire [1:0] bitshrink_1_where, register_2_q, Where;
  wire [4:0] head_1_head_x, head_1_head_y, tail_1_tail_x, tail_1_tail_y;
  wire [5:0] currPart, xnor_1_out;
  wire [5:5] not_9_out;
  wire [6:0] controlled_buffer_3_out, keyboard_1_data;
  wire [7:0] cdm_8_mark5_1_p10, cdm_8_mark5_1_p11, I_Odat;
  wire [7:1] cdm_8_mark5_1_p9;
  wire [9:0] CurrLength;
  wire [31:0] tomatrix_1__0, tomatrix_1_out_11, tomatrix_1_out_12, tomatrix_1_out_13, tomatrix_1_out_14,
       tomatrix_1_out_15, tomatrix_1_out_16, tomatrix_1_out_17, tomatrix_1_out_18, tomatrix_1_out_19,
       tomatrix_1_out_20, tomatrix_1_out_21, tomatrix_1_out_22, tomatrix_1_out_23, tomatrix_1_out_24,
       tomatrix_1_out_25, tomatrix_1_out_26, tomatrix_1_out_27, tomatrix_1_out_28, tomatrix_1_out_29,
       tomatrix_1_out_30, tomatrix_1_out_31, tomatrix_1_out_32, tomatrix_1_out_33, tomatrix_1_out_34,
       tomatrix_1_out_35, tomatrix_1_out_36, tomatrix_1_out_37, tomatrix_1_out_38, tomatrix_1_out_39,
       tomatrix_1_out_40, tomatrix_1_out_41;

  // Probe on cdm_8_mark5_1_p2
  // Probe on cdm_8_mark5_1_p1
  D_Flip_Flop d_ff_1 (.Q(Up), .preset(or_1_out), .reset(or_2_out));  // open: clk, D, Qn, en
  or or_1 (or_1_out, Start, and_1_out);
  or or_2 (or_2_out, A, Restart, D);
  and and_1 (and_1_out, ~Down, W);  // AND_Gate
  Clock clock_1 (.out(clock_1_out));
  and and_2 (CI, clock_1_out, EnG);
  // Probe on cdm_8_mark5_1_p5
  // Probe on cdm_8_mark5_1_p4
  // Probe on cdm_8_mark5_1_p4
  // Probe on cdm_8_mark5_1_p2
  and and_3 (and_3_out, ~Down, ~Up, ~Left, ~Right);  // AND_Gate
  and and_4 (and_4_out, ~Up, S);  // AND_Gate
  Decoder #(.disabled(0)) decoder_1 (.out0(code), .out1(data), .sel(cdm_8_mark5_1_p6), .en(cdm_8_mark5_1_p7));
  // CdM_8_mark5 cdm_8_mark5_1: pin names not known; wires that end beside it: cdm_8_mark5_1_p1, cdm_8_mark5_1_p2, CI, cdm_8_mark5_1_p4, cdm_8_mark5_1_p5, cdm_8_mark5_1_p6, cdm_8_mark5_1_p7, in_out_prime, {cdm_8_mark5_1_p9, I_Oadr}, cdm_8_mark5_1_p10, cdm_8_mark5_1_p11
  not not_1 (not_1_out, in_out_prime);
  assign cdm_8_mark5_1_p11 = in_out_prime ? I_Odat : 8'bz;  // Controlled_Buffer controlled_buffer_1
  or or_3 (or_3_out, Down, Up);
  and and_5 (and_5_out, or_3_out, or_4_out);
  or or_4 (or_4_out, A, D);
  or or_5 (or_5_out, Left, Right);
  and and_6 (and_6_out, or_5_out, or_6_out);
  or or_6 (or_6_out, W, S);
  D_Flip_Flop d_ff_2 (.Q(Down), .preset(and_4_out), .reset(or_7_out));  // open: clk, D, Qn, en
  or or_7 (or_7_out, A, Restart, D);
  and and_7 (and_7_out, ~Right, A);  // AND_Gate
  Counter #(.width(10), .max('h100)) counter_1 (
    .carry(counter_1_carry), .clk(CI), .clr(Restart));  // open: load, D, count, Q
  and and_8 (and_8_out, EnG, ~or_8_out);  // AND_Gate
  or or_8 (or_8_out, gameOver, Pause);
  assign I_Odat = not_1_out ? cdm_8_mark5_1_p10 : 8'bz;  // Controlled_Buffer controlled_buffer_2
  and and_9 (I_Osel, and_13_out, CI, data);
  or or_9 (Turn, and_5_out, and_3_out, and_6_out);
  D_Flip_Flop d_ff_3 (.Q(Left), .preset(and_7_out), .reset(or_10_out));  // open: clk, D, Qn, en
  or or_10 (or_10_out, W, Restart, S);
  and and_10 (and_10_out, ~Left, D);  // AND_Gate
  and and_11 (RAM, ~I_Osel, data);  // AND_Gate
  D_Flip_Flop d_ff_4 (.Q(Right), .preset(and_10_out), .reset(or_11_out));  // open: clk, D, Qn, en
  or or_11 (or_11_out, W, Restart, S);
  and and_12 (gameClock, counter_1_carry, ~Start, and_8_out);  // AND_Gate
  not not_2 (not_2_out, CI);
  // Probe on {cdm_8_mark5_1_p9, I_Oadr}
  and and_13 (and_13_out, ~cdm_8_mark5_1_p9[1], ~cdm_8_mark5_1_p9[2], ~cdm_8_mark5_1_p9[3], ~cdm_8_mark5_1_p9[4], ~cdm_8_mark5_1_p9[5], ~cdm_8_mark5_1_p9[6], ~cdm_8_mark5_1_p9[7]);  // AND_Gate
  ROM rom_1 (.addr({cdm_8_mark5_1_p9, I_Oadr}), .data(I_Odat), .sel(code));
  RAM ram_1 (
    .addr({cdm_8_mark5_1_p9, I_Oadr}), .data(I_Odat), .sel(RAM), .clk(not_2_out), .ld(in_out_prime));  // open: clr
  // Probe on I_Odat
  // Probe on {cdm_8_mark5_1_p9, I_Oadr}
  and and_14 (and_14_out, xnor_1_out[0], xnor_1_out[1], xnor_1_out[2], xnor_1_out[3], xnor_1_out[4], xnor_1_out[5]);
  Counter #(.width(6), .max('h3f)) counter_2 (
    .load(Start), .D(6'b000100), .count(not_3_out), .Q(currPart), .carry(counter_2_carry), .clk(or_12_out),
    .clr(not_5_out));
  not not_3 (not_3_out, Start);
  not not_4 (not_4_out, and_15_out);
  not not_5 (not_5_out, not_4_out);
  or or_12 (or_12_out, Start, gameClock);
  assign xnor_1_out = ~(currPart ^ CurrLength[5:0]);  // XNOR_Gate xnor_1, 6 bits wide
  Keyboard_part keyboard_1 (.clk(CI), .re(not_6_out), .clr(Restart), .data(keyboard_1_data));  // open: avail
  not not_6 (not_6_out, Pause);
  or or_13 (addPartToQ, and_14_out, counter_2_carry, Turn);
  and and_15 (and_15_out, procGotPart, ~CI);  // AND_Gate
  Head head_1 (
    .Up(Up), .Down(Down), .Left(Left), .Right(Right), .Start(Start), .Clock(gameClock),
    .Head_Y(head_1_head_y), .Head_X(head_1_head_x), .Restart(Restart));
  Tail tail_1 (
    .Clock(gameClock), .Start(Start), .Restart(Restart), .getScore(getScore), .Tail_Y(tail_1_tail_y),
    .Tail_X(tail_1_tail_x), .loadTime(LoadPartToTail), .Up(UpT), .Left(DownT), .Down(LeftT), .Right(RightT));
  Counter #(.width(3), .max('h4), .ongoal("stay")) counter_3 (
    .carry(counter_3_carry), .clk(gameClock), .clr(Restart));  // open: load, D, count, Q
  and and_16 (D, ~gameClock, bitshrink_1_d);  // AND_Gate
  and and_17 (S, ~gameClock, bitshrink_1_s);  // AND_Gate
  not not_7 (not_7_out, Start);
  toMatrix tomatrix_1 (
    .Head_X(head_1_head_x), .Tail_X(tail_1_tail_x), .Head_Y(head_1_head_y), .Tail_Y(tail_1_tail_y),
    .Clock(gameClock), ._0(tomatrix_1__0), .out_26(tomatrix_1_out_26), .out_11(tomatrix_1_out_11),
    .out_27(tomatrix_1_out_27), .out_12(tomatrix_1_out_12), .out_28(tomatrix_1_out_28),
    .out_13(tomatrix_1_out_13), .out_29(tomatrix_1_out_29), .out_14(tomatrix_1_out_14),
    .out_30(tomatrix_1_out_30), .out_15(tomatrix_1_out_15), .out_31(tomatrix_1_out_31),
    .out_16(tomatrix_1_out_16), .out_32(tomatrix_1_out_32), .out_17(tomatrix_1_out_17),
    .out_33(tomatrix_1_out_33), .Smash(beatTail), .out_18(tomatrix_1_out_18), .out_34(tomatrix_1_out_34),
    .out_19(tomatrix_1_out_19), .out_35(tomatrix_1_out_35), .out_20(tomatrix_1_out_20),
    .out_36(tomatrix_1_out_36), .out_21(tomatrix_1_out_21), .out_37(tomatrix_1_out_37),
    .out_22(tomatrix_1_out_22), .out_38(tomatrix_1_out_38), .out_23(tomatrix_1_out_23),
    .out_39(tomatrix_1_out_39), .out_24(tomatrix_1_out_24), .out_40(tomatrix_1_out_40),
    .out_25(tomatrix_1_out_25), .out_41(tomatrix_1_out_41), .EnT(EnG), .EnH(EnG), .Restart(Restart));
  DotMatrix #(.inputtype("row"), .matrixcols(32), .matrixrows(32)) dotmatrix_1 (
    .row0(tomatrix_1_out_41), .row1(tomatrix_1_out_40), .row2(tomatrix_1_out_39), .row3(tomatrix_1_out_38),
    .row4(tomatrix_1_out_37), .row5(tomatrix_1_out_36), .row6(tomatrix_1_out_35), .row7(tomatrix_1_out_34),
    .row8(tomatrix_1_out_33), .row9(tomatrix_1_out_32), .row10(tomatrix_1_out_31), .row11(tomatrix_1_out_30),
    .row12(tomatrix_1_out_29), .row13(tomatrix_1_out_28), .row14(tomatrix_1_out_27),
    .row15(tomatrix_1_out_26), .row16(tomatrix_1_out_25), .row17(tomatrix_1_out_24),
    .row18(tomatrix_1_out_23), .row19(tomatrix_1_out_22), .row20(tomatrix_1_out_21),
    .row21(tomatrix_1_out_20), .row22(tomatrix_1_out_19), .row23(tomatrix_1_out_18),
    .row24(tomatrix_1_out_17), .row25(tomatrix_1_out_16), .row26(tomatrix_1_out_15),
    .row27(tomatrix_1_out_14), .row28(tomatrix_1_out_13), .row29(tomatrix_1_out_12),
    .row30(tomatrix_1_out_11), .row31(tomatrix_1__0));
  // Probe on head_1_head_y
  // Probe on head_1_head_x
  // Probe on tail_1_tail_y
  // Probe on tail_1_tail_x
  assign controlled_buffer_3_out = counter_3_carry ? keyboard_1_data : 7'bz;  // Controlled_Buffer controlled_buffer_3
  Pull_Resistor pull_resistor_1 (.node(controlled_buffer_3_out));
  bitShrink bitshrink_1 (
    .In(controlled_buffer_3_out), .W(bitshrink_1_w), .A(bitshrink_1_a), .S(bitshrink_1_s), .D(bitshrink_1_d),
    .Where(bitshrink_1_where), .Pause(bitshrink_1_pause));
  Counter #(.width(10), .max('h3ff), .ongoal("stay")) counter_4 (
    .load(Start), .D(10'h4), .count(not_7_out), .Q(CurrLength), .clk(or_14_out), .clr(Restart));  // open: carry
  or or_14 (or_14_out, Start, getScore);
  Pull_Resistor #(.pull(1)) pull_resistor_2 (.node(pull_resistor_2_node));
  assign pull_resistor_2_node = Pause ? ~bitshrink_1_pause : 1'bz;  // Controlled_Inverter controlled_inverter_1
  and and_18 (W, ~gameClock, bitshrink_1_w);  // AND_Gate
  and and_19 (A, ~gameClock, bitshrink_1_a);  // AND_Gate
  D_Flip_Flop d_ff_5 (.Q(gameOver), .preset(and_20_out), .reset(Restart));  // open: clk, D, Qn, en
  and and_20 (and_20_out, beatTail, ~Start);  // AND_Gate
  Button u_RESTART (.out(Restart));
  and and_21 (and_21_out, ~gameClock, bitshrink_1_pause);  // AND_Gate
  D_Flip_Flop d_ff_6 (.clk(and_21_out), .D(pull_resistor_2_node), .Q(Pause), .reset(Restart));  // open: Qn, preset, en
  Register #(.width(2)) register_1 (.D(bitshrink_1_where), .Q(Where), .clk(Turn));  // open: en, clr
  Button u_START (.out(Start));
  D_Flip_Flop d_ff_7 (.Q(EnG), .preset(Start), .reset(or_15_out));  // open: clk, D, Qn, en
  or or_15 (or_15_out, Restart, gameOver);
  assign I_Odat = and_22_out ? {EnG, addPartToQ, not_9_out[5], {5{1'b0}}} : 8'bz;  // Controlled_Buffer controlled_buffer_4
  assign I_Odat = procGotPart ? {Where, currPart} : 8'bz;  // Controlled_Buffer controlled_buffer_5
  and and_22 (and_22_out, decoder_3_out1, ~I_Oadr);  // AND_Gate
  and and_23 (procGotPart, decoder_3_out1, I_Oadr);
  Counter #(.width(6), .max('h3f), .ongoal("load")) counter_5 (
    .load(1'b1), .D(I_Odat[5:0]), .count(not_8_out), .carry(counter_5_carry), .clk(and_24_out), .clr(Restart));  // open: Q
  not not_8 (not_8_out, LoadPartToTail);
  and and_24 (and_24_out, ~getScore, or_16_out);  // AND_Gate
  or or_16 (or_16_out, gameClock, LoadPartToTail);
  Register #(.width(2), .trigger("falling")) register_2 (
    .D(I_Odat[7:6]), .Q(register_2_q), .clk(LoadPartToTail), .clr(LoadPartToTail));  // open: en
  and and_25 (LoadPartToTail, I_Oadr, decoder_3_out0);
  not not_9 (not_9_out[5], not_10_out);
  Decoder #(.select(2), .disabled(0)) decoder_2 (
    .out0(UpT), .out1(LeftT), .out2(DownT), .out3(RightT), .sel(register_2_q), .en(not_10_out));
  not not_10 (not_10_out, counter_5_carry);
  Decoder #(.disabled(0)) decoder_3 (.out0(decoder_3_out0), .out1(decoder_3_out1), .sel(in_out_prime), .en(I_Osel));

  // Other names for the same wires on the sheet: KeyboardClock = CI; rd_wr_prime = in_out_prime

  // Notes on the sheet:
  //   contents of rom_1 (hex, n*v repeats v):
  //   d0 2 d1 10 a4 8d a4 d0 0 b1 5 e5 9 25 5 e5 1c d0 11 b0 d2 1 ba a2 8c d2 11 a8 25 5 e5 2e d0 10 b0 b0
  //   d2 1 a8 d0 10 b0 8c d2 10 a8 ee 7
endmodule

// TAIL
module Tail (
  input  Clock,
  input  Up,
  input  Start,
  input  Left,
  input  Restart,
  input  Down,
  input  getScore,
  input  Right,
  input  loadTime,
  output [4:0] Tail_Y,
  output [4:0] Tail_X
);

  wire and_1_out, and_2_out, not_1_out, not_2_out, or_1_out, or_2_out, or_3_out, or_4_out, or_5_out, or_6_out;

  or or_1 (or_1_out, Down, Start);
  not not_1 (not_1_out, Start);
  Counter #(.width(5), .max('h1f)) counter_1 (
    .load(or_1_out), .D(5'b01011), .count(not_1_out), .Q(Tail_Y), .clk(or_2_out), .clr(Restart));  // open: carry
  or or_2 (or_2_out, Start, and_1_out);
  and and_1 (and_1_out, ~getScore, or_3_out, Clock);  // AND_Gate
  or or_3 (or_3_out, Up, Down);
  or or_4 (or_4_out, Left, Start);
  not not_2 (not_2_out, Start);
  or or_5 (or_5_out, Start, and_2_out);
  and and_2 (and_2_out, ~getScore, or_6_out, Clock);  // AND_Gate
  or or_6 (or_6_out, Left, Right);
  Counter #(.width(5), .max('h1f)) counter_2 (
    .load(or_4_out), .D(5'b01111), .count(not_2_out), .Q(Tail_X), .clk(or_5_out), .clr(Restart));  // open: carry
endmodule

// HEAD
module Head (
  input  Up,
  input  Down,
  input  Left,
  input  Right,
  input  Start,
  input  Restart,
  input  Clock,
  output [4:0] Head_Y,
  output [4:0] Head_X
);

  wire and_1_out, and_2_out, not_1_out, not_2_out, or_1_out, or_2_out, or_3_out, or_4_out, or_5_out, or_6_out;

  or or_1 (or_1_out, Down, Start);
  not not_1 (not_1_out, Start);
  or or_2 (or_2_out, Start, and_1_out);
  and and_1 (and_1_out, or_3_out, Clock);
  or or_3 (or_3_out, Up, Down);
  Counter #(.width(5), .max('h1f)) counter_1 (
    .load(or_1_out), .D(5'b10000), .count(not_1_out), .Q(Head_Y), .clk(or_2_out), .clr(Restart));  // open: carry
  or or_4 (or_4_out, Left, Start);
  Counter #(.width(5), .max('h1f)) counter_2 (
    .load(or_4_out), .D(5'b01111), .count(not_2_out), .Q(Head_X), .clk(or_5_out), .clr(Restart));  // open: carry
  not not_2 (not_2_out, Start);
  or or_5 (or_5_out, Start, and_2_out);
  and and_2 (and_2_out, or_6_out, Clock);
  or or_6 (or_6_out, Left, Right);
endmodule

module toMatrix (
  input  Restart,
  input  [4:0] Head_X,
  input  [4:0] Tail_X,
  input  Clock,
  input  EnH,
  input  EnT,
  input  [4:0] Head_Y,
  input  [4:0] Tail_Y,
  output Smash,
  output [31:0] _0,
  output [31:0] out_11,
  output [31:0] out_12,
  output [31:0] out_13,
  output [31:0] out_14,
  output [31:0] out_15,
  output [31:0] out_16,
  output [31:0] out_17,
  output [31:0] out_18,
  output [31:0] out_19,
  output [31:0] out_20,
  output [31:0] out_21,
  output [31:0] out_22,
  output [31:0] out_23,
  output [31:0] out_24,
  output [31:0] out_25,
  output [31:0] out_26,
  output [31:0] out_27,
  output [31:0] out_28,
  output [31:0] out_29,
  output [31:0] out_30,
  output [31:0] out_31,
  output [31:0] out_32,
  output [31:0] out_33,
  output [31:0] out_34,
  output [31:0] out_35,
  output [31:0] out_36,
  output [31:0] out_37,
  output [31:0] out_38,
  output [31:0] out_39,
  output [31:0] out_40,
  output [31:0] out_41
);

  wire H0, H1, H2, H3, H4, H5, H6, H7, H8, H9, H10, H11, H12, H13, H14, H15, H16, H17, H18, H19, H20, H21,
       H22, H23, H24, H25, H26, H27, H28, H29, H30, H31, S0, S1, S2, S3, S4, S5, S6, S7, S8, S9, S10, S11,
       S12, S13, S14, S15, S16, S17, S18, S19, S20, S21, S22, S23, S24, S25, S26, S27, S28, S29, S30, S31,
       T0, T1, T2, T3, T4, T5, T6, T7, T8, T9, T10, T11, T12, T13, T14, T15, T16, T17, T18, T19, T20, T21,
       T22, T23, T24, T25, T26, T27, T28, T29, T30, T31;

  Decoder #(.select(5), .disabled(0)) decoder_1 (
    .out0(H0), .out1(H1), .out2(H2), .out3(H3), .out4(H4), .out5(H5), .out6(H6), .out7(H7), .out8(H8),
    .out9(H9), .out10(H10), .out11(H11), .out12(H12), .out13(H13), .out14(H14), .out15(H15), .out16(H16),
    .out17(H17), .out18(H18), .out19(H19), .out20(H20), .out21(H21), .out22(H22), .out23(H23), .out24(H24),
    .out25(H25), .out26(H26), .out27(H27), .out28(H28), .out29(H29), .out30(H30), .out31(H31), .sel(Head_Y),
    .en(EnH));
  Decoder #(.select(5), .disabled(0)) decoder_2 (
    .out0(T0), .out1(T1), .out2(T2), .out3(T3), .out4(T4), .out5(T5), .out6(T6), .out7(T7), .out8(T8),
    .out9(T9), .out10(T10), .out11(T11), .out12(T12), .out13(T13), .out14(T14), .out15(T15), .out16(T16),
    .out17(T17), .out18(T18), .out19(T19), .out20(T20), .out21(T21), .out22(T22), .out23(T23), .out24(T24),
    .out25(T25), .out26(T26), .out27(T27), .out28(T28), .out29(T29), .out30(T30), .out31(T31), .sel(Tail_Y),
    .en(EnT));
  Line line_1 (
    .EnT(T0), .Tail_X(Tail_X), .Head_X(Head_X), .Out(_0), .Smash(S0), .Clock(Clock), .EnH(H0),
    .Restart(Restart));
  Line line_2 (
    .EnT(T1), .Tail_X(Tail_X), .Head_X(Head_X), .Out(out_11), .Smash(S1), .Clock(Clock), .EnH(H1),
    .Restart(Restart));
  Line line_3 (
    .EnT(T2), .Tail_X(Tail_X), .Head_X(Head_X), .Out(out_12), .Smash(S2), .Clock(Clock), .EnH(H2),
    .Restart(Restart));
  Line line_4 (
    .EnT(T3), .Tail_X(Tail_X), .Head_X(Head_X), .Out(out_13), .Smash(S3), .Clock(Clock), .EnH(H3),
    .Restart(Restart));
  Line line_5 (
    .EnT(T4), .Tail_X(Tail_X), .Head_X(Head_X), .Out(out_14), .Smash(S4), .Clock(Clock), .EnH(H4),
    .Restart(Restart));
  Line line_6 (
    .EnT(T5), .Tail_X(Tail_X), .Head_X(Head_X), .Out(out_15), .Smash(S5), .Clock(Clock), .EnH(H5),
    .Restart(Restart));
  Line line_7 (
    .EnT(T6), .Tail_X(Tail_X), .Head_X(Head_X), .Out(out_16), .Smash(S6), .Clock(Clock), .EnH(H6),
    .Restart(Restart));
  Line line_8 (
    .EnT(T7), .Tail_X(Tail_X), .Head_X(Head_X), .Out(out_17), .Smash(S7), .Clock(Clock), .EnH(H7),
    .Restart(Restart));
  Line line_9 (
    .EnT(T8), .Tail_X(Tail_X), .Head_X(Head_X), .Out(out_18), .Smash(S8), .Clock(Clock), .EnH(H8),
    .Restart(Restart));
  Line line_10 (
    .EnT(T9), .Tail_X(Tail_X), .Head_X(Head_X), .Out(out_19), .Smash(S9), .Clock(Clock), .EnH(H9),
    .Restart(Restart));
  Line line_11 (
    .EnT(T10), .Tail_X(Tail_X), .Head_X(Head_X), .Out(out_20), .Smash(S10), .Clock(Clock), .EnH(H10),
    .Restart(Restart));
  Line line_12 (
    .EnT(T11), .Tail_X(Tail_X), .Head_X(Head_X), .Out(out_21), .Smash(S11), .Clock(Clock), .EnH(H11),
    .Restart(Restart));
  Line line_13 (
    .EnT(T12), .Tail_X(Tail_X), .Head_X(Head_X), .Out(out_22), .Smash(S12), .Clock(Clock), .EnH(H12),
    .Restart(Restart));
  Line line_14 (
    .EnT(T13), .Tail_X(Tail_X), .Head_X(Head_X), .Out(out_23), .Smash(S13), .Clock(Clock), .EnH(H13),
    .Restart(Restart));
  Line line_15 (
    .EnT(T14), .Tail_X(Tail_X), .Head_X(Head_X), .Out(out_24), .Smash(S14), .Clock(Clock), .EnH(H14),
    .Restart(Restart));
  Line line_16 (
    .EnT(T15), .Tail_X(Tail_X), .Head_X(Head_X), .Out(out_25), .Smash(S15), .Clock(Clock), .EnH(H15),
    .Restart(Restart));
  or or_1 (Smash, S0, S1, S2, S3, S4, S5, S6, S7, S8, S9, S10, S11, S12, S13, S14, S15, S16, S17, S18, S19, S20, S21, S22, S23, S24, S25, S26, S27, S28, S29, S30, S31);
  Line line_17 (
    .EnT(T16), .Tail_X(Tail_X), .Head_X(Head_X), .Out(out_26), .Smash(S16), .Clock(Clock), .EnH(H16),
    .Restart(Restart));
  Line line_18 (
    .EnT(T17), .Tail_X(Tail_X), .Head_X(Head_X), .Out(out_27), .Smash(S17), .Clock(Clock), .EnH(H17),
    .Restart(Restart));
  Line line_19 (
    .EnT(T18), .Tail_X(Tail_X), .Head_X(Head_X), .Out(out_28), .Smash(S18), .Clock(Clock), .EnH(H18),
    .Restart(Restart));
  Line line_20 (
    .EnT(T19), .Tail_X(Tail_X), .Head_X(Head_X), .Out(out_29), .Smash(S19), .Clock(Clock), .EnH(H19),
    .Restart(Restart));
  Line line_21 (
    .EnT(T20), .Tail_X(Tail_X), .Head_X(Head_X), .Out(out_30), .Smash(S20), .Clock(Clock), .EnH(H20),
    .Restart(Restart));
  Line line_22 (
    .EnT(T21), .Tail_X(Tail_X), .Head_X(Head_X), .Out(out_31), .Smash(S21), .Clock(Clock), .EnH(H21),
    .Restart(Restart));
  Line line_23 (
    .EnT(T22), .Tail_X(Tail_X), .Head_X(Head_X), .Out(out_32), .Smash(S22), .Clock(Clock), .EnH(H22),
    .Restart(Restart));
  Line line_24 (
    .EnT(T23), .Tail_X(Tail_X), .Head_X(Head_X), .Out(out_33), .Smash(S23), .Clock(Clock), .EnH(H23),
    .Restart(Restart));
  Line line_25 (
    .EnT(T24), .Tail_X(Tail_X), .Head_X(Head_X), .Out(out_34), .Smash(S24), .Clock(Clock), .EnH(H24),
    .Restart(Restart));
  Line line_26 (
    .EnT(T25), .Tail_X(Tail_X), .Head_X(Head_X), .Out(out_35), .Smash(S25), .Clock(Clock), .EnH(H25),
    .Restart(Restart));
  Line line_27 (
    .EnT(T26), .Tail_X(Tail_X), .Head_X(Head_X), .Out(out_36), .Smash(S26), .Clock(Clock), .EnH(H26),
    .Restart(Restart));
  Line line_28 (
    .EnT(T27), .Tail_X(Tail_X), .Head_X(Head_X), .Out(out_37), .Smash(S27), .Clock(Clock), .EnH(H27),
    .Restart(Restart));
  Line line_29 (
    .EnT(T28), .Tail_X(Tail_X), .Head_X(Head_X), .Out(out_38), .Smash(S28), .Clock(Clock), .EnH(H28),
    .Restart(Restart));
  Line line_30 (
    .EnT(T29), .Tail_X(Tail_X), .Head_X(Head_X), .Out(out_39), .Smash(S29), .Clock(Clock), .EnH(H29),
    .Restart(Restart));
  Line line_31 (
    .EnT(T30), .Tail_X(Tail_X), .Head_X(Head_X), .Out(out_40), .Smash(S30), .Clock(Clock), .EnH(H30),
    .Restart(Restart));
  Line line_32 (
    .EnT(T31), .Tail_X(Tail_X), .Head_X(Head_X), .Out(out_41), .Smash(S31), .Clock(Clock), .EnH(H31),
    .Restart(Restart));

  // Other names for the same wires on the sheet: O0[31:0] = _0; O1[31:0] = out_11; O2[31:0] = out_12;
  //   O3[31:0] = out_13; O4[31:0] = out_14; O5[31:0] = out_15; O6[31:0] = out_16; O7[31:0] = out_17;
  //   O8[31:0] = out_18; O9[31:0] = out_19; O10[31:0] = out_20; O11[31:0] = out_21; O12[31:0] = out_22;
  //   O13[31:0] = out_23; O14[31:0] = out_24; O15[31:0] = out_25; O16[31:0] = out_26; O17[31:0] = out_27;
  //   O18[31:0] = out_28; O19[31:0] = out_29; O20[31:0] = out_30; O21[31:0] = out_31; O22[31:0] = out_32;
  //   O23[31:0] = out_33; O24[31:0] = out_34; O25[31:0] = out_35; O26[31:0] = out_36; O27[31:0] = out_37;
  //   O28[31:0] = out_38; O29[31:0] = out_39; O30[31:0] = out_40; O31[31:0] = out_41
endmodule

module Line (
  input  Restart,
  input  Clock,
  input  EnT,
  input  EnH,
  input  [4:0] Tail_X,
  input  [4:0] Head_X,
  output [31:0] Out,
  output Smash
);

  wire H0, H1, H2, H3, H4, H5, H6, H7, H8, H9, H10, H11, H12, H13, H14, H15, H16, H17, H18, H19, H20, H21,
       H22, H23, H24, H25, H26, H27, H28, H29, H30, H31, S0, S1, S2, S3, S4, S5, S6, S7, S8, S9, S10, S11,
       S12, S13, S14, S15, S16, S17, S18, S19, S20, S21, S22, S23, S24, S25, S26, S27, S28, S29, S30, S31,
       T0, T1, T2, T3, T4, T5, T6, T7, T8, T9, T10, T11, T12, T13, T14, T15, T16, T17, T18, T19, T20, T21,
       T22, T23, T24, T25, T26, T27, T28, T29, T30, T31;

  Decoder #(.select(5), .disabled(0)) decoder_1 (
    .out0(T0), .out1(T1), .out2(T2), .out3(T3), .out4(T4), .out5(T5), .out6(T6), .out7(T7), .out8(T8),
    .out9(T9), .out10(T10), .out11(T11), .out12(T12), .out13(T13), .out14(T14), .out15(T15), .out16(T16),
    .out17(T17), .out18(T18), .out19(T19), .out20(T20), .out21(T21), .out22(T22), .out23(T23), .out24(T24),
    .out25(T25), .out26(T26), .out27(T27), .out28(T28), .out29(T29), .out30(T30), .out31(T31), .sel(Tail_X),
    .en(EnT));
  pixel pixel_1 (.Clock(Clock), .Up(H0), .T(T0), .Light(Out[31]), .Smash(S0), .Restart(Restart));
  pixel pixel_2 (.Clock(Clock), .Up(H16), .T(T16), .Light(Out[15]), .Smash(S16), .Restart(Restart));
  Decoder #(.select(5), .disabled(0)) decoder_2 (
    .out0(H0), .out1(H1), .out2(H2), .out3(H3), .out4(H4), .out5(H5), .out6(H6), .out7(H7), .out8(H8),
    .out9(H9), .out10(H10), .out11(H11), .out12(H12), .out13(H13), .out14(H14), .out15(H15), .out16(H16),
    .out17(H17), .out18(H18), .out19(H19), .out20(H20), .out21(H21), .out22(H22), .out23(H23), .out24(H24),
    .out25(H25), .out26(H26), .out27(H27), .out28(H28), .out29(H29), .out30(H30), .out31(H31), .sel(Head_X),
    .en(EnH));
  pixel pixel_3 (.Clock(Clock), .Up(H1), .T(T1), .Light(Out[30]), .Smash(S1), .Restart(Restart));
  pixel pixel_4 (.Clock(Clock), .Up(H2), .T(T2), .Light(Out[29]), .Smash(S2), .Restart(Restart));
  pixel pixel_5 (.Clock(Clock), .Up(H18), .T(T18), .Light(Out[13]), .Smash(S18), .Restart(Restart));
  pixel pixel_6 (.Clock(Clock), .Up(H17), .T(T17), .Light(Out[14]), .Smash(S17), .Restart(Restart));
  pixel pixel_7 (.Clock(Clock), .Up(H3), .T(T3), .Light(Out[28]), .Smash(S3), .Restart(Restart));
  pixel pixel_8 (.Clock(Clock), .Up(H19), .T(T19), .Light(Out[12]), .Smash(S19), .Restart(Restart));
  pixel pixel_9 (.Clock(Clock), .Up(H4), .T(T4), .Light(Out[27]), .Smash(S4), .Restart(Restart));
  pixel pixel_10 (.Clock(Clock), .Up(H5), .T(T5), .Light(Out[26]), .Smash(S5), .Restart(Restart));
  pixel pixel_11 (.Clock(Clock), .Up(H21), .T(T21), .Light(Out[10]), .Smash(S21), .Restart(Restart));
  pixel pixel_12 (.Clock(Clock), .Up(H20), .T(T20), .Light(Out[11]), .Smash(S20), .Restart(Restart));
  pixel pixel_13 (.Clock(Clock), .Up(H6), .T(T6), .Light(Out[25]), .Smash(S6), .Restart(Restart));
  pixel pixel_14 (.Clock(Clock), .Up(H22), .T(T22), .Light(Out[9]), .Smash(S22), .Restart(Restart));
  or or_1 (Smash, S0, S1, S2, S3, S4, S5, S6, S7, S8, S9, S10, S11, S12, S13, S14, S15, S16, S17, S18, S19, S20, S21, S22, S23, S24, S25, S26, S27, S28, S29, S30, S31);
  pixel pixel_15 (.Clock(Clock), .Up(H7), .T(T7), .Light(Out[24]), .Smash(S7), .Restart(Restart));
  pixel pixel_16 (.Clock(Clock), .Up(H8), .T(T8), .Light(Out[23]), .Smash(S8), .Restart(Restart));
  pixel pixel_17 (.Clock(Clock), .Up(H23), .T(T23), .Light(Out[8]), .Smash(S23), .Restart(Restart));
  pixel pixel_18 (.Clock(Clock), .Up(H24), .T(T24), .Light(Out[7]), .Smash(S24), .Restart(Restart));
  pixel pixel_19 (.Clock(Clock), .Up(H9), .T(T9), .Light(Out[22]), .Smash(S9), .Restart(Restart));
  pixel pixel_20 (.Clock(Clock), .Up(H10), .T(T10), .Light(Out[21]), .Smash(S10), .Restart(Restart));
  pixel pixel_21 (.Clock(Clock), .Up(H25), .T(T25), .Light(Out[6]), .Smash(S25), .Restart(Restart));
  pixel pixel_22 (.Clock(Clock), .Up(H26), .T(T26), .Light(Out[5]), .Smash(S26), .Restart(Restart));
  pixel pixel_23 (.Clock(Clock), .Up(H11), .T(T11), .Light(Out[20]), .Smash(S11), .Restart(Restart));
  pixel pixel_24 (.Clock(Clock), .Up(H27), .T(T27), .Light(Out[4]), .Smash(S27), .Restart(Restart));
  pixel pixel_25 (.Clock(Clock), .Up(H12), .T(T12), .Light(Out[19]), .Smash(S12), .Restart(Restart));
  pixel pixel_26 (.Clock(Clock), .Up(H13), .T(T13), .Light(Out[18]), .Smash(S13), .Restart(Restart));
  pixel pixel_27 (.Clock(Clock), .Up(H28), .T(T28), .Light(Out[3]), .Smash(S28), .Restart(Restart));
  pixel pixel_28 (.Clock(Clock), .Up(H29), .T(T29), .Light(Out[2]), .Smash(S29), .Restart(Restart));
  pixel pixel_29 (.Clock(Clock), .Up(H14), .T(T14), .Light(Out[17]), .Smash(S14), .Restart(Restart));
  pixel pixel_30 (.Clock(Clock), .Up(H30), .T(T30), .Light(Out[1]), .Smash(S30), .Restart(Restart));
  pixel pixel_31 (.Clock(Clock), .Up(H15), .T(T15), .Light(Out[16]), .Smash(S15), .Restart(Restart));
  pixel pixel_32 (.Clock(Clock), .Up(H31), .T(T31), .Light(Out[0]), .Smash(S31), .Restart(Restart));

  // Other names for the same wires on the sheet: L31 = Out[0]; L30 = Out[1]; L29 = Out[2]; L28 = Out[3]; L27 = Out[4];
  //   L26 = Out[5]; L25 = Out[6]; L24 = Out[7]; L23 = Out[8]; L22 = Out[9]; L21 = Out[10]; L20 = Out[11];
  //   L19 = Out[12]; L18 = Out[13]; L17 = Out[14]; L16 = Out[15]; L15 = Out[16]; L14 = Out[17]; L13 = Out[18];
  //   L12 = Out[19]; L11 = Out[20]; L10 = Out[21]; L9 = Out[22]; L8 = Out[23]; L7 = Out[24]; L6 = Out[25];
  //   L5 = Out[26]; L4 = Out[27]; L3 = Out[28]; L2 = Out[29]; L1 = Out[30]; L0 = Out[31]
endmodule

module pixel (
  input  Restart,
  input  Clock,
  input  Up,
  input  T,
  output Light,
  output Smash
);

  wire and_1_out, and_2_out, or_1_out;

  and and_1 (and_1_out, ~Light, Up);  // AND_Gate
  D_Flip_Flop d_ff_1 (.clk(Clock), .D(and_1_out), .Q(Light), .en(and_1_out), .reset(or_1_out));  // open: Qn, preset
  or or_1 (or_1_out, and_2_out, Restart);
  and and_2 (and_2_out, ~Up, T);  // AND_Gate
  and and_3 (Smash, Light, ~Clock, Up);  // AND_Gate

  // Notes on the sheet:
  //   Датчик коллизии
endmodule

module Keyboard (
  input  Clock,
  input  Turn,
  input  Restart,
  input  [6:0] In,
  output Pause,
  output [1:0] Where,
  output W,
  output A,
  output S,
  output D
);

  wire and_3_out, bitshrink_1_a, bitshrink_1_d, bitshrink_1_pause, bitshrink_1_s, bitshrink_1_w,
       pull_resistor_1_node;
  wire [1:0] bitshrink_1_where;

  and and_1 (D, ~Clock, bitshrink_1_d);  // AND_Gate
  and and_2 (S, ~Clock, bitshrink_1_s);  // AND_Gate
  bitShrink bitshrink_1 (
    .In(In), .W(bitshrink_1_w), .A(bitshrink_1_a), .S(bitshrink_1_s), .D(bitshrink_1_d),
    .Where(bitshrink_1_where), .Pause(bitshrink_1_pause));
  and and_3 (and_3_out, ~Clock, bitshrink_1_pause);  // AND_Gate
  D_Flip_Flop d_ff_1 (.clk(and_3_out), .D(pull_resistor_1_node), .Q(Pause), .reset(Restart));  // open: Qn, preset, en
  Pull_Resistor #(.pull(1)) pull_resistor_1 (.node(pull_resistor_1_node));
  assign pull_resistor_1_node = Pause ? ~bitshrink_1_pause : 1'bz;  // Controlled_Inverter controlled_inverter_1
  and and_4 (W, ~Clock, bitshrink_1_w);  // AND_Gate
  and and_5 (A, ~Clock, bitshrink_1_a);  // AND_Gate
  Register #(.width(2)) register_1 (.D(bitshrink_1_where), .Q(Where), .clk(Turn));  // open: en, clr
endmodule

module bitShrink (
  input  [6:0] In,
  output W,
  output A,
  output [1:0] Where,
  output S,
  output D,
  output Pause
);

  wire [6:0] xnor_1_out, xnor_2_out, xnor_3_out, xnor_4_out, xnor_5_out;

  // Probe on 7'b1110111
  // Probe on 7'b1100001
  // Probe on 7'b1110011
  // Probe on 7'b1100100
  // Probe on 7'b0100000
  assign xnor_1_out = ~(In ^ 7'b1110111);  // XNOR_Gate xnor_1, 7 bits wide
  assign xnor_2_out = ~(In ^ 7'b1100001);  // XNOR_Gate xnor_2, 7 bits wide
  assign xnor_3_out = ~(In ^ 7'b1110011);  // XNOR_Gate xnor_3, 7 bits wide
  assign xnor_4_out = ~(In ^ 7'b1100100);  // XNOR_Gate xnor_4, 7 bits wide
  assign xnor_5_out = ~(In ^ 7'b0100000);  // XNOR_Gate xnor_5, 7 bits wide
  and and_1 (W, xnor_1_out[0], xnor_1_out[1], xnor_1_out[2], xnor_1_out[3], xnor_1_out[4], xnor_1_out[5], xnor_1_out[6]);
  and and_2 (A, xnor_2_out[0], xnor_2_out[1], xnor_2_out[2], xnor_2_out[3], xnor_2_out[4], xnor_2_out[5], xnor_2_out[6]);
  and and_3 (S, xnor_3_out[0], xnor_3_out[1], xnor_3_out[2], xnor_3_out[3], xnor_3_out[4], xnor_3_out[5], xnor_3_out[6]);
  and and_4 (D, xnor_4_out[0], xnor_4_out[1], xnor_4_out[2], xnor_4_out[3], xnor_4_out[4], xnor_4_out[5], xnor_4_out[6]);
  and and_5 (Pause, xnor_5_out[0], xnor_5_out[1], xnor_5_out[2], xnor_5_out[3], xnor_5_out[4], xnor_5_out[5], xnor_5_out[6]);
  assign Where = W ? 2'b00 : 2'bz;  // Controlled_Buffer controlled_buffer_1
  assign Where = A ? 2'b01 : 2'bz;  // Controlled_Buffer controlled_buffer_2
  assign Where = S ? 2'b10 : 2'bz;  // Controlled_Buffer controlled_buffer_3
  assign Where = D ? 2'b11 : 2'bz;  // Controlled_Buffer controlled_buffer_4
  Pull_Resistor pull_resistor_1 (.node(Where));
endmodule

module Apples (
  input  [31:0] L1,
  input  [31:0] L1_2
);

  wire or_1_out;
  wire [4:0] random_1_out, random_2_out;
  wire [31:0] and_1_out, multiplexer_1_out, shifter_1_out;

  Random #(.width(5)) random_1 (.clk(or_1_out), .out(random_1_out));  // open: next, clr
  Random #(.width(5)) random_2 (.clk(or_1_out), .out(random_2_out));  // open: next, clr
  Multiplexer #(.select(5), .width(32)) multiplexer_1 (
    .out(multiplexer_1_out), .sel(random_1_out));  // open: in0, in1, in2, in3, in4, in5, in6, in7, in8, in9, in10, in11, in12, in13, in14, in15, in16, in17, in18, in19, in20, in21, in22, in23, in24, in25, in26, in27, in28, in29, in30, in31, en
  Shifter #(.width(32)) shifter_1 (.in(32'h1), .\dist (random_2_out), .out(shifter_1_out));
  assign and_1_out = shifter_1_out & multiplexer_1_out;  // AND_Gate and_1, 32 bits wide
  or or_1 (or_1_out, and_1_out[0], and_1_out[1], and_1_out[2], and_1_out[3], and_1_out[4], and_1_out[5], and_1_out[6], and_1_out[7], and_1_out[8], and_1_out[9], and_1_out[10], and_1_out[11], and_1_out[12], and_1_out[13], and_1_out[14], and_1_out[15], and_1_out[16], and_1_out[17], and_1_out[18], and_1_out[19], and_1_out[20], and_1_out[21], and_1_out[22], and_1_out[23], and_1_out[24], and_1_out[25], and_1_out[26], and_1_out[27], and_1_out[28], and_1_out[29], and_1_out[30], and_1_out[31]);
endmodule
