// Logisim project new.circ as structural Verilog
module Proc (
);

  wire cdm_8_mark5_1_p1, cdm_8_mark5_1_p2, cdm_8_mark5_1_p4, cdm_8_mark5_1_p5, cdm_8_mark5_1_p6,
       cdm_8_mark5_1_p7, cdm_8_mark5_1_p8, CI, code, data, I_Osel, in_out_prime, mem, nand_1_out, not_1_out,
       not_2_out, RAM;
  wire [3:0] I_Oadr;
  wire [7:0] cdm_8_mark5_1_p12, cdm_8_mark5_1_p13, I_Odat;
  wire [7:4] cdm_8_mark5_1_p11;

  // Probe on cdm_8_mark5_1_p5
  // Probe on cdm_8_mark5_1_p4
  // Probe on cdm_8_mark5_1_p2
  // Probe on cdm_8_mark5_1_p1
  // Probe on cdm_8_mark5_1_p7
  // Probe on cdm_8_mark5_1_p6
  Clock clock_1 (.out(CI));
  and and_1 (I_Osel, not_2_out, CI, data);
  Decoder decoder_1 (.out0(code), .out1(data), .sel(cdm_8_mark5_1_p8), .en(mem));
  // CdM_8_mark5 cdm_8_mark5_1: pin names not known; wires that end beside it: cdm_8_mark5_1_p1, cdm_8_mark5_1_p2, CI, cdm_8_mark5_1_p4, cdm_8_mark5_1_p5, cdm_8_mark5_1_p6, cdm_8_mark5_1_p7, cdm_8_mark5_1_p8, mem, in_out_prime, {cdm_8_mark5_1_p11, I_Oadr}, cdm_8_mark5_1_p12, cdm_8_mark5_1_p13
  not not_1 (not_1_out, in_out_prime);
  assign cdm_8_mark5_1_p13 = in_out_prime ? I_Odat : 8'bz;  // Controlled_Buffer controlled_buffer_1
  not not_2 (not_2_out, nand_1_out);
  and and_2 (RAM, nand_1_out, data);
  assign I_Odat = not_1_out ? cdm_8_mark5_1_p12 : 8'bz;  // Controlled_Buffer controlled_buffer_2
  nand nand_1 (nand_1_out, cdm_8_mark5_1_p11[4], cdm_8_mark5_1_p11[5], cdm_8_mark5_1_p11[6], cdm_8_mark5_1_p11[7]);
  ROM rom_1 (.addr({cdm_8_mark5_1_p11, I_Oadr}), .data(I_Odat), .sel(code));
  RAM ram_1 (.addr({cdm_8_mark5_1_p11, I_Oadr}), .data(I_Odat), .sel(RAM), .clk(CI), .ld(in_out_prime));  // open: clr

  // Other names for the same wires on the sheet: rd_wr_prime = in_out_prime
endmodule

module Main (
  input  Start,
  input  Pause,
  input  in_3,
  input  in_4
);

  wire and_1_out, and_2_out, and_3_out, and_4_out, and_5_out, and_6_out, Clock, clock_1_out, clock_2_out,
       clock_3_out, decoder_1_out0, decoder_1_out1, decoder_1_out2, decoder_1_out3, Down, Left, not_1_out,
       not_2_out, or_1_out, or_2_out, or_3_out, or_4_out, or_5_out, or_6_out, or_7_out, or_8_out, or_9_out,
       or_10_out, or_11_out, or_12_out, Right, transistor_2_out, transistor_3_out, transto2bit_1_en, Up;
  wire [1:0] transto2bit_1_out;
  wire [4:0] Head_X, Head_Y, Tail_X;
  wire [6:0] keyboard_1_data;
  wire [31:0] tomatrix_1__0, tomatrix_1_out_13, tomatrix_1_out_14, tomatrix_1_out_15, tomatrix_1_out_16,
       tomatrix_1_out_17, tomatrix_1_out_18, tomatrix_1_out_19, tomatrix_1_out_20, tomatrix_1_out_21,
       tomatrix_1_out_22, tomatrix_1_out_23, tomatrix_1_out_24, tomatrix_1_out_25, tomatrix_1_out_26,
       tomatrix_1_out_27, tomatrix_1_out_28, tomatrix_1_out_29, tomatrix_1_out_30, tomatrix_1_out_31,
       tomatrix_1_out_32, tomatrix_1_out_33, tomatrix_1_out_34, tomatrix_1_out_35, tomatrix_1_out_36,
       tomatrix_1_out_37, tomatrix_1_out_38, tomatrix_1_out_39, tomatrix_1_out_40, tomatrix_1_out_41,
       tomatrix_1_out_42, tomatrix_1_out_43;

  Clock clock_1 (.out(clock_1_out));
  Keyboard keyboard_1 (.clk(clock_2_out), .data(keyboard_1_data));  // open: re, clr, avail
  Clock clock_2 (.out(clock_2_out));
  or or_1 (or_1_out, Up, Down, Start, Left, Right);
  Transistor #(.\type ("n"), .gate("br")) transistor_1 (.in(clock_1_out), .out(Clock), .gate(and_1_out));
  Pull_Resistor pull_resistor_1 (.node(Clock));
  and and_1 (and_1_out, or_1_out, ~Pause);  // AND_Gate
  Keyboard keyboard_2 ();  // open: clk, re, clr, avail, data
  and and_2 (and_2_out, Clock, transto2bit_1_en);
  transTo2bit transto2bit_1 (.Out(transto2bit_1_out), .In(keyboard_1_data), .En(transto2bit_1_en));
  or or_2 (or_2_out, Down, Start);
  not not_1 (not_1_out, Start);
  or or_3 (or_3_out, Start, transistor_2_out);
  or or_4 (or_4_out, Up, Down);
  or or_5 (or_5_out, Start, and_4_out);
  Decoder #(.select(2), .disabled(0)) decoder_1 (
    .out0(decoder_1_out0), .out1(decoder_1_out1), .out2(decoder_1_out2), .out3(decoder_1_out3),
    .sel(transto2bit_1_out), .en(and_2_out));
  Counter #(.width(5), .max('h1f)) counter_1 (
    .load(or_2_out), .D(5'b10000), .count(not_1_out), .Q(Head_Y), .clk(or_3_out));  // open: carry, clr
  Transistor #(.\type ("n")) transistor_2 (.in(Clock), .out(transistor_2_out), .gate(or_4_out));
  Pull_Resistor pull_resistor_2 (.node(transistor_2_out));
  D_Flip_Flop d_ff_1 (.Q(Up), .preset(or_5_out), .reset(or_6_out));  // open: clk, D, Qn, en
  or or_6 (or_6_out, decoder_1_out3, decoder_1_out1);
  and and_3 (and_3_out, ~Up, decoder_1_out2);  // AND_Gate
  and and_4 (and_4_out, ~Down, decoder_1_out0);  // AND_Gate
  D_Flip_Flop d_ff_2 (.Q(Down), .preset(and_3_out), .reset(or_7_out));  // open: clk, D, Qn, en
  or or_7 (or_7_out, decoder_1_out3, decoder_1_out1);
  and and_5 (and_5_out, ~Right, decoder_1_out1);  // AND_Gate
  or or_8 (or_8_out, Left, Start);
  Counter #(.width(5), .max('h1f)) counter_2 (
    .load(or_8_out), .D(5'b10000), .count(not_2_out), .Q(Head_X), .clk(or_9_out));  // open: carry, clr
  not not_2 (not_2_out, Start);
  or or_9 (or_9_out, Start, transistor_3_out);
  Transistor #(.\type ("n")) transistor_3 (.in(Clock), .out(transistor_3_out), .gate(or_10_out));
  or or_10 (or_10_out, Left, Right);
  D_Flip_Flop d_ff_3 (.Q(Left), .preset(and_5_out), .reset(or_11_out));  // open: clk, D, Qn, en
  and and_6 (and_6_out, ~Left, decoder_1_out3);  // AND_Gate
  or or_11 (or_11_out, decoder_1_out2, decoder_1_out0);
  Pull_Resistor pull_resistor_3 (.node(transistor_3_out));
  D_Flip_Flop d_ff_4 (.Q(Right), .preset(and_6_out), .reset(or_12_out));  // open: clk, D, Qn, en
  or or_12 (or_12_out, decoder_1_out2, decoder_1_out0);
  toMatrix tomatrix_1 (
    .Head_X(Head_X), .Tail_X(Tail_X), .Head_Y(Head_Y), .Clock(clock_3_out), ._0(tomatrix_1__0),
    .out_28(tomatrix_1_out_28), .out_13(tomatrix_1_out_13), .out_29(tomatrix_1_out_29),
    .out_14(tomatrix_1_out_14), .out_30(tomatrix_1_out_30), .out_15(tomatrix_1_out_15),
    .out_31(tomatrix_1_out_31), .out_16(tomatrix_1_out_16), .out_32(tomatrix_1_out_32),
    .out_17(tomatrix_1_out_17), .out_33(tomatrix_1_out_33), .out_18(tomatrix_1_out_18),
    .out_34(tomatrix_1_out_34), .out_19(tomatrix_1_out_19), .out_35(tomatrix_1_out_35),
    .out_20(tomatrix_1_out_20), .out_36(tomatrix_1_out_36), .out_21(tomatrix_1_out_21),
    .out_37(tomatrix_1_out_37), .out_22(tomatrix_1_out_22), .out_38(tomatrix_1_out_38),
    .out_23(tomatrix_1_out_23), .out_39(tomatrix_1_out_39), .out_24(tomatrix_1_out_24),
    .out_40(tomatrix_1_out_40), .out_25(tomatrix_1_out_25), .out_41(tomatrix_1_out_41),
    .out_26(tomatrix_1_out_26), .out_42(tomatrix_1_out_42), .out_27(tomatrix_1_out_27),
    .out_43(tomatrix_1_out_43), .EnT(in_4), .EnH(in_3));  // open: Apple_X, EnA, Tail_Y, Apple_Y, Smash
  Clock clock_3 (.out(clock_3_out));
  DotMatrix #(.inputtype("row"), .matrixcols(32), .matrixrows(32)) dotmatrix_1 (
    .row0(tomatrix_1_out_43), .row1(tomatrix_1_out_42), .row2(tomatrix_1_out_41), .row3(tomatrix_1_out_40),
    .row4(tomatrix_1_out_39), .row5(tomatrix_1_out_38), .row6(tomatrix_1_out_37), .row7(tomatrix_1_out_36),
    .row8(tomatrix_1_out_35), .row9(tomatrix_1_out_34), .row10(tomatrix_1_out_33), .row11(tomatrix_1_out_32),
    .row12(tomatrix_1_out_31), .row13(tomatrix_1_out_30), .row14(tomatrix_1_out_29),
    .row15(tomatrix_1_out_28), .row16(tomatrix_1_out_27), .row17(tomatrix_1_out_26),
    .row18(tomatrix_1_out_25), .row19(tomatrix_1_out_24), .row20(tomatrix_1_out_23),
    .row21(tomatrix_1_out_22), .row22(tomatrix_1_out_21), .row23(tomatrix_1_out_20),
    .row24(tomatrix_1_out_19), .row25(tomatrix_1_out_18), .row26(tomatrix_1_out_17),
    .row27(tomatrix_1_out_16), .row28(tomatrix_1_out_15), .row29(tomatrix_1_out_14),
    .row30(tomatrix_1_out_13), .row31(tomatrix_1__0));
endmodule

module Head (
  input  Up,
  input  Down,
  input  Left,
  input  Right,
  input  Start,
  input  Clock,
  output [4:0] Head_Y,
  output [4:0] Head_X
);

  wire not_1_out, not_2_out, or_1_out, or_2_out, or_3_out, or_4_out, or_5_out, or_6_out, transistor_1_out,
       transistor_2_out;

  or or_1 (or_1_out, Down, Start);
  not not_1 (not_1_out, Start);
  or or_2 (or_2_out, Up, Down);
  Counter #(.width(5), .max('h1f)) counter_1 (
    .load(or_1_out), .D(5'b10000), .count(not_1_out), .Q(Head_Y), .clk(or_3_out));  // open: carry, clr
  or or_3 (or_3_out, Start, transistor_1_out);
  Transistor #(.\type ("n")) transistor_1 (.in(Clock), .out(transistor_1_out), .gate(or_2_out));
  Pull_Resistor pull_resistor_1 (.node(transistor_1_out));
  or or_4 (or_4_out, Left, Start);
  not not_2 (not_2_out, Start);
  or or_5 (or_5_out, Start, transistor_2_out);
  or or_6 (or_6_out, Left, Right);
  Counter #(.width(5), .max('h1f)) counter_2 (
    .load(or_4_out), .D(5'b10000), .count(not_2_out), .Q(Head_X), .clk(or_5_out));  // open: carry, clr
  Transistor #(.\type ("n")) transistor_2 (.in(Clock), .out(transistor_2_out), .gate(or_6_out));
  Pull_Resistor pull_resistor_2 (.node(transistor_2_out));
endmodule

module toMatrix (
  input  [4:0] Head_X,
  input  [4:0] Tail_X,
  input  [4:0] Apple_X,
  input  EnH,
  input  EnT,
  input  EnA,
  input  [4:0] Head_Y,
  input  [4:0] Tail_Y,
  input  [4:0] Apple_Y,
  input  Clock,
  output Smash,
  output [31:0] _0,
  output [31:0] out_13,
  output [31:0] out_14,
  output [31:0] out_15,
  output [31:0] out_16,
  output [31:0] out_17,
  output [31:0] out_18,
  output [31:0] out_19,
  output [31:0] out_20,
  output [31:0] out_21,
  output [31:0] out_22,
  output [31:0] out_23,
  output [31:0] out_24,
  output [31:0] out_25,
  output [31:0] out_26,
  output [31:0] out_27,
  output [31:0] out_28,
  output [31:0] out_29,
  output [31:0] out_30,
  output [31:0] out_31,
  output [31:0] out_32,
  output [31:0] out_33,
  output [31:0] out_34,
  output [31:0] out_35,
  output [31:0] out_36,
  output [31:0] out_37,
  output [31:0] out_38,
  output [31:0] out_39,
  output [31:0] out_40,
  output [31:0] out_41,
  output [31:0] out_42,
  output [31:0] out_43
);

  wire A0, A1, A2, A3, A4, A5, A6, A7, A8, A9, A10, A11, A12, A13, A14, A15, A16, A17, A18, A19, A20, A21,
       A22, A23, A24, A25, A26, A27, A28, A29, A30, A31, H0, H1, H2, H3, H4, H5, H6, H7, H8, H9, H10, H11,
       H12, H13, H14, H15, H16, H17, H18, H19, H20, H21, H22, H23, H24, H25, H26, H27, H28, H29, H30, H31,
       line_1_smash, line_2_smash, line_3_smash, line_4_smash, line_5_smash, line_6_smash, line_7_smash,
       line_8_smash, line_9_smash, line_10_smash, line_11_smash, line_12_smash, line_13_smash, line_14_smash,
       line_15_smash, line_16_smash, line_17_smash, line_18_smash, line_19_smash, line_20_smash,
       line_21_smash, line_22_smash, line_23_smash, line_24_smash, line_25_smash, line_26_smash,
       line_27_smash, line_28_smash, line_29_smash, line_30_smash, line_31_smash, line_32_smash, or_1_out,
       or_2_out, or_4_out, or_5_out, T0, T1, T2, T3, T4, T5, T6, T7, T8, T9, T10, T11, T12, T13, T14, T15,
       T16, T17, T18, T19, T20, T21, T22, T23, T24, T25, T26, T27, T28, T29, T30, T31;

  Decoder #(.select(5), .disabled(0)) decoder_1 (
    .out0(H0), .out1(H1), .out2(H2), .out3(H3), .out4(H4), .out5(H5), .out6(H6), .out7(H7), .out8(H8),
    .out9(H9), .out10(H10), .out11(H11), .out12(H12), .out13(H13), .out14(H14), .out15(H15), .out16(H16),
    .out17(H17), .out18(H18), .out19(H19), .out20(H20), .out21(H21), .out22(H22), .out23(H23), .out24(H24),
    .out25(H25), .out26(H26), .out27(H27), .out28(H28), .out29(H29), .out30(H30), .out31(H31), .sel(Head_Y),
    .en(EnH));
  Decoder #(.select(5), .disabled(0)) decoder_2 (
    .out0(T0), .out1(T1), .out2(T2), .out3(T3), .out4(T4), .out5(T5), .out6(T6), .out7(T7), .out8(T8),
    .out9(T9), .out10(T10), .out11(T11), .out12(T12), .out13(T13), .out14(T14), .out15(T15), .out16(T16),
    .out17(T17), .out18(T18), .out19(T19), .out20(T20), .out21(T21), .out22(T22), .out23(T23), .out24(T24),
    .out25(T25), .out26(T26), .out27(T27), .out28(T28), .out29(T29), .out30(T30), .out31(T31), .sel(Tail_Y),
    .en(EnT));
  Decoder #(.select(5), .disabled(0)) decoder_3 (
    .out0(A0), .out1(A1), .out2(A2), .out3(A3), .out4(A4), .out5(A5), .out6(A6), .out7(A7), .out8(A8),
    .out9(A9), .out10(A10), .out11(A11), .out12(A12), .out13(A13), .out14(A14), .out15(A15), .out16(A16),
    .out17(A17), .out18(A18), .out19(A19), .out20(A20), .out21(A21), .out22(A22), .out23(A23), .out24(A24),
    .out25(A25), .out26(A26), .out27(A27), .out28(A28), .out29(A29), .out30(A30), .out31(A31), .sel(Apple_Y),
    .en(EnA));
  Line line_1 (
    .EnA(A0), .EnT(T0), .Apple_X(Apple_X), .Tail_X(Tail_X), .Head_X(Head_X), .Out(_0), .Smash(line_1_smash),
    .Clock(Clock), .EnH(H0));
  Line line_2 (
    .EnA(A1), .EnT(T1), .Apple_X(Apple_X), .Tail_X(Tail_X), .Head_X(Head_X), .Out(out_13),
    .Smash(line_2_smash), .Clock(Clock), .EnH(H1));
  Line line_3 (
    .EnA(A2), .EnT(T2), .Apple_X(Apple_X), .Tail_X(Tail_X), .Head_X(Head_X), .Out(out_14),
    .Smash(line_3_smash), .Clock(Clock), .EnH(H2));
  Line line_4 (
    .EnA(A3), .EnT(T3), .Apple_X(Apple_X), .Tail_X(Tail_X), .Head_X(Head_X), .Out(out_15),
    .Smash(line_4_smash), .Clock(Clock), .EnH(H3));
  Line line_5 (
    .EnA(A4), .EnT(T4), .Apple_X(Apple_X), .Tail_X(Tail_X), .Head_X(Head_X), .Out(out_16),
    .Smash(line_5_smash), .Clock(Clock), .EnH(H4));
  Line line_6 (
    .EnA(A5), .EnT(T5), .Apple_X(Apple_X), .Tail_X(Tail_X), .Head_X(Head_X), .Out(out_17),
    .Smash(line_6_smash), .Clock(Clock), .EnH(H5));
  Line line_7 (
    .EnA(A6), .EnT(T6), .Apple_X(Apple_X), .Tail_X(Tail_X), .Head_X(Head_X), .Out(out_18),
    .Smash(line_7_smash), .Clock(Clock), .EnH(H6));
  Line line_8 (
    .EnA(A7), .EnT(T7), .Apple_X(Apple_X), .Tail_X(Tail_X), .Head_X(Head_X), .Out(out_19),
    .Smash(line_8_smash), .Clock(Clock), .EnH(H7));
  or or_1 (or_1_out, line_8_smash, line_7_smash, line_6_smash, line_5_smash, line_4_smash, line_3_smash, line_2_smash, line_1_smash);
  Line line_9 (
    .EnA(A8), .EnT(T8), .Apple_X(Apple_X), .Tail_X(Tail_X), .Head_X(Head_X), .Out(out_20),
    .Smash(line_9_smash), .Clock(Clock), .EnH(H8));
  Line line_10 (
    .EnA(A9), .EnT(T9), .Apple_X(Apple_X), .Tail_X(Tail_X), .Head_X(Head_X), .Out(out_21),
    .Smash(line_10_smash), .Clock(Clock), .EnH(H9));
  Line line_11 (
    .EnA(A10), .EnT(T10), .Apple_X(Apple_X), .Tail_X(Tail_X), .Head_X(Head_X), .Out(out_22),
    .Smash(line_11_smash), .Clock(Clock), .EnH(H10));
  Line line_12 (
    .EnA(A11), .EnT(T11), .Apple_X(Apple_X), .Tail_X(Tail_X), .Head_X(Head_X), .Out(out_23),
    .Smash(line_12_smash), .Clock(Clock), .EnH(H11));
  Line line_13 (
    .EnA(A12), .EnT(T12), .Apple_X(Apple_X), .Tail_X(Tail_X), .Head_X(Head_X), .Out(out_24),
    .Smash(line_13_smash), .Clock(Clock), .EnH(H12));
  Line line_14 (
    .EnA(A13), .EnT(T13), .Apple_X(Apple_X), .Tail_X(Tail_X), .Head_X(Head_X), .Out(out_25),
    .Smash(line_14_smash), .Clock(Clock), .EnH(H13));
  Line line_15 (
    .EnA(A14), .EnT(T14), .Apple_X(Apple_X), .Tail_X(Tail_X), .Head_X(Head_X), .Out(out_26),
    .Smash(line_15_smash), .Clock(Clock), .EnH(H14));
  Line line_16 (
    .EnA(A15), .EnT(T15), .Apple_X(Apple_X), .Tail_X(Tail_X), .Head_X(Head_X), .Out(out_27),
    .Smash(line_16_smash), .Clock(Clock), .EnH(H15));
  or or_2 (or_2_out, line_16_smash, line_15_smash, line_14_smash, line_13_smash, line_12_smash, line_11_smash, line_10_smash, line_9_smash);
  or or_3 (Smash, or_1_out, or_2_out, or_4_out, or_5_out);
  Line line_17 (
    .EnA(A16), .EnT(T16), .Apple_X(Apple_X), .Tail_X(Tail_X), .Head_X(Head_X), .Out(out_28),
    .Smash(line_17_smash), .Clock(Clock), .EnH(H16));
  Line line_18 (
    .EnA(A17), .EnT(T17), .Apple_X(Apple_X), .Tail_X(Tail_X), .Head_X(Head_X), .Out(out_29),
    .Smash(line_18_smash), .Clock(Clock), .EnH(H17));
  Line line_19 (
    .EnA(A18), .EnT(T18), .Apple_X(Apple_X), .Tail_X(Tail_X), .Head_X(Head_X), .Out(out_30),
    .Smash(line_19_smash), .Clock(Clock), .EnH(H18));
  Line line_20 (
    .EnA(A19), .EnT(T19), .Apple_X(Apple_X), .Tail_X(Tail_X), .Head_X(Head_X), .Out(out_31),
    .Smash(line_20_smash), .Clock(Clock), .EnH(H19));
  Line line_21 (
    .EnA(A20), .EnT(T20), .Apple_X(Apple_X), .Tail_X(Tail_X), .Head_X(Head_X), .Out(out_32),
    .Smash(line_21_smash), .Clock(Clock), .EnH(H20));
  Line line_22 (
    .EnA(A21), .EnT(T21), .Apple_X(Apple_X), .Tail_X(Tail_X), .Head_X(Head_X), .Out(out_33),
    .Smash(line_22_smash), .Clock(Clock), .EnH(H21));
  Line line_23 (
    .EnA(A22), .EnT(T22), .Apple_X(Apple_X), .Tail_X(Tail_X), .Head_X(Head_X), .Out(out_34),
    .Smash(line_23_smash), .Clock(Clock), .EnH(H22));
  Line line_24 (
    .EnA(A23), .EnT(T23), .Apple_X(Apple_X), .Tail_X(Tail_X), .Head_X(Head_X), .Out(out_35),
    .Smash(line_24_smash), .Clock(Clock), .EnH(H23));
  or or_4 (or_4_out, line_24_smash, line_23_smash, line_22_smash, line_21_smash, line_20_smash, line_19_smash, line_18_smash, line_17_smash);
  Line line_25 (
    .EnA(A24), .EnT(T24), .Apple_X(Apple_X), .Tail_X(Tail_X), .Head_X(Head_X), .Out(out_36),
    .Smash(line_25_smash), .Clock(Clock), .EnH(H24));
  Line line_26 (
    .EnA(A25), .EnT(T25), .Apple_X(Apple_X), .Tail_X(Tail_X), .Head_X(Head_X), .Out(out_37),
    .Smash(line_26_smash), .Clock(Clock), .EnH(H25));
  Line line_27 (
    .EnA(A26), .EnT(T26), .Apple_X(Apple_X), .Tail_X(Tail_X), .Head_X(Head_X), .Out(out_38),
    .Smash(line_27_smash), .Clock(Clock), .EnH(H26));
  Line line_28 (
    .EnA(A27), .EnT(T27), .Apple_X(Apple_X), .Tail_X(Tail_X), .Head_X(Head_X), .Out(out_39),
    .Smash(line_28_smash), .Clock(Clock), .EnH(H27));
  Line line_29 (
    .EnA(A28), .EnT(T28), .Apple_X(Apple_X), .Tail_X(Tail_X), .Head_X(Head_X), .Out(out_40),
    .Smash(line_29_smash), .Clock(Clock), .EnH(H28));
  Line line_30 (
    .EnA(A29), .EnT(T29), .Apple_X(Apple_X), .Tail_X(Tail_X), .Head_X(Head_X), .Out(out_41),
    .Smash(line_30_smash), .Clock(Clock), .EnH(H29));
  Line line_31 (
    .EnA(A30), .EnT(T30), .Apple_X(Apple_X), .Tail_X(Tail_X), .Head_X(Head_X), .Out(out_42),
    .Smash(line_31_smash), .Clock(Clock), .EnH(H30));
  Line line_32 (
    .EnA(A31), .EnT(T31), .Apple_X(Apple_X), .Tail_X(Tail_X), .Head_X(Head_X), .Out(out_43),
    .Smash(line_32_smash), .Clock(Clock), .EnH(H31));
  or or_5 (or_5_out, line_32_smash, line_31_smash, line_30_smash, line_29_smash, line_28_smash, line_27_smash, line_26_smash, line_25_smash);

  // Other names for the same wires on the sheet: O0[31:0] = _0; O1[31:0] = out_13; O2[31:0] = out_14;
  //   O3[31:0] = out_15; O4[31:0] = out_16; O5[31:0] = out_17; O6[31:0] = out_18; O7[31:0] = out_19;
  //   O8[31:0] = out_20; O9[31:0] = out_21; O10[31:0] = out_22; O11[31:0] = out_23; O12[31:0] = out_24;
  //   O13[31:0] = out_25; O14[31:0] = out_26; O15[31:0] = out_27; O16[31:0] = out_28; O17[31:0] = out_29;
  //   O18[31:0] = out_30; O19[31:0] = out_31; O20[31:0] = out_32; O21[31:0] = out_33; O22[31:0] = out_34;
  //   O23[31:0] = out_35; O24[31:0] = out_36; O25[31:0] = out_37; O26[31:0] = out_38; O27[31:0] = out_39;
  //   O28[31:0] = out_40; O29[31:0] = out_41; O30[31:0] = out_42; O31[31:0] = out_43
endmodule

module Line (
  input  EnA,
  input  EnT,
  input  EnH,
  input  [4:0] Apple_X,
  input  [4:0] Tail_X,
  input  [4:0] Head_X,
  input  Clock,
  output [31:0] Out,
  output Smash
);

  wire A0, A1, A2, A3, A4, A5, A6, A7, A8, A9, A10, A11, A12, A13, A14, A15, A16, A17, A18, A19, A20, A21,
       A22, A23, A24, A25, A26, A27, A28, A29, A30, A31, H0, H1, H2, H3, H4, H5, H6, H7, H8, H9, H10, H11,
       H12, H13, H14, H15, H16, H17, H18, H19, H20, H21, H22, H23, H24, H25, H26, H27, H28, H29, H30, H31,
       S0, S1, S2, S3, S4, S5, S6, S7, S8, S9, S10, S11, S12, S13, S14, S15, S16, S17, S18, S19, S20, S21,
       S22, S23, S24, S25, S26, S27, S28, S29, S30, S31, T0, T1, T2, T3, T4, T5, T6, T7, T8, T9, T10, T11,
       T12, T13, T14, T15, T16, T17, T18, T19, T20, T21, T22, T23, T24, T25, T26, T27, T28, T29, T30, T31;

  Pixel pixel_1 (.H(H1), .T(T1), .A(A1), .Light(Out[30]), .Smash(S1), .Clock(Clock));
  Pixel pixel_2 (.H(H0), .T(T0), .A(A0), .Light(Out[31]), .Smash(S0), .Clock(Clock));
  Pixel pixel_3 (.H(H16), .T(T16), .A(A16), .Light(Out[15]), .Smash(S16), .Clock(Clock));
  Pixel pixel_4 (.H(H17), .T(T17), .A(A17), .Light(Out[14]), .Smash(S17), .Clock(Clock));
  Decoder #(.select(5), .disabled(0)) decoder_1 (
    .out0(A0), .out1(A1), .out2(A2), .out3(A3), .out4(A4), .out5(A5), .out6(A6), .out7(A7), .out8(A8),
    .out9(A9), .out10(A10), .out11(A11), .out12(A12), .out13(A13), .out14(A14), .out15(A15), .out16(A16),
    .out17(A17), .out18(A18), .out19(A19), .out20(A20), .out21(A21), .out22(A22), .out23(A23), .out24(A24),
    .out25(A25), .out26(A26), .out27(A27), .out28(A28), .out29(A29), .out30(A30), .out31(A31), .sel(Apple_X),
    .en(EnA));
  Pixel pixel_5 (.H(H3), .T(T3), .A(A3), .Light(Out[28]), .Smash(S3), .Clock(Clock));
  Pixel pixel_6 (.H(H2), .T(T2), .A(A2), .Light(Out[29]), .Smash(S2), .Clock(Clock));
  Pixel pixel_7 (.H(H18), .T(T18), .A(A18), .Light(Out[13]), .Smash(S18), .Clock(Clock));
  Pixel pixel_8 (.H(H19), .T(T19), .A(A19), .Light(Out[12]), .Smash(S19), .Clock(Clock));
  Pixel pixel_9 (.H(H4), .T(T4), .A(A4), .Light(Out[27]), .Smash(S4), .Clock(Clock));
  Pixel pixel_10 (.H(H5), .T(T5), .A(A5), .Light(Out[26]), .Smash(S5), .Clock(Clock));
  Pixel pixel_11 (.H(H20), .T(T20), .A(A20), .Light(Out[11]), .Smash(S20), .Clock(Clock));
  Pixel pixel_12 (.H(H21), .T(T21), .A(A21), .Light(Out[10]), .Smash(S21), .Clock(Clock));
  Decoder #(.select(5), .disabled(0)) decoder_2 (
    .out0(T0), .out1(T1), .out2(T2), .out3(T3), .out4(T4), .out5(T5), .out6(T6), .out7(T7), .out8(T8),
    .out9(T9), .out10(T10), .out11(T11), .out12(T12), .out13(T13), .out14(T14), .out15(T15), .out16(T16),
    .out17(T17), .out18(T18), .out19(T19), .out20(T20), .out21(T21), .out22(T22), .out23(T23), .out24(T24),
    .out25(T25), .out26(T26), .out27(T27), .out28(T28), .out29(T29), .out30(T30), .out31(T31), .sel(Tail_X),
    .en(EnT));
  Pixel pixel_13 (.H(H6), .T(T6), .A(A6), .Light(Out[25]), .Smash(S6), .Clock(Clock));
  Pixel pixel_14 (.H(H7), .T(T7), .A(A7), .Light(Out[24]), .Smash(S7), .Clock(Clock));
  Pixel pixel_15 (.H(H22), .T(T22), .A(A22), .Light(Out[9]), .Smash(S22), .Clock(Clock));
  Pixel pixel_16 (.H(H23), .T(T23), .A(A23), .Light(Out[8]), .Smash(S23), .Clock(Clock));
  Pixel pixel_17 (.H(H8), .T(T8), .A(A8), .Light(Out[23]), .Smash(S8), .Clock(Clock));
  Pixel pixel_18 (.H(H9), .T(T9), .A(A9), .Light(Out[22]), .Smash(S9), .Clock(Clock));
  Pixel pixel_19 (.H(H24), .T(T24), .A(A24), .Light(Out[7]), .Smash(S24), .Clock(Clock));
  Pixel pixel_20 (.H(H25), .T(T25), .A(A25), .Light(Out[6]), .Smash(S25), .Clock(Clock));
  Pixel pixel_21 (.H(H11), .T(T11), .A(A11), .Light(Out[20]), .Smash(S11), .Clock(Clock));
  Pixel pixel_22 (.H(H10), .T(T10), .A(A10), .Light(Out[21]), .Smash(S10), .Clock(Clock));
  Pixel pixel_23 (.H(H26), .T(T26), .A(A26), .Light(Out[5]), .Smash(S26), .Clock(Clock));
  Pixel pixel_24 (.H(H27), .T(T27), .A(A27), .Light(Out[4]), .Smash(S27), .Clock(Clock));
  Decoder #(.select(5), .disabled(0)) decoder_3 (
    .out0(H0), .out1(H1), .out2(H2), .out3(H3), .out4(H4), .out5(H5), .out6(H6), .out7(H7), .out8(H8),
    .out9(H9), .out10(H10), .out11(H11), .out12(H12), .out13(H13), .out14(H14), .out15(H15), .out16(H16),
    .out17(H17), .out18(H18), .out19(H19), .out20(H20), .out21(H21), .out22(H22), .out23(H23), .out24(H24),
    .out25(H25), .out26(H26), .out27(H27), .out28(H28), .out29(H29), .out30(H30), .out31(H31), .sel(Head_X),
    .en(EnH));
  Pixel pixel_25 (.H(H12), .T(T12), .A(A12), .Light(Out[19]), .Smash(S12), .Clock(Clock));
  Pixel pixel_26 (.H(H13), .T(T13), .A(A13), .Light(Out[18]), .Smash(S13), .Clock(Clock));
  Pixel pixel_27 (.H(H28), .T(T28), .A(A28), .Light(Out[3]), .Smash(S28), .Clock(Clock));
  Pixel pixel_28 (.H(H29), .T(T29), .A(A29), .Light(Out[2]), .Smash(S29), .Clock(Clock));
  Pixel pixel_29 (.H(H14), .T(T14), .A(A14), .Light(Out[17]), .Smash(S14), .Clock(Clock));
  Pixel pixel_30 (.H(H15), .T(T15), .A(A15), .Light(Out[16]), .Smash(S15), .Clock(Clock));
  Pixel pixel_31 (.H(H30), .T(T30), .A(A30), .Light(Out[1]), .Smash(S30), .Clock(Clock));
  Pixel pixel_32 (.H(H31), .T(T31), .A(A31), .Light(Out[0]), .Smash(S31), .Clock(Clock));
  or or_1 (Smash, S0, S1, S2, S3, S4, S5, S6, S7, S8, S9, S10, S11, S12, S13, S14, S15, S16, S17, S18, S19, S20, S21, S22, S23, S24, S25, S26, S27, S28, S29, S30, S31);

  // Other names for the same wires on the sheet: L31 = Out[0]; L30 = Out[1]; L29 = Out[2]; L28 = Out[3]; L27 = Out[4];
  //   L26 = Out[5]; L25 = Out[6]; L24 = Out[7]; L23 = Out[8]; L22 = Out[9]; L21 = Out[10]; L20 = Out[11];
  //   L19 = Out[12]; L18 = Out[13]; L17 = Out[14]; L16 = Out[15]; L15 = Out[16]; L14 = Out[17]; L13 = Out[18];
  //   L12 = Out[19]; L11 = Out[20]; L10 = Out[21]; L9 = Out[22]; L8 = Out[23]; L7 = Out[24]; L6 = Out[25];
  //   L5 = Out[26]; L4 = Out[27]; L3 = Out[28]; L2 = Out[29]; L1 = Out[30]; L0 = Out[31]

  // Notes on the sheet:
  //   0
  //   31
  //   Датчик коллизии
  //   Значения светодиодов на линии
endmodule

module Pixel (
  input  Clock,
  input  H,
  input  T,
  input  A,
  output Light,
  output Smash
);

  wire and_1_out, and_2_out, and_3_out, or_1_out;

  and and_1 (and_1_out, H, ~Light);  // AND_Gate
  D_Flip_Flop #(.trigger("low")) d_ff_1 (
    .clk(Clock), .D(or_1_out), .Q(Light), .en(or_1_out), .reset(and_2_out));  // open: Qn, preset
  or or_1 (or_1_out, and_1_out, and_3_out);
  and and_2 (and_2_out, ~H, ~Clock, T);  // AND_Gate
  and and_3 (and_3_out, ~Light, A);  // AND_Gate
  and and_4 (Smash, Light, Clock, H);

  // Notes on the sheet:
  //   H:
  //   T:
  //   A:
  //   Clock:
  //   Входные данные
  //    Вход тактового генератора
  //   Датчик коллизии
  //   Как работает D-тригер Light:
  //   И при этом сам бит Light не поднят
  //   Последние два битика несут в себе текущее направление движения головы
  //   1 - если координата хвоста совпадает с координатой пикселя
  //    1 - если координата яблока совпадает с координатой пикселя
  //   Включение пикселя(светодиода на матрице)
  //   LIght отвечает за то, горит ли данный пиксель на матрице или нет.
  //   Помимо этого, при помощи него определяется коллизия
  //   Это нужно, чтобы коллизия работала корректно, то есть
  //   Light поднимается когда либо поднят H0(голова зашла в этот битик), либо когда поднят бит A(здесь появилось яблочко)
  //    Массив битов, отвечающий за данные головы, первый бит(считая справа) поднят, если координата головы совпадает с этим пикселем
  //   Однако, не всё так просто, к нему подключён Clock - тактовый генератор, Light поднимается только когда Clock = 0(срабатывает при низком уровне)
  //   Если изменять значение Light в тот же момент, когда на него подали H0, то Smash будет подниматься даже тогда, когда мы просто зажгли битик
  //   Если же использовать тактовый генератор, то бит Smash будет подниматься только тогда, когда голова зашла в поднятый до этого битик(то что нужно!)
  //   Light опускается если зашёл хвост, но при этом здесь нет головы, в этом случае коллизия не происходит, но и бит не должен опускаться
endmodule

module transTo2bit (
  input  [6:0] In,
  output En,
  output [1:0] Out
);

  wire and_1_out, and_2_out, and_3_out, and_4_out;
  wire [6:0] xnor_1_out, xnor_2_out, xnor_3_out, xnor_4_out;

  // Probe on 7'b1110111
  // Probe on 7'b1100001
  // Probe on 7'b1110011
  // Probe on 7'b1100100
  assign xnor_1_out = ~(In ^ 7'b1110111);  // XNOR_Gate xnor_1, 7 bits wide
  assign xnor_2_out = ~(In ^ 7'b1100001);  // XNOR_Gate xnor_2, 7 bits wide
  assign xnor_3_out = ~(In ^ 7'b1110011);  // XNOR_Gate xnor_3, 7 bits wide
  assign xnor_4_out = ~(In ^ 7'b1100100);  // XNOR_Gate xnor_4, 7 bits wide
  and and_1 (and_1_out, xnor_1_out[0], xnor_1_out[1], xnor_1_out[2], xnor_1_out[3], xnor_1_out[4], xnor_1_out[5], xnor_1_out[6]);
  and and_2 (and_2_out, xnor_2_out[0], xnor_2_out[1], xnor_2_out[2], xnor_2_out[3], xnor_2_out[4], xnor_2_out[5], xnor_2_out[6]);
  and and_3 (and_3_out, xnor_3_out[0], xnor_3_out[1], xnor_3_out[2], xnor_3_out[3], xnor_3_out[4], xnor_3_out[5], xnor_3_out[6]);
  and and_4 (and_4_out, xnor_4_out[0], xnor_4_out[1], xnor_4_out[2], xnor_4_out[3], xnor_4_out[4], xnor_4_out[5], xnor_4_out[6]);
  or or_1 (En, and_1_out, and_2_out, and_3_out, and_4_out);
  Transistor #(.\type ("n"), .width(2)) transistor_1 (.in(2'b00), .out(Out), .gate(and_1_out));
  Transistor #(.\type ("n"), .width(2)) transistor_2 (.in(2'b01), .out(Out), .gate(and_2_out));
  Transistor #(.\type ("n"), .width(2)) transistor_3 (.in(2'b10), .out(Out), .gate(and_3_out));
  Transistor #(.\type ("n"), .width(2)) transistor_4 (.in(2'b11), .out(Out), .gate(and_4_out));
  Pull_Resistor pull_resistor_1 (.node(Out));
endmodule
