// Logisim project Snake.circ as structural Verilog: 13 circuits, main circuit Snake
module Snake (
);

  wire clock_1_out, main_1_dead, main_1_pause_2, main_1_play, PAUSE_out, START_out;
  wire [3:0] main_1_maxscore1, main_1_maxscore2, main_1_maxscore3, main_1_maxscore4, main_1_score1,
       main_1_score2, main_1_score3, main_1_score4;
  wire [6:0] keyboard_1_data;
  wire [29:0] main_1_out_17, main_1_out_18, main_1_out_24, main_1_out_25, main_1_out_28, main_1_out_29,
       main_1_out_32, main_1_out_33, main_1_out_36, main_1_out_37, main_1_out_40, main_1_out_41,
       main_1_out_44, main_1_out_45, main_1_out_48, main_1_out_49, main_1_out_52, main_1_out_53,
       main_1_out_56, main_1_out_57, main_1_out_60, main_1_out_61, main_1_out_64, main_1_out_65,
       main_1_out_68, main_1_out_69, main_1_out_72, main_1_out_73, main_1_out_76, main_1_out_77;
  wire [31:0] main_1_out_5, main_1_out_6, main_1_out_15, main_1_out_16, main_1_out_22, main_1_out_23,
       main_1_out_26, main_1_out_27, main_1_out_30, main_1_out_31, main_1_out_34, main_1_out_35,
       main_1_out_38, main_1_out_39, main_1_out_42, main_1_out_43, main_1_out_46, main_1_out_47,
       main_1_out_50, main_1_out_51, main_1_out_54, main_1_out_55, main_1_out_58, main_1_out_59,
       main_1_out_62, main_1_out_63, main_1_out_66, main_1_out_67, main_1_out_70, main_1_out_71,
       main_1_out_74, main_1_out_75;

  Clock clock_1 (.out(clock_1_out));
  Hex_Digit_Display hex_digit_display_1 (.value(main_1_maxscore4));  // open: dp
  DotMatrix #(.inputtype("row"), .matrixcols(32), .matrixrows(32)) dotmatrix_1 (
    .row0(main_1_out_5), .row1(main_1_out_15), .row2(main_1_out_22), .row3(main_1_out_26),
    .row4(main_1_out_30), .row5(main_1_out_34), .row6(main_1_out_38), .row7(main_1_out_42),
    .row8(main_1_out_46), .row9(main_1_out_50), .row10(main_1_out_54), .row11(main_1_out_58),
    .row12(main_1_out_62), .row13(main_1_out_66), .row14(main_1_out_70), .row15(main_1_out_74),
    .row16(main_1_out_6), .row17(main_1_out_16), .row18(main_1_out_23), .row19(main_1_out_27),
    .row20(main_1_out_31), .row21(main_1_out_35), .row22(main_1_out_39), .row23(main_1_out_43),
    .row24(main_1_out_47), .row25(main_1_out_51), .row26(main_1_out_55), .row27(main_1_out_59),
    .row28(main_1_out_63), .row29(main_1_out_67), .row30(main_1_out_71), .row31(main_1_out_75));
  DotMatrix #(.inputtype("row"), .matrixcols(30), .matrixrows(30)) dotmatrix_2 (
    .row0(main_1_out_17), .row1(main_1_out_24), .row2(main_1_out_28), .row3(main_1_out_32),
    .row4(main_1_out_36), .row5(main_1_out_40), .row6(main_1_out_44), .row7(main_1_out_48),
    .row8(main_1_out_52), .row9(main_1_out_56), .row10(main_1_out_60), .row11(main_1_out_64),
    .row12(main_1_out_68), .row13(main_1_out_72), .row14(main_1_out_76), .row15(main_1_out_18),
    .row16(main_1_out_25), .row17(main_1_out_29), .row18(main_1_out_33), .row19(main_1_out_37),
    .row20(main_1_out_41), .row21(main_1_out_45), .row22(main_1_out_49), .row23(main_1_out_53),
    .row24(main_1_out_57), .row25(main_1_out_61), .row26(main_1_out_65), .row27(main_1_out_69),
    .row28(main_1_out_73), .row29(main_1_out_77));
  Keyboard_part keyboard_1 (.clk(clock_1_out), .data(keyboard_1_data));  // open: re, clr, avail
  Hex_Digit_Display hex_digit_display_2 (.value(main_1_maxscore2));  // open: dp
  Hex_Digit_Display hex_digit_display_3 (.value(main_1_maxscore3));  // open: dp
  Hex_Digit_Display hex_digit_display_4 (.value(main_1_maxscore1));  // open: dp
  Button START (.out(START_out));
  Hex_Digit_Display hex_digit_display_5 (.value(main_1_score4));  // open: dp
  Button PAUSE (.out(PAUSE_out));
  Hex_Digit_Display hex_digit_display_6 (.value(main_1_score2));  // open: dp
  Hex_Digit_Display hex_digit_display_7 (.value(main_1_score3));  // open: dp
  LED led_1 (.in(main_1_play));
  LED led_2 (.in(main_1_dead));
  LED led_3 (.in(main_1_pause_2));
  Hex_Digit_Display hex_digit_display_8 (.value(main_1_score1));  // open: dp
  MAIN main_1 (
    .START(START_out), .Clock(clock_1_out), .out_17(main_1_out_17), .out_18(main_1_out_18),
    .out_24(main_1_out_24), .out_25(main_1_out_25), .out_28(main_1_out_28), .out_29(main_1_out_29),
    .out_32(main_1_out_32), .out_33(main_1_out_33), .out_36(main_1_out_36), .out_37(main_1_out_37),
    .out_40(main_1_out_40), .out_41(main_1_out_41), .out_44(main_1_out_44), .out_45(main_1_out_45),
    .out_48(main_1_out_48), .out_49(main_1_out_49), .out_52(main_1_out_52), .out_53(main_1_out_53),
    .out_56(main_1_out_56), .out_57(main_1_out_57), .out_60(main_1_out_60), .out_61(main_1_out_61),
    .out_64(main_1_out_64), .out_65(main_1_out_65), .out_68(main_1_out_68), .out_69(main_1_out_69),
    .out_72(main_1_out_72), .out_73(main_1_out_73), .out_76(main_1_out_76), .out_77(main_1_out_77),
    .out_5(main_1_out_5), .out_6(main_1_out_6), .out_15(main_1_out_15), .out_16(main_1_out_16),
    .out_22(main_1_out_22), .out_23(main_1_out_23), .out_26(main_1_out_26), .out_27(main_1_out_27),
    .out_30(main_1_out_30), .out_31(main_1_out_31), .out_34(main_1_out_34), .out_35(main_1_out_35),
    .out_38(main_1_out_38), .out_39(main_1_out_39), .out_42(main_1_out_42), .out_43(main_1_out_43),
    .out_46(main_1_out_46), .out_47(main_1_out_47), .out_50(main_1_out_50), .out_51(main_1_out_51),
    .out_54(main_1_out_54), .out_55(main_1_out_55), .out_58(main_1_out_58), .out_59(main_1_out_59),
    .out_62(main_1_out_62), .out_63(main_1_out_63), .out_66(main_1_out_66), .out_67(main_1_out_67),
    .out_70(main_1_out_70), .out_71(main_1_out_71), .out_74(main_1_out_74), .out_75(main_1_out_75),
    .KeyboardInput(keyboard_1_data), .PAUSE(PAUSE_out), .Score2(main_1_score2), .Score1(main_1_score1),
    .Play(main_1_play), .Pause_2(main_1_pause_2), .Dead(main_1_dead), .Score3(main_1_score3),
    .Score4(main_1_score4), .MaxScore1(main_1_maxscore1), .MaxScore2(main_1_maxscore2),
    .MaxScore3(main_1_maxscore3), .MaxScore4(main_1_maxscore4));

  // Notes on the sheet:
  //   Launching the game:
  //   1 - Enable the tics
  //   2 - Press start
  //   3 - Use the keyboard to control the snake
endmodule

module MAIN (
  input  Clock,
  input  [6:0] KeyboardInput,
  input  PAUSE,
  input  START,
  output [31:0] out_5,
  output [31:0] out_6,
  output [3:0] Score1,
  output [3:0] Score2,
  output [3:0] Score3,
  output [3:0] Score4,
  output [3:0] MaxScore1,
  output [3:0] MaxScore2,
  output [3:0] MaxScore3,
  output [3:0] MaxScore4,
  output [31:0] out_15,
  output [31:0] out_16,
  output [29:0] out_17,
  output [29:0] out_18,
  output Pause_2,
  output Dead,
  output Play,
  output [31:0] out_22,
  output [31:0] out_23,
  output [29:0] out_24,
  output [29:0] out_25,
  output [31:0] out_26,
  output [31:0] out_27,
  output [29:0] out_28,
  output [29:0] out_29,
  output [31:0] out_30,
  output [31:0] out_31,
  output [29:0] out_32,
  output [29:0] out_33,
  output [31:0] out_34,
  output [31:0] out_35,
  output [29:0] out_36,
  output [29:0] out_37,
  output [31:0] out_38,
  output [31:0] out_39,
  output [29:0] out_40,
  output [29:0] out_41,
  output [31:0] out_42,
  output [31:0] out_43,
  output [29:0] out_44,
  output [29:0] out_45,
  output [31:0] out_46,
  output [31:0] out_47,
  output [29:0] out_48,
  output [29:0] out_49,
  output [31:0] out_50,
  output [31:0] out_51,
  output [29:0] out_52,
  output [29:0] out_53,
  output [31:0] out_54,
  output [31:0] out_55,
  output [29:0] out_56,
  output [29:0] out_57,
  output [31:0] out_58,
  output [31:0] out_59,
  output [29:0] out_60,
  output [29:0] out_61,
  output [31:0] out_62,
  output [31:0] out_63,
  output [29:0] out_64,
  output [29:0] out_65,
  output [31:0] out_66,
  output [31:0] out_67,
  output [29:0] out_68,
  output [29:0] out_69,
  output [31:0] out_70,
  output [31:0] out_71,
  output [29:0] out_72,
  output [29:0] out_73,
  output [31:0] out_74,
  output [31:0] out_75,
  output [29:0] out_76,
  output [29:0] out_77
);

  wire A, AddPartToQ, and_1_out, and_2_out, and_4_out, and_5_out, and_8_out, and_9_out, and_10_out,
       and_12_out, and_13_out, cdm_8_mark5_1_p1, cdm_8_mark5_1_p2, cdm_8_mark5_1_p4, cdm_8_mark5_1_p5,
       cdm_8_mark5_1_p6, cdm_8_mark5_1_p7, cdm_8_mark5_1_p8, code, controlled_inverter_1_out,
       counter_1_carry, counter_2_carry, counter_3_carry, counter_4_carry, counter_6_carry, counter_7_carry,
       counter_8_carry, counter_9_carry, counter_12_carry, D, d_ff_2_q, d_ff_3_q, data, decoder_3_out0,
       decoder_3_out1, DownT, EatApple, EnApple, EnTurn, eq4_1_eq, eq4_2_eq, eq4_3_eq, eq4_4_eq, eq30_1_eq,
       eq30_2_eq, GameCl, I_Oadr, I_Osel, in_out_prime, LeftT, LoadPartToProc, LoadPartToTail, nand_1_out,
       NeedNewPart, not_1_out, not_2_out, not_3_out, not_4_out, not_5_out, not_6_out, not_7_out, not_8_out,
       not_9_out, not_10_out, not_11_out, or_1_out, or_2_out, or_3_out, or_5_out, or_6_out, or_7_out,
       or_9_out, ProcCl, ProcGotPart, ProcWork, RAM, RightT, S, Smash, Spawn, TailWait, Turn, UpT, W;
  wire [1:0] Direction, keyboard_1_where, register_3_q;
  wire [5:0] CurrPart, xnor_1_out, xnor_2_out;
  wire [6:0] controlled_buffer_1_out;
  wire [7:0] cdm_8_mark5_1_p11, cdm_8_mark5_1_p12, I_Odat, register_2_q;
  wire [7:1] cdm_8_mark5_1_p10;
  wire [9:0] CurrLength;
  wire [29:0] Apple_X, Apple_Y, Head_X, Head_Y, Tail_X, Tail_Y;

  // Probe on cdm_8_mark5_1_p4
  // Probe on cdm_8_mark5_1_p2
  // Probe on cdm_8_mark5_1_p1
  and and_1 (and_1_out, EnTurn, ~Pause_2, ~or_1_out);  // AND_Gate
  assign controlled_buffer_1_out = and_1_out ? KeyboardInput : 7'bz;  // Controlled_Buffer controlled_buffer_1
  Pull_Resistor pull_resistor_1 (.node(controlled_buffer_1_out));
  Keyboard keyboard_1 (
    .GameClock(GameCl), .START(START), .Where(keyboard_1_where), .W(W), .A(A), .S(S), .D(D),
    .In(controlled_buffer_1_out));
  and and_2 (and_2_out, ~GameCl, PAUSE);  // AND_Gate
  assign controlled_inverter_1_out = Pause_2 ? ~PAUSE : 1'bz;  // Controlled_Inverter controlled_inverter_1
  Pull_Resistor #(.pull(1)) pull_resistor_2 (.node(controlled_inverter_1_out));
  // Probe on cdm_8_mark5_1_p5
  // Probe on cdm_8_mark5_1_p6
  ClManager clmanager_1 (
    .EnG(Play), .GameOver(Dead), .ProcWorks(ProcWork), .START(START), .Pause(Pause_2), .Clock(Clock),
    .GameCl(GameCl), .ProcCl(ProcCl));
  or or_1 (or_1_out, LoadPartToProc, d_ff_3_q, AddPartToQ);
  Register #(.width(2), .trigger("falling")) register_1 (
    .D(keyboard_1_where), .Q(Direction), .clk(Turn), .clr(START));  // open: en
  D_Flip_Flop d_ff_1 (.clk(and_2_out), .D(controlled_inverter_1_out), .Q(Pause_2));  // open: Qn, preset, en, reset
  Decoder #(.disabled(0)) decoder_1 (.out0(code), .out1(data), .sel(cdm_8_mark5_1_p7), .en(cdm_8_mark5_1_p8));
  // CdM_8_mark5 cdm_8_mark5_1: pin names not known; wires that end beside it: cdm_8_mark5_1_p1, cdm_8_mark5_1_p2, ProcCl, cdm_8_mark5_1_p4, cdm_8_mark5_1_p5, cdm_8_mark5_1_p6, cdm_8_mark5_1_p7, cdm_8_mark5_1_p8, in_out_prime, {cdm_8_mark5_1_p10, I_Oadr}, cdm_8_mark5_1_p11, cdm_8_mark5_1_p12
  assign I_Odat = not_1_out ? cdm_8_mark5_1_p11 : 8'bz;  // Controlled_Buffer controlled_buffer_2
  not not_1 (not_1_out, in_out_prime);
  assign cdm_8_mark5_1_p12 = in_out_prime ? I_Odat : 8'bz;  // Controlled_Buffer controlled_buffer_3
  and and_3 (I_Osel, and_5_out, ProcCl, data);
  D_Flip_Flop d_ff_2 (.Q(d_ff_2_q), .preset(EatApple), .reset(counter_1_carry));  // open: clk, D, Qn, en
  D_Flip_Flop d_ff_3 (.Q(d_ff_3_q), .preset(Turn), .reset(or_2_out));  // open: clk, D, Qn, en
  or or_2 (or_2_out, GameCl, START);
  Eq30 eq30_1 (.A(Head_X), .B(Apple_X), .Eq(eq30_1_eq));
  Eq30 eq30_2 (.A(Head_Y), .B(Apple_Y), .Eq(eq30_2_eq));
  Counter #(.width(4), .max('h5)) counter_1 (
    .carry(counter_1_carry), .clk(and_4_out), .clr(counter_1_carry));  // open: load, D, count, Q
  and and_4 (and_4_out, d_ff_2_q, Clock);
  not not_2 (not_2_out, ProcCl);
  and and_5 (and_5_out, ~cdm_8_mark5_1_p10[1], ~cdm_8_mark5_1_p10[2], ~cdm_8_mark5_1_p10[3], cdm_8_mark5_1_p10[4], cdm_8_mark5_1_p10[5], cdm_8_mark5_1_p10[6], cdm_8_mark5_1_p10[7]);  // AND_Gate
  and and_6 (RAM, data, ~I_Osel);  // AND_Gate
  Counter #(.width(4), .max('h9), .trigger("falling")) counter_2 (
    .Q(Score1), .carry(counter_2_carry), .clk(and_4_out), .clr(START));  // open: load, D, count
  and and_7 (EatApple, eq30_1_eq, EnApple, ~GameCl, eq30_2_eq);  // AND_Gate
  ROM rom_1 (.addr({cdm_8_mark5_1_p10, I_Oadr}), .data(I_Odat), .sel(code));
  RAM ram_1 (
    .addr({cdm_8_mark5_1_p10, I_Oadr}), .data(I_Odat), .sel(RAM), .clk(not_2_out), .ld(in_out_prime));  // open: clr
  Counter #(.width(4), .max('h9), .trigger("falling")) counter_3 (
    .Q(Score3), .carry(counter_3_carry), .clk(counter_4_carry), .clr(START));  // open: load, D, count
  Counter #(.width(4), .max('h9), .trigger("falling")) counter_4 (
    .Q(Score2), .carry(counter_4_carry), .clk(counter_2_carry), .clr(START));  // open: load, D, count
  Eq4 eq4_1 (.A(Score4), .B(MaxScore4), .Eq(eq4_1_eq));
  Eq4 eq4_2 (.A(Score3), .B(MaxScore3), .Eq(eq4_2_eq));
  Eq4 eq4_3 (.A(Score2), .B(MaxScore2), .Eq(eq4_3_eq));
  Eq4 eq4_4 (.A(Score1), .B(MaxScore1), .Eq(eq4_4_eq));
  and and_8 (and_8_out, xnor_1_out[0], xnor_1_out[1], xnor_1_out[2], xnor_1_out[3], xnor_1_out[4], xnor_1_out[5]);
  Counter #(.width(4), .max('h9), .trigger("falling")) counter_5 (
    .Q(Score4), .clk(counter_3_carry), .clr(START));  // open: load, D, count, carry
  and and_9 (and_9_out, eq4_1_eq, eq4_2_eq, eq4_3_eq, eq4_4_eq);
  Counter #(.width(6), .max('h3f), .trigger("falling")) counter_6 (
    .Q(CurrPart), .carry(counter_6_carry), .clk(GameCl), .clr(or_3_out));  // open: load, D, count
  or or_3 (or_3_out, not_6_out, START);
  assign xnor_1_out = ~(CurrPart ^ CurrLength[5:0]);  // XNOR_Gate xnor_1, 6 bits wide
  Counter #(.width(4), .max('h9), .trigger("falling")) counter_7 (
    .Q(MaxScore1), .carry(counter_7_carry), .clk(and_10_out));  // open: load, D, count, clr
  and and_10 (and_10_out, and_4_out, and_9_out);
  assign xnor_2_out = ~({6{1'b0}} ^ CurrPart);  // XNOR_Gate xnor_2, 6 bits wide
  or or_4 (AddPartToQ, and_8_out, counter_6_carry, Turn);
  not not_3 (not_3_out, AddPartToQ);
  not not_4 (not_4_out, not_5_out);
  not not_5 (not_5_out, not_3_out);
  not not_6 (not_6_out, not_4_out);
  Counter #(.width(4), .max('h9), .trigger("falling")) counter_8 (
    .Q(MaxScore2), .carry(counter_8_carry), .clk(counter_7_carry));  // open: load, D, count, clr
  not not_7 (not_7_out, START);
  or or_5 (or_5_out, START, EatApple);
  and and_11 (EnTurn, ~GameCl, nand_1_out);  // AND_Gate
  nand nand_1 (nand_1_out, xnor_2_out[0], xnor_2_out[1], xnor_2_out[2], xnor_2_out[3], xnor_2_out[4], xnor_2_out[5]);
  Counter #(.width(4), .max('h9), .trigger("falling")) counter_9 (
    .Q(MaxScore3), .carry(counter_9_carry), .clk(counter_8_carry));  // open: load, D, count, clr
  Counter #(.width(4), .max('h9), .trigger("falling")) counter_10 (
    .Q(MaxScore4), .clk(counter_9_carry));  // open: load, D, count, carry, clr
  Counter #(.width(10), .max('h3ff), .ongoal("stay")) counter_11 (
    .load(START), .D(10'h4), .count(not_7_out), .Q(CurrLength), .clk(or_5_out));  // open: carry, clr
  Head head_1 (
    .W(W), .A(A), .S(S), .D(D), .START(START), .GameClock(GameCl), .Head_Y_toMatrix(Head_Y),
    .Head_X_toMatrix(Head_X), .Turn(Turn), .EnH(Play));
  D_Flip_Flop #(.trigger("falling")) d_ff_4 (.clk(START), .D(1'b1), .Q(Spawn), .reset(Play));  // open: Qn, preset, en
  Tail tail_1 (
    .GameClock(GameCl), .START(START), .TailWait(TailWait), .Tail_Y(Tail_Y), .Tail_X(Tail_X), .UpT(UpT),
    .LeftT(LeftT), .DownT(DownT), .RightT(RightT), .EnT(Play));
  Register register_2 (.D({Direction, CurrPart}), .Q(register_2_q), .clk(AddPartToQ), .clr(START));  // open: en
  not not_8 (not_8_out, LoadPartToTail);
  or or_6 (or_6_out, LoadPartToTail, and_12_out);
  D_Flip_Flop #(.trigger("falling")) d_ff_5 (
    .clk(GameCl), .D(1'b0), .Q(TailWait), .preset(EatApple), .reset(START));  // open: Qn, en
  toMatrix tomatrix_1 (
    .Head_X(Head_X), .Head_Y(Head_Y), .Tail_Y(Tail_Y), ._0(out_17), .out_24(out_25), .out_9(out_24),
    .out_25(out_29), .out_10(out_28), .out_26(out_33), .out_11(out_32), .out_27(out_37), .out_12(out_36),
    .out_28(out_41), .out_13(out_40), .out_29(out_45), .out_14(out_44), .out_30(out_49), .out_15(out_48),
    .out_31(out_53), .Smash(Smash), .out_16(out_52), .out_32(out_57), .out_17(out_56), .out_33(out_61),
    .out_18(out_60), .out_34(out_65), .out_19(out_64), .out_35(out_69), .out_20(out_68), .out_36(out_73),
    .out_21(out_72), .out_37(out_77), .out_22(out_76), .out_23(out_18), .CLEAR(START), .START(Spawn),
    .Tail_X(Tail_X));
  assign I_Odat = and_13_out ? {Play, LoadPartToProc, NeedNewPart, {5{1'b0}}} : 8'bz;  // Controlled_Buffer controlled_buffer_4
  assign I_Odat = ProcGotPart ? register_2_q : 8'bz;  // Controlled_Buffer controlled_buffer_5
  D_Flip_Flop #(.trigger("falling")) d_ff_6 (
    .clk(AddPartToQ), .D(1'b1), .Q(LoadPartToProc), .reset(or_7_out));  // open: Qn, preset, en
  or or_7 (or_7_out, ProcGotPart, START);
  Counter #(.width(6), .max('h3f), .ongoal("load"), .trigger("falling")) counter_12 (
    .load(1'b1), .D(I_Odat[5:0]), .count(not_8_out), .carry(counter_12_carry), .clk(or_6_out), .clr(START));  // open: Q
  and and_12 (and_12_out, ~TailWait, GameCl);  // AND_Gate
  Register #(.width(2)) register_3 (.D(I_Odat[7:6]), .Q(register_3_q), .clk(LoadPartToTail), .clr(START));  // open: en
  D_Flip_Flop d_ff_7 (.Q(Dead), .preset(Smash), .reset(START));  // open: clk, D, Qn, en
  and and_13 (and_13_out, decoder_3_out1, ~I_Oadr);  // AND_Gate
  and and_14 (ProcGotPart, decoder_3_out1, I_Oadr);
  not not_9 (not_9_out, NeedNewPart);
  and and_15 (NeedNewPart, ~TailWait, counter_12_carry);  // AND_Gate
  and and_16 (LoadPartToTail, I_Oadr, decoder_3_out0);
  or or_8 (ProcWork, LoadPartToProc, AddPartToQ, NeedNewPart);
  Decoder #(.select(2), .disabled(0)) decoder_2 (
    .out0(UpT), .out1(LeftT), .out2(DownT), .out3(RightT), .sel(register_3_q), .en(not_9_out));
  not not_10 (not_10_out, not_11_out);
  not not_11 (not_11_out, START);
  or or_9 (or_9_out, TailWait, Spawn);
  Apples apples_1 (
    .NewApple(or_9_out), .in_1(out_17), .in_2(out_18), .in_5(out_24), .in_6(out_25), .in_8(out_28),
    .in_9(out_29), .in_10(out_32), .in_11(out_33), .in_12(out_36), .in_13(out_37), .in_14(out_40),
    .in_15(out_41), .in_16(out_44), .in_17(out_45), .in_18(out_48), .in_19(out_49), .in_20(out_52),
    .in_21(out_53), .in_22(out_56), .in_23(out_57), .in_24(out_60), .in_25(out_61), .in_26(out_64),
    .in_27(out_65), .in_28(out_68), .in_29(out_69), .in_30(out_72), .in_31(out_73), .in_32(out_76),
    .in_33(out_77), .out_34(out_5), .out_35(out_74), .out_36(out_15), .out_37(out_6), .out_38(out_22),
    .out_39(out_16), .out_40(out_26), .out_41(out_23), .out_42(out_30), .out_43(out_27), .out_44(out_34),
    .out_45(out_31), .out_46(out_38), .out_47(out_35), .out_48(out_42), .out_49(out_39), .out_50(out_46),
    .out_51(out_43), .out_52(out_50), .out_53(out_47), .out_54(out_54), .out_55(out_51), .out_56(out_58),
    .out_57(out_55), .out_58(out_62), .out_59(out_59), .out_60(out_66), .out_61(out_63), .out_62(out_70),
    .out_63(out_67), .out_65(out_71), .out_66(out_75), .Apple_Y(Apple_Y), .Apple_X(Apple_X), .Clock(Clock),
    .EnApple(EnApple), .GameOver(Dead));
  Decoder #(.disabled(0)) decoder_3 (.out0(decoder_3_out0), .out1(decoder_3_out1), .sel(in_out_prime), .en(I_Osel));
  D_Flip_Flop #(.trigger("falling")) d_ff_8 (
    .clk(not_10_out), .D(1'b1), .Q(Play), .reset(Dead));  // open: Qn, preset, en

  // Other names for the same wires on the sheet: EnG = Play; GameOver = Dead; MScore1[3:0] = MaxScore1;
  //   MScore2[3:0] = MaxScore2; MScore3[3:0] = MaxScore3; MScore4[3:0] = MaxScore4; OutA0[31:0] = out_5;
  //   OutA1[31:0] = out_15; OutA2[31:0] = out_22; OutA3[31:0] = out_26; OutA4[31:0] = out_30; OutA5[31:0] = out_34;
  //   OutA6[31:0] = out_38; OutA7[31:0] = out_42; OutA8[31:0] = out_46; OutA9[31:0] = out_50; OutA10[31:0] = out_54;
  //   OutA11[31:0] = out_58; OutA12[31:0] = out_62; OutA13[31:0] = out_66; OutA14[31:0] = out_70;
  //   OutA15[31:0] = out_74; OutA16[31:0] = out_6; OutA17[31:0] = out_16; OutA18[31:0] = out_23;
  //   OutA19[31:0] = out_27; OutA20[31:0] = out_31; OutA21[31:0] = out_35; OutA22[31:0] = out_39;
  //   OutA23[31:0] = out_43; OutA24[31:0] = out_47; OutA25[31:0] = out_51; OutA26[31:0] = out_55;
  //   OutA27[31:0] = out_59; OutA28[31:0] = out_63; OutA29[31:0] = out_67; OutA30[31:0] = out_71;
  //   OutA31[31:0] = out_75; OutS0[29:0] = out_17; OutS1[29:0] = out_24; OutS2[29:0] = out_28; OutS3[29:0] = out_32;
  //   OutS4[29:0] = out_36; OutS5[29:0] = out_40; OutS6[29:0] = out_44; OutS7[29:0] = out_48; OutS8[29:0] = out_52;
  //   OutS9[29:0] = out_56; OutS10[29:0] = out_60; OutS11[29:0] = out_64; OutS12[29:0] = out_68;
  //   OutS13[29:0] = out_72; OutS14[29:0] = out_76; OutS15[29:0] = out_18; OutS16[29:0] = out_25;
  //   OutS17[29:0] = out_29; OutS18[29:0] = out_33; OutS19[29:0] = out_37; OutS20[29:0] = out_41;
  //   OutS21[29:0] = out_45; OutS22[29:0] = out_49; OutS23[29:0] = out_53; OutS24[29:0] = out_57;
  //   OutS25[29:0] = out_61; OutS26[29:0] = out_65; OutS27[29:0] = out_69; OutS28[29:0] = out_73;
  //   OutS29[29:0] = out_77; Pause_t = Pause_2; rd_wr_prime = in_out_prime; AppleClock = Clock; ScoreCl = Clock

  // Notes on the sheet:
  //   CLOCK MANAGER
  //   BUTTONS
  //   KEYBOARD MANAGER
  //   CdM-8 mark 5
  //   EATING APPLE
  //   contents of rom_1 (hex, n*v repeats v):
  //   d0 f0 b1 5 e4 1f d0 0 d1 f2 a4 b5 d0 4 a4 d1 f3 d0 1 a4 d1 f4 d0 1 a4 d0 f0 b1 5 e5 1b 25 5 e5 45 d2
  //   f1 ba b 2f 2f f e0 45 d0 f3 b0 a2 8c d2 f3 a8 8e b8 8c a8 d0 f3 b0 d2 f0 72 e1 45 d2 0 d0 f3 a2 25 5
  //   e5 6e d0 f4 b0 0 e0 6e 88 d2 f4 a8 d0 f2 b0 b0 d2 f1 a8 d0 f2 b0 8c d2 f2 a8 d0 f2 b0 d2 f0 72 e1 6e
  //   d2 0 d0 f2 a2 ee
  //   LOAD PARTS MANAGER
  //   SCORE AND SNAKE'S LENGTH
  //   TAIL MANAGER
  //   SNAKE'S OUTPUT CIRCUIT
  //   PROC CONNECTION
  //   PARTS STATES
  //   GAME STATES
  //   APPLES CIRCUIT
  //   OUTPUT TO MATRIX
endmodule

// TAIL
module Tail (
  input  EnT,
  input  TailWait,
  input  GameClock,
  input  START,
  input  UpT,
  input  LeftT,
  input  DownT,
  input  RightT,
  output [29:0] Tail_Y,
  output [29:0] Tail_X
);

  wire and_1_out, and_2_out, not_1_out, not_2_out, or_1_out, or_2_out, or_3_out, or_4_out, or_5_out, or_6_out;
  wire [4:0] Tail_X_t, Tail_Y_t;
  wire [29:0] shifter_1_out, shifter_2_out;

  or or_1 (or_1_out, UpT, START);
  not not_1 (not_1_out, START);
  or or_2 (or_2_out, START, and_1_out);
  or or_3 (or_3_out, UpT, DownT);
  Counter #(.width(5), .max('h1d)) counter_1 (
    .load(or_1_out), .D(5'b01111), .count(not_1_out), .Q(Tail_Y_t), .clk(or_2_out));  // open: carry, clr
  and and_1 (and_1_out, or_3_out, ~TailWait, GameClock);  // AND_Gate
  or or_4 (or_4_out, RightT, START);
  Counter #(.width(5), .max('h1d)) counter_2 (
    .load(or_4_out), .D(5'b01111), .count(not_2_out), .Q(Tail_X_t), .clk(or_5_out));  // open: carry, clr
  not not_2 (not_2_out, START);
  or or_5 (or_5_out, START, and_2_out);
  and and_2 (and_2_out, or_6_out, ~TailWait, GameClock);  // AND_Gate
  or or_6 (or_6_out, LeftT, RightT);
  Shifter #(.width(30)) shifter_1 (.in(30'h1), .\dist (Tail_Y_t), .out(shifter_1_out));
  assign Tail_Y = EnT ? shifter_1_out : 30'bz;  // Controlled_Buffer controlled_buffer_1
  Pull_Resistor pull_resistor_1 (.node(Tail_Y));
  assign Tail_X = EnT ? shifter_2_out : 30'bz;  // Controlled_Buffer controlled_buffer_2
  Shifter #(.width(30)) shifter_2 (.in(30'h1), .\dist (Tail_X_t), .out(shifter_2_out));
  Pull_Resistor pull_resistor_2 (.node(Tail_X));
endmodule

// HEAD
module Head (
  input  W,
  input  A,
  input  S,
  input  D,
  input  START,
  input  GameClock,
  input  EnH,
  output Turn,
  output [29:0] Head_Y_toMatrix,
  output [29:0] Head_X_toMatrix
);

  wire and_1_out, and_2_out, and_3_out, and_4_out, and_5_out, and_6_out, and_7_out, and_8_out, Down, Left,
       not_1_out, not_2_out, or_1_out, or_2_out, or_3_out, or_4_out, or_5_out, or_6_out, or_7_out, or_8_out,
       or_9_out, or_10_out, or_11_out, or_12_out, or_13_out, or_14_out, or_15_out, Right, Up;
  wire [4:0] Head_X, Head_Y;
  wire [29:0] shifter_1_out, shifter_2_out;

  or or_1 (or_1_out, Up, START);
  not not_1 (not_1_out, START);
  or or_2 (or_2_out, START, and_2_out);
  or or_3 (or_3_out, Up, Down);
  D_Flip_Flop d_ff_1 (.Q(Up), .preset(or_5_out), .reset(or_4_out));  // open: clk, D, Qn, en
  or or_4 (or_4_out, A, D);
  or or_5 (or_5_out, START, and_1_out);
  and and_1 (and_1_out, ~Down, W);  // AND_Gate
  Counter #(.width(5), .max('h1d)) counter_1 (
    .load(or_1_out), .D(5'b01011), .count(not_1_out), .Q(Head_Y), .clk(or_2_out));  // open: carry, clr
  and and_2 (and_2_out, or_3_out, GameClock);
  and and_3 (and_3_out, ~Up, S);  // AND_Gate
  D_Flip_Flop d_ff_2 (.Q(Down), .preset(and_3_out), .reset(or_6_out));  // open: clk, D, Qn, en
  and and_4 (and_4_out, ~Right, A);  // AND_Gate
  or or_6 (or_6_out, A, START, D);
  or or_7 (or_7_out, Right, START);
  Counter #(.width(5), .max('h1d)) counter_2 (
    .load(or_7_out), .D(5'b01111), .count(not_2_out), .Q(Head_X), .clk(or_8_out));  // open: carry, clr
  not not_2 (not_2_out, START);
  or or_8 (or_8_out, START, and_5_out);
  and and_5 (and_5_out, or_9_out, GameClock);
  or or_9 (or_9_out, Left, Right);
  D_Flip_Flop d_ff_3 (.Q(Left), .preset(and_4_out), .reset(or_10_out));  // open: clk, D, Qn, en
  and and_6 (and_6_out, ~Left, D);  // AND_Gate
  or or_10 (or_10_out, W, START, S);
  D_Flip_Flop d_ff_4 (.Q(Right), .preset(and_6_out), .reset(or_11_out));  // open: clk, D, Qn, en
  or or_11 (or_11_out, W, START, S);
  or or_12 (or_12_out, Down, Up);
  or or_13 (or_13_out, A, D);
  or or_14 (or_14_out, Left, Right);
  or or_15 (or_15_out, W, S);
  Shifter #(.width(30)) shifter_1 (.in(30'h1), .\dist (Head_Y), .out(shifter_1_out));
  Shifter #(.width(30)) shifter_2 (.in(30'h1), .\dist (Head_X), .out(shifter_2_out));
  and and_7 (and_7_out, or_12_out, or_13_out);
  or or_16 (Turn, and_7_out, and_8_out);
  and and_8 (and_8_out, or_14_out, or_15_out);
  // Probe on Head_Y_toMatrix
  assign Head_Y_toMatrix = EnH ? shifter_1_out : 30'bz;  // Controlled_Buffer controlled_buffer_1
  Pull_Resistor pull_resistor_1 (.node(Head_Y_toMatrix));
  assign Head_X_toMatrix = EnH ? shifter_2_out : 30'bz;  // Controlled_Buffer controlled_buffer_2
  Pull_Resistor pull_resistor_2 (.node(Head_X_toMatrix));
  // Probe on Head_X_toMatrix
endmodule

// SnakeMoving
module toMatrix (
  input  START,
  input  CLEAR,
  input  [29:0] Head_Y,
  input  [29:0] Tail_Y,
  input  [29:0] Head_X,
  input  [29:0] Tail_X,
  output Smash,
  output [29:0] _0,
  output [29:0] out_9,
  output [29:0] out_10,
  output [29:0] out_11,
  output [29:0] out_12,
  output [29:0] out_13,
  output [29:0] out_14,
  output [29:0] out_15,
  output [29:0] out_16,
  output [29:0] out_17,
  output [29:0] out_18,
  output [29:0] out_19,
  output [29:0] out_20,
  output [29:0] out_21,
  output [29:0] out_22,
  output [29:0] out_23,
  output [29:0] out_24,
  output [29:0] out_25,
  output [29:0] out_26,
  output [29:0] out_27,
  output [29:0] out_28,
  output [29:0] out_29,
  output [29:0] out_30,
  output [29:0] out_31,
  output [29:0] out_32,
  output [29:0] out_33,
  output [29:0] out_34,
  output [29:0] out_35,
  output [29:0] out_36,
  output [29:0] out_37
);

  wire H12, H13, H14;

  Pull_Resistor pull_resistor_1 (.node(_0));
  Pull_Resistor pull_resistor_2 (.node(out_24));
  Pull_Resistor pull_resistor_3 (.node(out_9));
  Pull_Resistor pull_resistor_4 (.node(out_25));
  Pull_Resistor pull_resistor_5 (.node(out_10));
  Pull_Resistor pull_resistor_6 (.node(out_26));
  or or_1 (H13, START, Head_Y[13]);
  or or_2 (H12, START, Head_Y[12]);
  Pull_Resistor pull_resistor_7 (.node(out_11));
  Pull_Resistor pull_resistor_8 (.node(out_27));
  or or_3 (H14, START, Head_Y[14]);
  Pull_Resistor pull_resistor_9 (.node(out_12));
  Pull_Resistor pull_resistor_10 (.node(out_28));
  Pull_Resistor pull_resistor_11 (.node(out_13));
  Pull_Resistor pull_resistor_12 (.node(out_29));
  Pull_Resistor pull_resistor_13 (.node(out_14));
  Pull_Resistor pull_resistor_14 (.node(out_30));
  Pull_Resistor pull_resistor_15 (.node(out_15));
  Pull_Resistor pull_resistor_16 (.node(out_31));
  Pull_Resistor pull_resistor_17 (.node(out_16));
  Pull_Resistor pull_resistor_18 (.node(out_32));
  Line line_1 (
    .Out(_0), .Smash(Smash), .CLEAR(CLEAR), .HeadOnLine(Head_X), .TailOnLine(Tail_X), .EnT(Tail_Y[0]),
    .EnH(Head_Y[0]));
  Line line_2 (
    .Out(out_9), .Smash(Smash), .CLEAR(CLEAR), .HeadOnLine(Head_X), .TailOnLine(Tail_X), .EnT(Tail_Y[1]),
    .EnH(Head_Y[1]));
  Line line_3 (
    .Out(out_10), .Smash(Smash), .CLEAR(CLEAR), .HeadOnLine(Head_X), .TailOnLine(Tail_X), .EnT(Tail_Y[2]),
    .EnH(Head_Y[2]));
  Line line_4 (
    .Out(out_11), .Smash(Smash), .CLEAR(CLEAR), .HeadOnLine(Head_X), .TailOnLine(Tail_X), .EnT(Tail_Y[3]),
    .EnH(Head_Y[3]));
  Line line_5 (
    .Out(out_12), .Smash(Smash), .CLEAR(CLEAR), .HeadOnLine(Head_X), .TailOnLine(Tail_X), .EnT(Tail_Y[4]),
    .EnH(Head_Y[4]));
  Line line_6 (
    .Out(out_13), .Smash(Smash), .CLEAR(CLEAR), .HeadOnLine(Head_X), .TailOnLine(Tail_X), .EnT(Tail_Y[5]),
    .EnH(Head_Y[5]));
  Line line_7 (
    .Out(out_14), .Smash(Smash), .CLEAR(CLEAR), .HeadOnLine(Head_X), .TailOnLine(Tail_X), .EnT(Tail_Y[6]),
    .EnH(Head_Y[6]));
  Line line_8 (
    .Out(out_15), .Smash(Smash), .CLEAR(CLEAR), .HeadOnLine(Head_X), .TailOnLine(Tail_X), .EnT(Tail_Y[7]),
    .EnH(Head_Y[7]));
  Pull_Resistor pull_resistor_19 (.node(out_17));
  Pull_Resistor pull_resistor_20 (.node(out_33));
  Pull_Resistor pull_resistor_21 (.node(out_18));
  Pull_Resistor pull_resistor_22 (.node(out_34));
  Line line_9 (
    .Out(out_16), .Smash(Smash), .CLEAR(CLEAR), .HeadOnLine(Head_X), .TailOnLine(Tail_X), .EnT(Tail_Y[8]),
    .EnH(Head_Y[8]));
  Line line_10 (
    .Out(out_17), .Smash(Smash), .CLEAR(CLEAR), .HeadOnLine(Head_X), .TailOnLine(Tail_X), .EnT(Tail_Y[9]),
    .EnH(Head_Y[9]));
  Line line_11 (
    .Out(out_18), .Smash(Smash), .CLEAR(CLEAR), .HeadOnLine(Head_X), .TailOnLine(Tail_X), .EnT(Tail_Y[10]),
    .EnH(Head_Y[10]));
  Line line_12 (
    .Out(out_19), .Smash(Smash), .CLEAR(CLEAR), .HeadOnLine(Head_X), .TailOnLine(Tail_X), .EnT(Tail_Y[11]),
    .EnH(Head_Y[11]));
  Line line_13 (
    .Out(out_20), .Smash(Smash), .CLEAR(CLEAR), .HeadOnLine(Head_X), .TailOnLine(Tail_X), .EnT(Tail_Y[12]),
    .EnH(H12));
  Line line_14 (
    .Out(out_21), .Smash(Smash), .CLEAR(CLEAR), .HeadOnLine(Head_X), .TailOnLine(Tail_X), .EnT(Tail_Y[13]),
    .EnH(H13));
  Line line_15 (
    .Out(out_22), .Smash(Smash), .CLEAR(CLEAR), .HeadOnLine(Head_X), .TailOnLine(Tail_X), .EnT(Tail_Y[14]),
    .EnH(H14));
  Line line_16 (
    .Out(out_23), .Smash(Smash), .CLEAR(CLEAR), .HeadOnLine(Head_X), .TailOnLine(Tail_X), .EnT(Tail_Y[15]),
    .EnH(Head_Y[15]));
  Pull_Resistor pull_resistor_23 (.node(out_19));
  Pull_Resistor pull_resistor_24 (.node(out_35));
  Pull_Resistor pull_resistor_25 (.node(out_20));
  Pull_Resistor pull_resistor_26 (.node(out_36));
  Line line_17 (
    .Out(out_24), .Smash(Smash), .CLEAR(CLEAR), .HeadOnLine(Head_X), .TailOnLine(Tail_X), .EnT(Tail_Y[16]),
    .EnH(Head_Y[16]));
  Line line_18 (
    .Out(out_25), .Smash(Smash), .CLEAR(CLEAR), .HeadOnLine(Head_X), .TailOnLine(Tail_X), .EnT(Tail_Y[17]),
    .EnH(Head_Y[17]));
  Line line_19 (
    .Out(out_26), .Smash(Smash), .CLEAR(CLEAR), .HeadOnLine(Head_X), .TailOnLine(Tail_X), .EnT(Tail_Y[18]),
    .EnH(Head_Y[18]));
  Line line_20 (
    .Out(out_27), .Smash(Smash), .CLEAR(CLEAR), .HeadOnLine(Head_X), .TailOnLine(Tail_X), .EnT(Tail_Y[19]),
    .EnH(Head_Y[19]));
  Line line_21 (
    .Out(out_28), .Smash(Smash), .CLEAR(CLEAR), .HeadOnLine(Head_X), .TailOnLine(Tail_X), .EnT(Tail_Y[20]),
    .EnH(Head_Y[20]));
  Line line_22 (
    .Out(out_29), .Smash(Smash), .CLEAR(CLEAR), .HeadOnLine(Head_X), .TailOnLine(Tail_X), .EnT(Tail_Y[21]),
    .EnH(Head_Y[21]));
  Line line_23 (
    .Out(out_30), .Smash(Smash), .CLEAR(CLEAR), .HeadOnLine(Head_X), .TailOnLine(Tail_X), .EnT(Tail_Y[22]),
    .EnH(Head_Y[22]));
  Line line_24 (
    .Out(out_31), .Smash(Smash), .CLEAR(CLEAR), .HeadOnLine(Head_X), .TailOnLine(Tail_X), .EnT(Tail_Y[23]),
    .EnH(Head_Y[23]));
  Pull_Resistor pull_resistor_27 (.node(Smash));
  Pull_Resistor pull_resistor_28 (.node(out_21));
  Pull_Resistor pull_resistor_29 (.node(out_37));
  Pull_Resistor pull_resistor_30 (.node(out_22));
  Line line_25 (
    .Out(out_32), .Smash(Smash), .CLEAR(CLEAR), .HeadOnLine(Head_X), .TailOnLine(Tail_X), .EnT(Tail_Y[24]),
    .EnH(Head_Y[24]));
  Line line_26 (
    .Out(out_33), .Smash(Smash), .CLEAR(CLEAR), .HeadOnLine(Head_X), .TailOnLine(Tail_X), .EnT(Tail_Y[25]),
    .EnH(Head_Y[25]));
  Line line_27 (
    .Out(out_34), .Smash(Smash), .CLEAR(CLEAR), .HeadOnLine(Head_X), .TailOnLine(Tail_X), .EnT(Tail_Y[26]),
    .EnH(Head_Y[26]));
  Line line_28 (
    .Out(out_35), .Smash(Smash), .CLEAR(CLEAR), .HeadOnLine(Head_X), .TailOnLine(Tail_X), .EnT(Tail_Y[27]),
    .EnH(Head_Y[27]));
  Line line_29 (
    .Out(out_36), .Smash(Smash), .CLEAR(CLEAR), .HeadOnLine(Head_X), .TailOnLine(Tail_X), .EnT(Tail_Y[28]),
    .EnH(Head_Y[28]));
  Line line_30 (
    .Out(out_37), .Smash(Smash), .CLEAR(CLEAR), .HeadOnLine(Head_X), .TailOnLine(Tail_X), .EnT(Tail_Y[29]),
    .EnH(Head_Y[29]));
  Pull_Resistor pull_resistor_31 (.node(out_23));

  // Other names for the same wires on the sheet: H0 = Head_Y[0]; H1 = Head_Y[1]; H2 = Head_Y[2]; H3 = Head_Y[3];
  //   H4 = Head_Y[4]; H5 = Head_Y[5]; H6 = Head_Y[6]; H7 = Head_Y[7]; H8 = Head_Y[8]; H9 = Head_Y[9];
  //   H10 = Head_Y[10]; H11 = Head_Y[11]; H15 = Head_Y[15]; H16 = Head_Y[16]; H17 = Head_Y[17]; H18 = Head_Y[18];
  //   H19 = Head_Y[19]; H20 = Head_Y[20]; H21 = Head_Y[21]; H22 = Head_Y[22]; H23 = Head_Y[23]; H24 = Head_Y[24];
  //   H25 = Head_Y[25]; H26 = Head_Y[26]; H27 = Head_Y[27]; H28 = Head_Y[28]; H29 = Head_Y[29];
  //   HeadOnLine[29:0] = Head_X; O0[29:0] = _0; O1[29:0] = out_9; O2[29:0] = out_10; O3[29:0] = out_11;
  //   O4[29:0] = out_12; O5[29:0] = out_13; O6[29:0] = out_14; O7[29:0] = out_15; O8[29:0] = out_16;
  //   O9[29:0] = out_17; O10[29:0] = out_18; O11[29:0] = out_19; O12[29:0] = out_20; O13[29:0] = out_21;
  //   O14[29:0] = out_22; O15[29:0] = out_23; O16[29:0] = out_24; O17[29:0] = out_25; O18[29:0] = out_26;
  //   O19[29:0] = out_27; O20[29:0] = out_28; O21[29:0] = out_29; O22[29:0] = out_30; O23[29:0] = out_31;
  //   O24[29:0] = out_32; O25[29:0] = out_33; O26[29:0] = out_34; O27[29:0] = out_35; O28[29:0] = out_36;
  //   O29[29:0] = out_37; T0 = Tail_Y[0]; T1 = Tail_Y[1]; T2 = Tail_Y[2]; T3 = Tail_Y[3]; T4 = Tail_Y[4];
  //   T5 = Tail_Y[5]; T6 = Tail_Y[6]; T7 = Tail_Y[7]; T8 = Tail_Y[8]; T9 = Tail_Y[9]; T10 = Tail_Y[10];
  //   T11 = Tail_Y[11]; T12 = Tail_Y[12]; T13 = Tail_Y[13]; T14 = Tail_Y[14]; T15 = Tail_Y[15]; T16 = Tail_Y[16];
  //   T17 = Tail_Y[17]; T18 = Tail_Y[18]; T19 = Tail_Y[19]; T20 = Tail_Y[20]; T21 = Tail_Y[21]; T22 = Tail_Y[22];
  //   T23 = Tail_Y[23]; T24 = Tail_Y[24]; T25 = Tail_Y[25]; T26 = Tail_Y[26]; T27 = Tail_Y[27]; T28 = Tail_Y[28];
  //   T29 = Tail_Y[29]; TailOnLine[29:0] = Tail_X
endmodule

// LINE
module Line (
  input  CLEAR,
  input  EnH,
  input  [29:0] HeadOnLine,
  input  EnT,
  input  [29:0] TailOnLine,
  output [29:0] Out,
  output Smash
);

  wire H0, H1, H2, H3, H4, H5, H6, H7, H8, H9, H10, H11, H12, H13, H14, H15, H16, H17, H18, H19, H20, H21,
       H22, H23, H24, H25, H26, H27, H28, H29, pixel_1_smash, pixel_2_smash, pixel_3_smash, pixel_4_smash,
       pixel_5_smash, pixel_6_smash, pixel_7_smash, pixel_8_smash, pixel_9_smash, pixel_10_smash,
       pixel_11_smash, pixel_12_smash, pixel_13_smash, pixel_14_smash, pixel_15_smash, pixel_16_smash,
       pixel_17_smash, pixel_18_smash, pixel_19_smash, pixel_20_smash, pixel_21_smash, pixel_22_smash,
       pixel_23_smash, pixel_24_smash, pixel_25_smash, pixel_26_smash, pixel_27_smash, pixel_28_smash,
       pixel_29_smash, pixel_30_smash, T0, T1, T2, T3, T4, T5, T6, T7, T8, T9, T10, T11, T12, T13, T14, T15,
       T16, T17, T18, T19, T20, T21, T22, T23, T24, T25, T26, T27, T28, T29;

  pixel pixel_1 (.Up(H0), .Down(T0), .Light(Out[0]), .Smash(pixel_1_smash), .CLEAR(CLEAR));
  assign Smash = H0 ? pixel_1_smash : 1'bz;  // Controlled_Buffer controlled_buffer_1
  pixel pixel_2 (.Up(H16), .Down(T16), .Light(Out[16]), .Smash(pixel_2_smash), .CLEAR(CLEAR));
  assign Smash = H16 ? pixel_2_smash : 1'bz;  // Controlled_Buffer controlled_buffer_2
  assign {H29, H28, H27, H26, H25, H24, H23, H22, H21, H20, H19, H18, H17, H16, H15, H14, H13, H12, H11, H10, H9, H8, H7, H6, H5, H4, H3, H2, H1, H0} = EnH ? HeadOnLine : 30'bz;  // Controlled_Buffer controlled_buffer_3
  assign {T29, T28, T27, T26, T25, T24, T23, T22, T21, T20, T19, T18, T17, T16, T15, T14, T13, T12, T11, T10, T9, T8, T7, T6, T5, T4, T3, T2, T1, T0} = EnT ? TailOnLine : 30'bz;  // Controlled_Buffer controlled_buffer_4
  pixel pixel_3 (.Up(H2), .Down(T2), .Light(Out[2]), .Smash(pixel_3_smash), .CLEAR(CLEAR));
  pixel pixel_4 (.Up(H1), .Down(T1), .Light(Out[1]), .Smash(pixel_4_smash), .CLEAR(CLEAR));
  assign Smash = H1 ? pixel_4_smash : 1'bz;  // Controlled_Buffer controlled_buffer_5
  assign Smash = H2 ? pixel_3_smash : 1'bz;  // Controlled_Buffer controlled_buffer_6
  pixel pixel_5 (.Up(H18), .Down(T18), .Light(Out[18]), .Smash(pixel_5_smash), .CLEAR(CLEAR));
  pixel pixel_6 (.Up(H17), .Down(T17), .Light(Out[17]), .Smash(pixel_6_smash), .CLEAR(CLEAR));
  assign Smash = H18 ? pixel_5_smash : 1'bz;  // Controlled_Buffer controlled_buffer_7
  assign Smash = H17 ? pixel_6_smash : 1'bz;  // Controlled_Buffer controlled_buffer_8
  Pull_Resistor pull_resistor_1 (.node({H29, H28, H27, H26, H25, H24, H23, H22, H21, H20, H19, H18, H17, H16, H15, H14, H13, H12, H11, H10, H9, H8, H7, H6, H5, H4, H3, H2, H1, H0}));
  Pull_Resistor pull_resistor_2 (.node({T29, T28, T27, T26, T25, T24, T23, T22, T21, T20, T19, T18, T17, T16, T15, T14, T13, T12, T11, T10, T9, T8, T7, T6, T5, T4, T3, T2, T1, T0}));
  pixel pixel_7 (.Up(H3), .Down(T3), .Light(Out[3]), .Smash(pixel_7_smash), .CLEAR(CLEAR));
  assign Smash = H3 ? pixel_7_smash : 1'bz;  // Controlled_Buffer controlled_buffer_9
  pixel pixel_8 (.Up(H19), .Down(T19), .Light(Out[19]), .Smash(pixel_8_smash), .CLEAR(CLEAR));
  assign Smash = H19 ? pixel_8_smash : 1'bz;  // Controlled_Buffer controlled_buffer_10
  pixel pixel_9 (.Up(H4), .Down(T4), .Light(Out[4]), .Smash(pixel_9_smash), .CLEAR(CLEAR));
  pixel pixel_10 (.Up(H5), .Down(T5), .Light(Out[5]), .Smash(pixel_10_smash), .CLEAR(CLEAR));
  assign Smash = H5 ? pixel_10_smash : 1'bz;  // Controlled_Buffer controlled_buffer_11
  assign Smash = H4 ? pixel_9_smash : 1'bz;  // Controlled_Buffer controlled_buffer_12
  pixel pixel_11 (.Up(H21), .Down(T21), .Light(Out[21]), .Smash(pixel_11_smash), .CLEAR(CLEAR));
  pixel pixel_12 (.Up(H20), .Down(T20), .Light(Out[20]), .Smash(pixel_12_smash), .CLEAR(CLEAR));
  assign Smash = H20 ? pixel_12_smash : 1'bz;  // Controlled_Buffer controlled_buffer_13
  assign Smash = H21 ? pixel_11_smash : 1'bz;  // Controlled_Buffer controlled_buffer_14
  pixel pixel_13 (.Up(H6), .Down(T6), .Light(Out[6]), .Smash(pixel_13_smash), .CLEAR(CLEAR));
  assign Smash = H6 ? pixel_13_smash : 1'bz;  // Controlled_Buffer controlled_buffer_15
  assign Smash = H7 ? pixel_15_smash : 1'bz;  // Controlled_Buffer controlled_buffer_16
  pixel pixel_14 (.Up(H22), .Down(T22), .Light(Out[22]), .Smash(pixel_14_smash), .CLEAR(CLEAR));
  assign Smash = H22 ? pixel_14_smash : 1'bz;  // Controlled_Buffer controlled_buffer_17
  assign Smash = H23 ? pixel_17_smash : 1'bz;  // Controlled_Buffer controlled_buffer_18
  pixel pixel_15 (.Up(H7), .Down(T7), .Light(Out[7]), .Smash(pixel_15_smash), .CLEAR(CLEAR));
  pixel pixel_16 (.Up(H8), .Down(T8), .Light(Out[8]), .Smash(pixel_16_smash), .CLEAR(CLEAR));
  assign Smash = H8 ? pixel_16_smash : 1'bz;  // Controlled_Buffer controlled_buffer_19
  pixel pixel_17 (.Up(H23), .Down(T23), .Light(Out[23]), .Smash(pixel_17_smash), .CLEAR(CLEAR));
  pixel pixel_18 (.Up(H24), .Down(T24), .Light(Out[24]), .Smash(pixel_18_smash), .CLEAR(CLEAR));
  assign Smash = H24 ? pixel_18_smash : 1'bz;  // Controlled_Buffer controlled_buffer_20
  pixel pixel_19 (.Up(H9), .Down(T9), .Light(Out[9]), .Smash(pixel_19_smash), .CLEAR(CLEAR));
  pixel pixel_20 (.Up(H10), .Down(T10), .Light(Out[10]), .Smash(pixel_20_smash), .CLEAR(CLEAR));
  assign Smash = H10 ? pixel_20_smash : 1'bz;  // Controlled_Buffer controlled_buffer_21
  assign Smash = H9 ? pixel_19_smash : 1'bz;  // Controlled_Buffer controlled_buffer_22
  pixel pixel_21 (.Up(H26), .Down(T26), .Light(Out[26]), .Smash(pixel_21_smash), .CLEAR(CLEAR));
  pixel pixel_22 (.Up(H25), .Down(T25), .Light(Out[25]), .Smash(pixel_22_smash), .CLEAR(CLEAR));
  assign Smash = H26 ? pixel_21_smash : 1'bz;  // Controlled_Buffer controlled_buffer_23
  assign Smash = H25 ? pixel_22_smash : 1'bz;  // Controlled_Buffer controlled_buffer_24
  pixel pixel_23 (.Up(H11), .Down(T11), .Light(Out[11]), .Smash(pixel_23_smash), .CLEAR(CLEAR));
  assign Smash = H11 ? pixel_23_smash : 1'bz;  // Controlled_Buffer controlled_buffer_25
  pixel pixel_24 (.Up(H27), .Down(T27), .Light(Out[27]), .Smash(pixel_24_smash), .CLEAR(CLEAR));
  assign Smash = H27 ? pixel_24_smash : 1'bz;  // Controlled_Buffer controlled_buffer_26
  pixel pixel_25 (.Up(H12), .Down(T12), .Light(Out[12]), .Smash(pixel_25_smash), .CLEAR(CLEAR));
  pixel pixel_26 (.Up(H13), .Down(T13), .Light(Out[13]), .Smash(pixel_26_smash), .CLEAR(CLEAR));
  assign Smash = H12 ? pixel_25_smash : 1'bz;  // Controlled_Buffer controlled_buffer_27
  assign Smash = H13 ? pixel_26_smash : 1'bz;  // Controlled_Buffer controlled_buffer_28
  pixel pixel_27 (.Up(H29), .Down(T29), .Light(Out[29]), .Smash(pixel_27_smash), .CLEAR(CLEAR));
  pixel pixel_28 (.Up(H28), .Down(T28), .Light(Out[28]), .Smash(pixel_28_smash), .CLEAR(CLEAR));
  assign Smash = H29 ? pixel_27_smash : 1'bz;  // Controlled_Buffer controlled_buffer_29
  assign Smash = H28 ? pixel_28_smash : 1'bz;  // Controlled_Buffer controlled_buffer_30
  pixel pixel_29 (.Up(H14), .Down(T14), .Light(Out[14]), .Smash(pixel_29_smash), .CLEAR(CLEAR));
  assign Smash = H15 ? pixel_30_smash : 1'bz;  // Controlled_Buffer controlled_buffer_31
  assign Smash = H14 ? pixel_29_smash : 1'bz;  // Controlled_Buffer controlled_buffer_32
  pixel pixel_30 (.Up(H15), .Down(T15), .Light(Out[15]), .Smash(pixel_30_smash), .CLEAR(CLEAR));

  // Other names for the same wires on the sheet: L0 = Out[0]; L1 = Out[1]; L2 = Out[2]; L3 = Out[3]; L4 = Out[4];
  //   L5 = Out[5]; L6 = Out[6]; L7 = Out[7]; L8 = Out[8]; L9 = Out[9]; L10 = Out[10]; L11 = Out[11]; L12 = Out[12];
  //   L13 = Out[13]; L14 = Out[14]; L15 = Out[15]; L16 = Out[16]; L17 = Out[17]; L18 = Out[18]; L19 = Out[19];
  //   L20 = Out[20]; L21 = Out[21]; L22 = Out[22]; L23 = Out[23]; L24 = Out[24]; L25 = Out[25]; L26 = Out[26];
  //   L27 = Out[27]; L28 = Out[28]; L29 = Out[29]
endmodule

// Pix
module pixel (
  input  CLEAR,
  input  Up,
  input  Down,
  output Light,
  output Smash
);

  wire and_2_out, or_1_out, Visited;

  D_Flip_Flop d_ff_1 (.clk(Up), .D(1'b1), .Q(Light), .reset(or_1_out));  // open: Qn, preset, en
  and and_1 (Smash, Visited, Up);
  or or_1 (or_1_out, and_2_out, CLEAR);
  and and_2 (and_2_out, ~Up, Down);  // AND_Gate
  D_Flip_Flop #(.trigger("falling")) d_ff_2 (
    .clk(Up), .D(1'b1), .Q(Visited), .reset(or_1_out));  // open: Qn, preset, en
endmodule

module Keyboard (
  input  GameClock,
  input  START,
  input  [6:0] In,
  output [1:0] Where,
  output D,
  output S,
  output A,
  output W
);

  wire or_1_out;
  wire [1:0] bitshrink_1_where;

  bitShrink bitshrink_1 (.In(In), .W(W), .A(A), .S(S), .D(D), .Where(bitshrink_1_where));
  Register #(.width(2)) register_1 (.D(bitshrink_1_where), .Q(Where), .clk(or_1_out), .clr(START));  // open: en
  or or_1 (or_1_out, W, A, S, D);
endmodule

module bitShrink (
  input  [6:0] In,
  output W,
  output A,
  output [1:0] Where,
  output S,
  output D
);

  wire [6:0] xnor_1_out, xnor_2_out, xnor_3_out, xnor_4_out;

  // Probe on 7'b1110111
  // Probe on 7'b1100001
  // Probe on 7'b1110011
  // Probe on 7'b1100100
  assign xnor_1_out = ~(In ^ 7'b1110111);  // XNOR_Gate xnor_1, 7 bits wide
  assign xnor_2_out = ~(In ^ 7'b1100001);  // XNOR_Gate xnor_2, 7 bits wide
  assign xnor_3_out = ~(In ^ 7'b1110011);  // XNOR_Gate xnor_3, 7 bits wide
  assign xnor_4_out = ~(In ^ 7'b1100100);  // XNOR_Gate xnor_4, 7 bits wide
  and and_1 (W, xnor_1_out[0], xnor_1_out[1], xnor_1_out[2], xnor_1_out[3], xnor_1_out[4], xnor_1_out[5], xnor_1_out[6]);
  and and_2 (A, xnor_2_out[0], xnor_2_out[1], xnor_2_out[2], xnor_2_out[3], xnor_2_out[4], xnor_2_out[5], xnor_2_out[6]);
  and and_3 (S, xnor_3_out[0], xnor_3_out[1], xnor_3_out[2], xnor_3_out[3], xnor_3_out[4], xnor_3_out[5], xnor_3_out[6]);
  and and_4 (D, xnor_4_out[0], xnor_4_out[1], xnor_4_out[2], xnor_4_out[3], xnor_4_out[4], xnor_4_out[5], xnor_4_out[6]);
  assign Where = W ? 2'b00 : 2'bz;  // Controlled_Buffer controlled_buffer_1
  assign Where = A ? 2'b01 : 2'bz;  // Controlled_Buffer controlled_buffer_2
  assign Where = S ? 2'b10 : 2'bz;  // Controlled_Buffer controlled_buffer_3
  assign Where = D ? 2'b11 : 2'bz;  // Controlled_Buffer controlled_buffer_4
  Pull_Resistor pull_resistor_1 (.node(Where));
endmodule

// APPLES
module Apples (
  input  [29:0] in_1,
  input  [29:0] in_2,
  input  NewApple,
  input  Clock,
  input  [29:0] in_5,
  input  [29:0] in_6,
  input  GameOver,
  input  [29:0] in_8,
  input  [29:0] in_9,
  input  [29:0] in_10,
  input  [29:0] in_11,
  input  [29:0] in_12,
  input  [29:0] in_13,
  input  [29:0] in_14,
  input  [29:0] in_15,
  input  [29:0] in_16,
  input  [29:0] in_17,
  input  [29:0] in_18,
  input  [29:0] in_19,
  input  [29:0] in_20,
  input  [29:0] in_21,
  input  [29:0] in_22,
  input  [29:0] in_23,
  input  [29:0] in_24,
  input  [29:0] in_25,
  input  [29:0] in_26,
  input  [29:0] in_27,
  input  [29:0] in_28,
  input  [29:0] in_29,
  input  [29:0] in_30,
  input  [29:0] in_31,
  input  [29:0] in_32,
  input  [29:0] in_33,
  output [31:0] out_34,
  output [31:0] out_35,
  output [31:0] out_36,
  output [31:0] out_37,
  output [31:0] out_38,
  output [31:0] out_39,
  output [31:0] out_40,
  output [31:0] out_41,
  output [31:0] out_42,
  output [31:0] out_43,
  output [31:0] out_44,
  output [31:0] out_45,
  output [31:0] out_46,
  output [31:0] out_47,
  output [31:0] out_48,
  output [31:0] out_49,
  output [31:0] out_50,
  output [31:0] out_51,
  output [31:0] out_52,
  output [31:0] out_53,
  output [31:0] out_54,
  output [31:0] out_55,
  output [31:0] out_56,
  output [31:0] out_57,
  output [31:0] out_58,
  output [31:0] out_59,
  output [31:0] out_60,
  output [31:0] out_61,
  output [31:0] out_62,
  output [31:0] out_63,
  output EnApple,
  output [31:0] out_65,
  output [31:0] out_66,
  output [29:0] Apple_Y,
  output [29:0] Apple_X
);

  wire Clock_t, counter_1_carry, Intersect, or_1_out, or_2_out, or_3_out, or_4_out, Working;
  wire [4:0] random_1_out, random_2_out;
  wire [29:0] and_2_out, Apple_X_t, Apple_Y_t, ChosenLine, controlled_buffer_31_out;

  and and_1 (Clock_t, Clock, Working);
  assign ChosenLine = Apple_Y_t[0] ? in_1 : 30'bz;  // Controlled_Buffer controlled_buffer_1
  assign ChosenLine = Apple_Y_t[1] ? in_5 : 30'bz;  // Controlled_Buffer controlled_buffer_2
  assign ChosenLine = Apple_Y_t[2] ? in_8 : 30'bz;  // Controlled_Buffer controlled_buffer_3
  assign ChosenLine = Apple_Y_t[3] ? in_10 : 30'bz;  // Controlled_Buffer controlled_buffer_4
  assign ChosenLine = Apple_Y_t[4] ? in_12 : 30'bz;  // Controlled_Buffer controlled_buffer_5
  assign ChosenLine = Apple_Y_t[5] ? in_14 : 30'bz;  // Controlled_Buffer controlled_buffer_6
  assign ChosenLine = Apple_Y_t[6] ? in_16 : 30'bz;  // Controlled_Buffer controlled_buffer_7
  assign ChosenLine = Apple_Y_t[7] ? in_18 : 30'bz;  // Controlled_Buffer controlled_buffer_8
  assign ChosenLine = Apple_Y_t[8] ? in_20 : 30'bz;  // Controlled_Buffer controlled_buffer_9
  assign ChosenLine = Apple_Y_t[9] ? in_22 : 30'bz;  // Controlled_Buffer controlled_buffer_10
  assign ChosenLine = Apple_Y_t[10] ? in_24 : 30'bz;  // Controlled_Buffer controlled_buffer_11
  assign ChosenLine = Apple_Y_t[11] ? in_26 : 30'bz;  // Controlled_Buffer controlled_buffer_12
  assign ChosenLine = Apple_Y_t[12] ? in_28 : 30'bz;  // Controlled_Buffer controlled_buffer_13
  assign ChosenLine = Apple_Y_t[13] ? in_30 : 30'bz;  // Controlled_Buffer controlled_buffer_14
  assign ChosenLine = Apple_Y_t[14] ? in_32 : 30'bz;  // Controlled_Buffer controlled_buffer_15
  assign ChosenLine = Apple_Y_t[15] ? in_2 : 30'bz;  // Controlled_Buffer controlled_buffer_16
  Counter #(.width(4), .max('hf)) counter_1 (.carry(counter_1_carry), .clk(Intersect));  // open: load, D, count, Q, clr
  or or_1 (or_1_out, NewApple, Intersect);
  or or_2 (or_2_out, NewApple, counter_1_carry);
  assign and_2_out = Apple_X_t & ChosenLine;  // AND_Gate and_2, 30 bits wide
  D_Flip_Flop #(.trigger("falling")) d_ff_1 (
    .clk(NewApple), .D(1'b1), .Q(Working), .reset(EnApple));  // open: Qn, preset, en
  assign ChosenLine = Apple_Y_t[16] ? in_6 : 30'bz;  // Controlled_Buffer controlled_buffer_17
  assign ChosenLine = Apple_Y_t[17] ? in_9 : 30'bz;  // Controlled_Buffer controlled_buffer_18
  assign ChosenLine = Apple_Y_t[18] ? in_11 : 30'bz;  // Controlled_Buffer controlled_buffer_19
  assign ChosenLine = Apple_Y_t[19] ? in_13 : 30'bz;  // Controlled_Buffer controlled_buffer_20
  assign ChosenLine = Apple_Y_t[20] ? in_15 : 30'bz;  // Controlled_Buffer controlled_buffer_21
  assign ChosenLine = Apple_Y_t[21] ? in_17 : 30'bz;  // Controlled_Buffer controlled_buffer_22
  assign ChosenLine = Apple_Y_t[22] ? in_19 : 30'bz;  // Controlled_Buffer controlled_buffer_23
  assign ChosenLine = Apple_Y_t[23] ? in_21 : 30'bz;  // Controlled_Buffer controlled_buffer_24
  assign ChosenLine = Apple_Y_t[24] ? in_23 : 30'bz;  // Controlled_Buffer controlled_buffer_25
  assign ChosenLine = Apple_Y_t[25] ? in_25 : 30'bz;  // Controlled_Buffer controlled_buffer_26
  assign ChosenLine = Apple_Y_t[26] ? in_27 : 30'bz;  // Controlled_Buffer controlled_buffer_27
  assign ChosenLine = Apple_Y_t[27] ? in_29 : 30'bz;  // Controlled_Buffer controlled_buffer_28
  assign ChosenLine = Apple_Y_t[28] ? in_31 : 30'bz;  // Controlled_Buffer controlled_buffer_29
  assign ChosenLine = Apple_Y_t[29] ? in_33 : 30'bz;  // Controlled_Buffer controlled_buffer_30
  Pull_Resistor pull_resistor_1 (.node(ChosenLine));
  Random #(.width(5)) random_1 (.clk(or_1_out), .out(random_1_out));  // open: next, clr
  Random #(.width(5)) random_2 (.clk(or_2_out), .out(random_2_out));  // open: next, clr
  Shifter #(.width(30), .shift("rl")) shifter_1 (.in(30'h1), .\dist (random_1_out), .out(Apple_X_t));
  Shifter #(.width(30), .shift("rl")) shifter_2 (.in(30'h1), .\dist (random_2_out), .out(Apple_Y_t));
  assign controlled_buffer_31_out = EnApple ? Apple_X_t : 30'bz;  // Controlled_Buffer controlled_buffer_31
  Counter #(.width(3), .max('h7), .ongoal("stay")) counter_2 (
    .carry(EnApple), .clk(Clock_t), .clr(or_3_out));  // open: load, D, count, Q
  or or_3 (or_3_out, Intersect, GameOver, NewApple);
  or or_4 (or_4_out, and_2_out[0], and_2_out[1], and_2_out[2], and_2_out[3], and_2_out[4], and_2_out[5], and_2_out[6], and_2_out[7], and_2_out[8], and_2_out[9], and_2_out[10], and_2_out[11], and_2_out[12], and_2_out[13], and_2_out[14], and_2_out[15], and_2_out[16], and_2_out[17], and_2_out[18], and_2_out[19], and_2_out[20], and_2_out[21], and_2_out[22], and_2_out[23], and_2_out[24], and_2_out[25], and_2_out[26], and_2_out[27], and_2_out[28], and_2_out[29]);
  assign out_36[30:1] = Apple_Y_t[0] ? controlled_buffer_31_out : 30'bz;  // Controlled_Buffer controlled_buffer_32
  Pull_Resistor pull_resistor_2 (.node(out_36[30:1]));
  assign out_38[30:1] = Apple_Y_t[1] ? controlled_buffer_31_out : 30'bz;  // Controlled_Buffer controlled_buffer_33
  Pull_Resistor pull_resistor_3 (.node(out_38[30:1]));
  assign out_40[30:1] = Apple_Y_t[2] ? controlled_buffer_31_out : 30'bz;  // Controlled_Buffer controlled_buffer_34
  Pull_Resistor pull_resistor_4 (.node(out_40[30:1]));
  assign out_42[30:1] = Apple_Y_t[3] ? controlled_buffer_31_out : 30'bz;  // Controlled_Buffer controlled_buffer_35
  Pull_Resistor pull_resistor_5 (.node(out_42[30:1]));
  assign out_44[30:1] = Apple_Y_t[4] ? controlled_buffer_31_out : 30'bz;  // Controlled_Buffer controlled_buffer_36
  Pull_Resistor pull_resistor_6 (.node(out_44[30:1]));
  Pull_Resistor pull_resistor_7 (.node(out_46[30:1]));
  assign out_46[30:1] = Apple_Y_t[5] ? controlled_buffer_31_out : 30'bz;  // Controlled_Buffer controlled_buffer_37
  Pull_Resistor pull_resistor_8 (.node(out_48[30:1]));
  assign out_48[30:1] = Apple_Y_t[6] ? controlled_buffer_31_out : 30'bz;  // Controlled_Buffer controlled_buffer_38
  Pull_Resistor pull_resistor_9 (.node(out_50[30:1]));
  assign out_50[30:1] = Apple_Y_t[7] ? controlled_buffer_31_out : 30'bz;  // Controlled_Buffer controlled_buffer_39
  assign out_52[30:1] = Apple_Y_t[8] ? controlled_buffer_31_out : 30'bz;  // Controlled_Buffer controlled_buffer_40
  Pull_Resistor pull_resistor_10 (.node(out_52[30:1]));
  Pull_Resistor pull_resistor_11 (.node(out_54[30:1]));
  assign out_54[30:1] = Apple_Y_t[9] ? controlled_buffer_31_out : 30'bz;  // Controlled_Buffer controlled_buffer_41
  Pull_Resistor pull_resistor_12 (.node(out_56[30:1]));
  assign out_56[30:1] = Apple_Y_t[10] ? controlled_buffer_31_out : 30'bz;  // Controlled_Buffer controlled_buffer_42
  Pull_Resistor pull_resistor_13 (.node(out_58[30:1]));
  assign out_58[30:1] = Apple_Y_t[11] ? controlled_buffer_31_out : 30'bz;  // Controlled_Buffer controlled_buffer_43
  assign out_60[30:1] = Apple_Y_t[12] ? controlled_buffer_31_out : 30'bz;  // Controlled_Buffer controlled_buffer_44
  Pull_Resistor pull_resistor_14 (.node(out_60[30:1]));
  assign out_62[30:1] = Apple_Y_t[13] ? controlled_buffer_31_out : 30'bz;  // Controlled_Buffer controlled_buffer_45
  Pull_Resistor pull_resistor_15 (.node(out_62[30:1]));
  Pull_Resistor pull_resistor_16 (.node(out_35[30:1]));
  assign out_35[30:1] = Apple_Y_t[14] ? controlled_buffer_31_out : 30'bz;  // Controlled_Buffer controlled_buffer_46
  Pull_Resistor pull_resistor_17 (.node(out_37[30:1]));
  assign out_37[30:1] = Apple_Y_t[15] ? controlled_buffer_31_out : 30'bz;  // Controlled_Buffer controlled_buffer_47
  and and_3 (Intersect, Clock_t, or_4_out);
  Pull_Resistor pull_resistor_18 (.node(out_39[30:1]));
  assign out_39[30:1] = Apple_Y_t[16] ? controlled_buffer_31_out : 30'bz;  // Controlled_Buffer controlled_buffer_48
  Pull_Resistor pull_resistor_19 (.node(out_41[30:1]));
  assign out_41[30:1] = Apple_Y_t[17] ? controlled_buffer_31_out : 30'bz;  // Controlled_Buffer controlled_buffer_49
  assign out_43[30:1] = Apple_Y_t[18] ? controlled_buffer_31_out : 30'bz;  // Controlled_Buffer controlled_buffer_50
  Pull_Resistor pull_resistor_20 (.node(out_43[30:1]));
  assign out_45[30:1] = Apple_Y_t[19] ? controlled_buffer_31_out : 30'bz;  // Controlled_Buffer controlled_buffer_51
  Pull_Resistor pull_resistor_21 (.node(out_45[30:1]));
  assign out_47[30:1] = Apple_Y_t[20] ? controlled_buffer_31_out : 30'bz;  // Controlled_Buffer controlled_buffer_52
  Pull_Resistor pull_resistor_22 (.node(out_47[30:1]));
  Pull_Resistor pull_resistor_23 (.node(out_49[30:1]));
  assign out_49[30:1] = Apple_Y_t[21] ? controlled_buffer_31_out : 30'bz;  // Controlled_Buffer controlled_buffer_53
  assign out_51[30:1] = Apple_Y_t[22] ? controlled_buffer_31_out : 30'bz;  // Controlled_Buffer controlled_buffer_54
  Pull_Resistor pull_resistor_24 (.node(out_51[30:1]));
  assign out_53[30:1] = Apple_Y_t[23] ? controlled_buffer_31_out : 30'bz;  // Controlled_Buffer controlled_buffer_55
  Pull_Resistor pull_resistor_25 (.node(out_53[30:1]));
  Pull_Resistor pull_resistor_26 (.node(out_55[30:1]));
  assign out_55[30:1] = Apple_Y_t[24] ? controlled_buffer_31_out : 30'bz;  // Controlled_Buffer controlled_buffer_56
  assign out_57[30:1] = Apple_Y_t[25] ? controlled_buffer_31_out : 30'bz;  // Controlled_Buffer controlled_buffer_57
  Pull_Resistor pull_resistor_27 (.node(out_57[30:1]));
  Pull_Resistor pull_resistor_28 (.node(out_59[30:1]));
  assign out_59[30:1] = Apple_Y_t[26] ? controlled_buffer_31_out : 30'bz;  // Controlled_Buffer controlled_buffer_58
  assign out_61[30:1] = Apple_Y_t[27] ? controlled_buffer_31_out : 30'bz;  // Controlled_Buffer controlled_buffer_59
  Pull_Resistor pull_resistor_29 (.node(out_61[30:1]));
  assign out_63[30:1] = Apple_Y_t[28] ? controlled_buffer_31_out : 30'bz;  // Controlled_Buffer controlled_buffer_60
  Pull_Resistor pull_resistor_30 (.node(out_63[30:1]));
  Pull_Resistor pull_resistor_31 (.node(out_65[30:1]));
  assign out_65[30:1] = Apple_Y_t[29] ? controlled_buffer_31_out : 30'bz;  // Controlled_Buffer controlled_buffer_61
  Register #(.width(30)) register_1 (.D(Apple_Y_t), .Q(Apple_Y), .clk(EnApple), .clr(GameOver));  // open: en
  Register #(.width(30)) register_2 (.D(Apple_X_t), .Q(Apple_X), .clk(EnApple), .clr(GameOver));  // open: en

  assign out_34 = {32{1'b1}};
  assign {out_35[31], out_35[0]} = 2'b11;
  assign {out_36[31], out_36[0]} = 2'b11;
  assign {out_37[31], out_37[0]} = 2'b11;
  assign {out_38[31], out_38[0]} = 2'b11;
  assign {out_39[31], out_39[0]} = 2'b11;
  assign {out_40[31], out_40[0]} = 2'b11;
  assign {out_41[31], out_41[0]} = 2'b11;
  assign {out_42[31], out_42[0]} = 2'b11;
  assign {out_43[31], out_43[0]} = 2'b11;
  assign {out_44[31], out_44[0]} = 2'b11;
  assign {out_45[31], out_45[0]} = 2'b11;
  assign {out_46[31], out_46[0]} = 2'b11;
  assign {out_47[31], out_47[0]} = 2'b11;
  assign {out_48[31], out_48[0]} = 2'b11;
  assign {out_49[31], out_49[0]} = 2'b11;
  assign {out_50[31], out_50[0]} = 2'b11;
  assign {out_51[31], out_51[0]} = 2'b11;
  assign {out_52[31], out_52[0]} = 2'b11;
  assign {out_53[31], out_53[0]} = 2'b11;
  assign {out_54[31], out_54[0]} = 2'b11;
  assign {out_55[31], out_55[0]} = 2'b11;
  assign {out_56[31], out_56[0]} = 2'b11;
  assign {out_57[31], out_57[0]} = 2'b11;
  assign {out_58[31], out_58[0]} = 2'b11;
  assign {out_59[31], out_59[0]} = 2'b11;
  assign {out_60[31], out_60[0]} = 2'b11;
  assign {out_61[31], out_61[0]} = 2'b11;
  assign {out_62[31], out_62[0]} = 2'b11;
  assign {out_63[31], out_63[0]} = 2'b11;
  assign {out_65[31], out_65[0]} = 2'b11;
  assign out_66 = {32{1'b1}};

  // Other names for the same wires on the sheet: EnL1 = Apple_Y_t[0]; EnL2 = Apple_Y_t[1]; EnL3 = Apple_Y_t[2];
  //   EnL4 = Apple_Y_t[3]; EnL5 = Apple_Y_t[4]; EnL6 = Apple_Y_t[5]; EnL7 = Apple_Y_t[6]; EnL8 = Apple_Y_t[7];
  //   EnL9 = Apple_Y_t[8]; EnL10 = Apple_Y_t[9]; EnL11 = Apple_Y_t[10]; EnL12 = Apple_Y_t[11]; EnL13 = Apple_Y_t[12];
  //   EnL14 = Apple_Y_t[13]; EnL15 = Apple_Y_t[14]; EnL16 = Apple_Y_t[15]; EnL17 = Apple_Y_t[16];
  //   EnL18 = Apple_Y_t[17]; EnL19 = Apple_Y_t[18]; EnL20 = Apple_Y_t[19]; EnL21 = Apple_Y_t[20];
  //   EnL22 = Apple_Y_t[21]; EnL23 = Apple_Y_t[22]; EnL24 = Apple_Y_t[23]; EnL25 = Apple_Y_t[24];
  //   EnL26 = Apple_Y_t[25]; EnL27 = Apple_Y_t[26]; EnL28 = Apple_Y_t[27]; EnL29 = Apple_Y_t[28];
  //   EnL30 = Apple_Y_t[29]; In1[29:0] = in_1; In2[29:0] = in_5; In3[29:0] = in_8; In4[29:0] = in_10;
  //   In5[29:0] = in_12; In6[29:0] = in_14; In7[29:0] = in_16; In8[29:0] = in_18; In9[29:0] = in_20;
  //   In10[29:0] = in_22; In11[29:0] = in_24; In12[29:0] = in_26; In13[29:0] = in_28; In14[29:0] = in_30;
  //   In15[29:0] = in_32; In16[29:0] = in_2; In17[29:0] = in_6; In18[29:0] = in_9; In19[29:0] = in_11;
  //   In20[29:0] = in_13; In21[29:0] = in_15; In22[29:0] = in_17; In23[29:0] = in_19; In24[29:0] = in_21;
  //   In25[29:0] = in_23; In26[29:0] = in_25; In27[29:0] = in_27; In28[29:0] = in_29; In29[29:0] = in_31;
  //   In30[29:0] = in_33; Out16[29:0] = out_35[30:1]; Out2[29:0] = out_36[30:1]; Out17[29:0] = out_37[30:1];
  //   Out3[29:0] = out_38[30:1]; Out18[29:0] = out_39[30:1]; Out4[29:0] = out_40[30:1]; Out19[29:0] = out_41[30:1];
  //   Out5[29:0] = out_42[30:1]; Out20[29:0] = out_43[30:1]; Out6[29:0] = out_44[30:1]; Out21[29:0] = out_45[30:1];
  //   Out7[29:0] = out_46[30:1]; Out22[29:0] = out_47[30:1]; Out8[29:0] = out_48[30:1]; Out23[29:0] = out_49[30:1];
  //   Out9[29:0] = out_50[30:1]; Out24[29:0] = out_51[30:1]; Out10[29:0] = out_52[30:1]; Out25[29:0] = out_53[30:1];
  //   Out11[29:0] = out_54[30:1]; Out26[29:0] = out_55[30:1]; Out12[29:0] = out_56[30:1]; Out27[29:0] = out_57[30:1];
  //   Out13[29:0] = out_58[30:1]; Out28[29:0] = out_59[30:1]; Out14[29:0] = out_60[30:1]; Out29[29:0] = out_61[30:1];
  //   Out15[29:0] = out_62[30:1]; Out30[29:0] = out_63[30:1]; Out31[29:0] = out_65[30:1]

  // Notes on the sheet:
  //   Input Lines
  //   Random generation of apple position
  //   Apple have been spawned
  //   Output Lines
  //   Checking for spawn inside the snake
endmodule

module ClManager (
  input  EnG,
  input  GameOver,
  input  ProcWorks,
  input  START,
  input  Pause,
  input  Clock,
  output GameCl,
  output ProcCl
);

  wire counter_1_carry, counter_2_carry, counter_3_carry, or_2_out;

  Counter #(.width(1), .max('h1), .trigger("falling")) counter_1 (
    .carry(counter_1_carry), .clk(Clock));  // open: load, D, count, Q, clr
  Counter #(.width(1), .max('h1)) counter_2 (.carry(counter_2_carry), .clk(Clock));  // open: load, D, count, Q, clr
  or or_1 (ProcCl, counter_2_carry, counter_1_carry);
  Counter #(.width(12), .max('h70)) counter_3 (
    .carry(counter_3_carry), .clk(Clock), .clr(START));  // open: load, D, count, Q
  or or_2 (or_2_out, Pause, ProcWorks, GameOver);
  and and_1 (GameCl, counter_3_carry, EnG, ~or_2_out);  // AND_Gate
endmodule

module Eq30 (
  input  [29:0] A,
  input  [29:0] B,
  output Eq
);

  wire [29:0] xnor_1_out;

  assign xnor_1_out = ~(A ^ B);  // XNOR_Gate xnor_1, 30 bits wide
  and and_1 (Eq, xnor_1_out[0], xnor_1_out[1], xnor_1_out[2], xnor_1_out[3], xnor_1_out[4], xnor_1_out[5], xnor_1_out[6], xnor_1_out[7], xnor_1_out[8], xnor_1_out[9], xnor_1_out[10], xnor_1_out[11], xnor_1_out[12], xnor_1_out[13], xnor_1_out[14], xnor_1_out[15], xnor_1_out[16], xnor_1_out[17], xnor_1_out[18], xnor_1_out[19], xnor_1_out[20], xnor_1_out[21], xnor_1_out[22], xnor_1_out[23], xnor_1_out[24], xnor_1_out[25], xnor_1_out[26], xnor_1_out[27], xnor_1_out[28], xnor_1_out[29]);
endmodule

module Eq4 (
  input  [3:0] A,
  input  [3:0] B,
  output Eq
);

  wire [3:0] xnor_1_out;

  assign xnor_1_out = ~(A ^ B);  // XNOR_Gate xnor_1, 4 bits wide
  and and_1 (Eq, xnor_1_out[0], xnor_1_out[1], xnor_1_out[2], xnor_1_out[3]);
endmodule
