// Logisim project additional.circ as structural Verilog: 2 circuits, main circuit ScoreDisplayDriver
module ScoreDisplayDriver (
  input  [7:0] in_1,
  output [3:0] out_2,
  output [3:0] out_3
);

  wire [7:4] divider_1_out, divider_1_rem;

  Divider divider_1 (.a(in_1), .b(8'ha), .out({divider_1_out, out_2}), .rem({divider_1_rem, out_3}));  // open: upper
endmodule

module map_store (
  input  Permissive_entry,
  input  ResetAdr,
  input  map_clock,
  input  [1:0] map_num,
  output [29:0] Line,
  output [29:0] Data,
  output End
);

  wire and_1_out, power_map_1, power_map_2, power_map_3, power_map_4;
  wire [4:0] counter_1_q;
  wire [29:0] shifter_1_out;

  Counter #(.width(5), .max('h1d), .ongoal("stay")) counter_1 (
    .Q(counter_1_q), .carry(End), .clk(and_1_out), .clr(ResetAdr));  // open: load, D, count
  and and_1 (and_1_out, Permissive_entry, map_clock);
  Shifter #(.width(30)) shifter_1 (.in(30'h1), .\dist (counter_1_q), .out(shifter_1_out));
  Pull_Resistor pull_resistor_1 (.node(Line));
  assign Line = Permissive_entry ? shifter_1_out : 30'bz;  // Controlled_Buffer controlled_buffer_1
  ROM #(.addrWidth(5), .dataWidth(30)) rom_1 (.addr(counter_1_q), .data(Data), .sel(power_map_1));
  ROM #(.addrWidth(5), .dataWidth(30)) rom_2 (.addr(counter_1_q), .data(Data), .sel(power_map_2));
  Pull_Resistor pull_resistor_2 (.node(Data));
  ROM #(.addrWidth(5), .dataWidth(30)) rom_3 (.addr(counter_1_q), .data(Data), .sel(power_map_3));
  ROM #(.addrWidth(5), .dataWidth(30)) rom_4 (.addr(counter_1_q), .data(Data), .sel(power_map_4));
  Decoder #(.select(2), .disabled(0)) decoder_1 (
    .out0(power_map_1), .out1(power_map_2), .out2(power_map_3), .out3(power_map_4), .sel(map_num),
    .en(Permissive_entry));

  // Notes on the sheet:
  //   contents of rom_1 (hex, n*v repeats v):
  //   11111111 28*10000001
  //   contents of rom_2 (hex, n*v repeats v):
  //   28*0 123 0 0 123
endmodule
