// Logisim project main.circ as structural Verilog: 11 circuits, main circuit Main
module Main (
  input  getApple
);

  wire A, AddPartToQ, and_2_out, and_4_out, and_6_out, and_9_out, and_10_out, cdm_8_mark5_1_p1,
       cdm_8_mark5_1_p2, cdm_8_mark5_1_p4, cdm_8_mark5_1_p5, cdm_8_mark5_1_p6, cdm_8_mark5_1_p7,
       cdm_8_mark5_1_p8, CI, code, counter_1_carry, counter_2_carry, counter_3_carry, counter_4_carry,
       counter_6_carry, D, d_ff_1_q, d_ff_3_q, data, decoder_3_out0, decoder_3_out1, DownT, EnG, EnTurn,
       GameClock, GameOver, GetScore, I_Oadr, I_Osel, in_out_prime, KeyboardClock, LeftT, LoadPartToProc,
       LoadPartToTail, nand_1_out, not_1_out, not_2_out, not_3_out, not_4_out, not_5_out, not_6_out,
       not_7_out, not_8_out, not_9_out, not_10_out, or_1_out, or_3_out, or_4_out, or_6_out, or_7_out,
       or_8_out, Pause, ProcGotPart, ProcWork, RAM, RightT, S, Smash, START, TailWait, Turn, UpT, W;
  wire [1:0] keyboard_2_where, register_3_q, Where;
  wire [4:0] CurrLength, CurrPart, xnor_1_out, xnor_2_out;
  wire [5:5] and_12_out;
  wire [6:0] controlled_buffer_1_out, keyboard_1_data;
  wire [7:0] cdm_8_mark5_1_p11, cdm_8_mark5_1_p12, I_Odat, register_2_q;
  wire [7:1] cdm_8_mark5_1_p10;
  wire [29:0] head_1_head_x, head_1_head_y, tail_1_tail_x, tail_1_tail_y, tomatrix_1__0, tomatrix_1_out_9,
       tomatrix_1_out_10, tomatrix_1_out_11, tomatrix_1_out_12, tomatrix_1_out_13, tomatrix_1_out_14,
       tomatrix_1_out_15, tomatrix_1_out_16, tomatrix_1_out_17, tomatrix_1_out_18, tomatrix_1_out_19,
       tomatrix_1_out_20, tomatrix_1_out_21, tomatrix_1_out_22, tomatrix_1_out_23, tomatrix_1_out_24,
       tomatrix_1_out_25, tomatrix_1_out_26, tomatrix_1_out_27, tomatrix_1_out_28, tomatrix_1_out_29,
       tomatrix_1_out_30, tomatrix_1_out_31, tomatrix_1_out_32, tomatrix_1_out_33, tomatrix_1_out_34,
       tomatrix_1_out_35, tomatrix_1_out_36, tomatrix_1_out_37;

  Clock clock_1 (.out(KeyboardClock));
  Keyboard_part #(.buflen(1)) keyboard_1 (.clk(KeyboardClock), .clr(START), .data(keyboard_1_data));  // open: re, avail
  D_Flip_Flop #(.trigger("falling")) d_ff_1 (.Q(d_ff_1_q), .preset(Turn), .reset(or_1_out));  // open: clk, D, Qn, en
  or or_1 (or_1_out, START, GameClock);
  // Probe on cdm_8_mark5_1_p5
  // Probe on cdm_8_mark5_1_p4
  // Probe on cdm_8_mark5_1_p2
  // Probe on cdm_8_mark5_1_p1
  Counter #(.width(12), .max('h80)) counter_1 (
    .carry(counter_1_carry), .clk(KeyboardClock), .clr(START));  // open: load, D, count, Q
  Counter #(.width(1), .max('h1), .trigger("falling")) counter_2 (
    .carry(counter_2_carry), .clk(KeyboardClock));  // open: load, D, count, Q, clr
  Counter #(.width(1), .max('h1)) counter_3 (
    .carry(counter_3_carry), .clk(KeyboardClock));  // open: load, D, count, Q, clr
  or or_2 (CI, counter_3_carry, counter_2_carry);
  // Probe on cdm_8_mark5_1_p6
  // CdM_8_mark5 cdm_8_mark5_1: pin names not known; wires that end beside it: cdm_8_mark5_1_p1, cdm_8_mark5_1_p2, CI, cdm_8_mark5_1_p4, cdm_8_mark5_1_p5, cdm_8_mark5_1_p6, cdm_8_mark5_1_p7, cdm_8_mark5_1_p8, in_out_prime, {cdm_8_mark5_1_p10, I_Oadr}, cdm_8_mark5_1_p11, cdm_8_mark5_1_p12
  and and_1 (GameClock, counter_1_carry, EnG, ~or_3_out);  // AND_Gate
  or or_3 (or_3_out, Pause, ProcWork, GameOver);
  and and_2 (and_2_out, EnTurn, ~d_ff_1_q, ~LoadPartToProc);  // AND_Gate
  assign controlled_buffer_1_out = and_2_out ? keyboard_1_data : 7'bz;  // Controlled_Buffer controlled_buffer_1
  Pull_Resistor pull_resistor_1 (.node(controlled_buffer_1_out));
  Keyboard keyboard_2 (
    .GameClock(GameClock), .START(START), .Pause(Pause), .Where(keyboard_2_where), .W(W), .A(A), .S(S),
    .D(D), .In(controlled_buffer_1_out));
  Decoder #(.disabled(0)) decoder_1 (.out0(code), .out1(data), .sel(cdm_8_mark5_1_p7), .en(cdm_8_mark5_1_p8));
  assign I_Odat = not_1_out ? cdm_8_mark5_1_p11 : 8'bz;  // Controlled_Buffer controlled_buffer_2
  not not_1 (not_1_out, in_out_prime);
  assign cdm_8_mark5_1_p12 = in_out_prime ? I_Odat : 8'bz;  // Controlled_Buffer controlled_buffer_3
  Register #(.width(2), .trigger("falling")) register_1 (
    .D(keyboard_2_where), .Q(Where), .clk(Turn), .clr(START));  // open: en
  and and_3 (I_Osel, and_4_out, CI, data);
  and and_4 (and_4_out, ~cdm_8_mark5_1_p10[1], ~cdm_8_mark5_1_p10[2], ~cdm_8_mark5_1_p10[3], cdm_8_mark5_1_p10[4], cdm_8_mark5_1_p10[5], cdm_8_mark5_1_p10[6], cdm_8_mark5_1_p10[7]);  // AND_Gate
  and and_5 (RAM, data, ~I_Osel);  // AND_Gate
  not not_2 (not_2_out, CI);
  ROM rom_1 (.addr({cdm_8_mark5_1_p10, I_Oadr}), .data(I_Odat), .sel(code));
  RAM ram_1 (
    .addr({cdm_8_mark5_1_p10, I_Oadr}), .data(I_Odat), .sel(RAM), .clk(not_2_out), .ld(in_out_prime));  // open: clr
  and and_6 (and_6_out, xnor_1_out[0], xnor_1_out[1], xnor_1_out[2], xnor_1_out[3], xnor_1_out[4]);
  and and_7 (GetScore, getApple, GameClock);
  Counter #(.width(5), .max('h1d), .trigger("falling")) counter_4 (
    .Q(CurrPart), .carry(counter_4_carry), .clk(GameClock), .clr(or_4_out));  // open: load, D, count
  or or_4 (or_4_out, not_4_out, START);
  assign xnor_1_out = ~(CurrPart ^ CurrLength);  // XNOR_Gate xnor_1, 5 bits wide
  D_Flip_Flop #(.trigger("falling")) d_ff_2 (
    .clk(GameClock), .D(GetScore), .Q(TailWait), .reset(START));  // open: Qn, preset, en
  Head head_1 (
    .W(W), .A(A), .S(S), .D(D), .START(START), .GameClock(GameClock), .Head_Y(head_1_head_y),
    .Head_X(head_1_head_x), .Turn(Turn), .EnH(EnG));
  D_Flip_Flop #(.trigger("falling")) d_ff_3 (.clk(START), .D(1'b1), .Q(d_ff_3_q), .reset(EnG));  // open: Qn, preset, en
  Tail tail_1 (
    .GameClock(GameClock), .START(START), .TailWait(TailWait), .Tail_Y(tail_1_tail_y),
    .Tail_X(tail_1_tail_x), .UpT(UpT), .LeftT(LeftT), .DownT(DownT), .RightT(RightT), .EnT(EnG));
  assign xnor_2_out = ~({5{1'b0}} ^ CurrPart);  // XNOR_Gate xnor_2, 5 bits wide
  or or_5 (AddPartToQ, and_6_out, counter_4_carry, Turn);
  not not_3 (not_3_out, AddPartToQ);
  not not_4 (not_4_out, not_3_out);
  not not_5 (not_5_out, START);
  toMatrix tomatrix_1 (
    .Head_X(head_1_head_x), .Head_Y(head_1_head_y), .Tail_Y(tail_1_tail_y), ._0(tomatrix_1__0),
    .out_24(tomatrix_1_out_24), .out_9(tomatrix_1_out_9), .out_25(tomatrix_1_out_25),
    .out_10(tomatrix_1_out_10), .out_26(tomatrix_1_out_26), .out_11(tomatrix_1_out_11),
    .out_27(tomatrix_1_out_27), .out_12(tomatrix_1_out_12), .out_28(tomatrix_1_out_28),
    .out_13(tomatrix_1_out_13), .out_29(tomatrix_1_out_29), .out_14(tomatrix_1_out_14),
    .out_30(tomatrix_1_out_30), .out_15(tomatrix_1_out_15), .out_31(tomatrix_1_out_31), .Smash(Smash),
    .out_16(tomatrix_1_out_16), .out_32(tomatrix_1_out_32), .out_17(tomatrix_1_out_17),
    .out_33(tomatrix_1_out_33), .out_18(tomatrix_1_out_18), .out_34(tomatrix_1_out_34),
    .out_19(tomatrix_1_out_19), .out_35(tomatrix_1_out_35), .out_20(tomatrix_1_out_20),
    .out_36(tomatrix_1_out_36), .out_21(tomatrix_1_out_21), .out_37(tomatrix_1_out_37),
    .out_22(tomatrix_1_out_22), .out_23(tomatrix_1_out_23), .CLEAR(START), .START(d_ff_3_q),
    .Tail_X(tail_1_tail_x));
  // Probe on head_1_head_y
  DotMatrix #(.inputtype("row"), .matrixcols(30), .matrixrows(30)) dotmatrix_1 (
    .row0(tomatrix_1_out_37), .row1(tomatrix_1_out_36), .row2(tomatrix_1_out_35), .row3(tomatrix_1_out_34),
    .row4(tomatrix_1_out_33), .row5(tomatrix_1_out_32), .row6(tomatrix_1_out_31), .row7(tomatrix_1_out_30),
    .row8(tomatrix_1_out_29), .row9(tomatrix_1_out_28), .row10(tomatrix_1_out_27), .row11(tomatrix_1_out_26),
    .row12(tomatrix_1_out_25), .row13(tomatrix_1_out_24), .row14(tomatrix_1_out_23),
    .row15(tomatrix_1_out_22), .row16(tomatrix_1_out_21), .row17(tomatrix_1_out_20),
    .row18(tomatrix_1_out_19), .row19(tomatrix_1_out_18), .row20(tomatrix_1_out_17),
    .row21(tomatrix_1_out_16), .row22(tomatrix_1_out_15), .row23(tomatrix_1_out_14),
    .row24(tomatrix_1_out_13), .row25(tomatrix_1_out_12), .row26(tomatrix_1_out_11),
    .row27(tomatrix_1_out_10), .row28(tomatrix_1_out_9), .row29(tomatrix_1__0));
  // Probe on tail_1_tail_y
  nand nand_1 (nand_1_out, xnor_2_out[0], xnor_2_out[1], xnor_2_out[2], xnor_2_out[3], xnor_2_out[4]);
  Counter #(.width(5), .max('h1f), .ongoal("stay")) counter_5 (
    .load(START), .D(5'b00100), .count(not_5_out), .Q(CurrLength), .clk(or_6_out));  // open: carry, clr
  or or_6 (or_6_out, START, GetScore);
  and and_8 (EnTurn, ~GameClock, nand_1_out);  // AND_Gate
  D_Flip_Flop d_ff_4 (.Q(GameOver), .preset(Smash), .reset(START));  // open: clk, D, Qn, en
  Button u_START (.out(START));
  not not_6 (not_6_out, START);
  not not_7 (not_7_out, not_6_out);
  assign I_Odat = ProcGotPart ? register_2_q : 8'bz;  // Controlled_Buffer controlled_buffer_4
  Register register_2 (.D({Where, 1'b0, CurrPart}), .Q(register_2_q), .clk(AddPartToQ), .clr(START));  // open: en
  not not_8 (not_8_out, LoadPartToTail);
  D_Flip_Flop #(.trigger("falling")) d_ff_5 (
    .clk(not_7_out), .D(1'b1), .Q(EnG), .reset(GameOver));  // open: Qn, preset, en
  _7_Segment_Display u_7_segment_display_1 ();  // open: g, f, a, b, e, d, c, dp
  _7_Segment_Display u_7_segment_display_2 ();  // open: g, f, a, b, e, d, c, dp
  assign I_Odat = and_10_out ? {EnG, LoadPartToProc, and_12_out[5], {5{1'b0}}} : 8'bz;  // Controlled_Buffer controlled_buffer_5
  D_Flip_Flop #(.trigger("falling")) d_ff_6 (
    .clk(AddPartToQ), .D(1'b1), .Q(LoadPartToProc), .reset(or_7_out));  // open: Qn, preset, en
  or or_7 (or_7_out, ProcGotPart, START);
  not not_9 (not_9_out, TailWait);
  Counter #(.width(5), .max('h1d), .ongoal("load"), .trigger("falling")) counter_6 (
    .load(1'b1), .D(I_Odat[4:0]), .count(not_8_out), .carry(counter_6_carry), .clk(or_8_out), .clr(START));  // open: Q
  or or_8 (or_8_out, LoadPartToTail, and_9_out);
  and and_9 (and_9_out, ~TailWait, GameClock);  // AND_Gate
  Register #(.width(2)) register_3 (.D(I_Odat[7:6]), .Q(register_3_q), .clk(LoadPartToTail), .clr(START));  // open: en
  and and_10 (and_10_out, decoder_3_out1, ~I_Oadr);  // AND_Gate
  and and_11 (ProcGotPart, decoder_3_out1, I_Oadr);
  or or_9 (ProcWork, LoadPartToProc, AddPartToQ, and_12_out[5]);
  Decoder #(.select(2), .disabled(0)) decoder_2 (
    .out0(UpT), .out1(LeftT), .out2(DownT), .out3(RightT), .sel(register_3_q), .en(not_10_out));
  not not_10 (not_10_out, and_12_out[5]);
  and and_12 (and_12_out[5], not_9_out, counter_6_carry);
  Decoder #(.disabled(0)) decoder_3 (.out0(decoder_3_out0), .out1(decoder_3_out1), .sel(in_out_prime), .en(I_Osel));
  and and_13 (LoadPartToTail, I_Oadr, decoder_3_out0);

  // Other names for the same wires on the sheet: rd_wr_prime = in_out_prime

  // Notes on the sheet:
  //   contents of rom_1 (hex, n*v repeats v):
  //   d0 f0 b1 5 e4 1f d0 0 d1 f2 a4 b5 d0 4 a4 d1 f3 d0 1 a4 d1 f4 d0 1 a4 d0 f0 b1 5 e5 1b 25 5 e5 42 d2
  //   f1 ba a e0 42 d0 f3 b0 a2 8c d2 f3 a8 8e b8 8c a8 d0 f3 b0 d2 f0 72 e1 42 d2 0 d0 f3 a2 25 5 e5 6b
  //   d0 f4 b0 0 e0 6b 88 d2 f4 a8 d0 f2 b0 b0 d2 f1 a8 d0 f2 b0 8c d2 f2 a8 d0 f2 b0 d2 f0 72 e1 6b d2 0
  //   d0 f2 a2 ee
endmodule

// TAIL
module Tail (
  input  EnT,
  input  TailWait,
  input  GameClock,
  input  START,
  input  UpT,
  input  LeftT,
  input  DownT,
  input  RightT,
  output [29:0] Tail_Y,
  output [29:0] Tail_X
);

  wire and_1_out, and_2_out, not_1_out, not_2_out, or_1_out, or_2_out, or_3_out, or_4_out, or_5_out, or_6_out;
  wire [4:0] Tail_X_t, Tail_Y_t;
  wire [29:0] shifter_1_out, shifter_2_out;

  or or_1 (or_1_out, DownT, START);
  not not_1 (not_1_out, START);
  or or_2 (or_2_out, START, and_1_out);
  or or_3 (or_3_out, UpT, DownT);
  Counter #(.width(5), .max('h1d)) counter_1 (
    .load(or_1_out), .D(5'b01011), .count(not_1_out), .Q(Tail_Y_t), .clk(or_2_out));  // open: carry, clr
  and and_1 (and_1_out, or_3_out, ~TailWait, GameClock);  // AND_Gate
  or or_4 (or_4_out, RightT, START);
  Counter #(.width(5), .max('h1d)) counter_2 (
    .load(or_4_out), .D(5'b01111), .count(not_2_out), .Q(Tail_X_t), .clk(or_5_out));  // open: carry, clr
  not not_2 (not_2_out, START);
  or or_5 (or_5_out, START, and_2_out);
  and and_2 (and_2_out, or_6_out, ~TailWait, GameClock);  // AND_Gate
  or or_6 (or_6_out, LeftT, RightT);
  assign Tail_Y = EnT ? shifter_1_out : 30'bz;  // Controlled_Buffer controlled_buffer_1
  Shifter #(.width(30)) shifter_1 (.in(30'h1), .\dist (Tail_Y_t), .out(shifter_1_out));
  Pull_Resistor pull_resistor_1 (.node(Tail_Y));
  assign Tail_X = EnT ? shifter_2_out : 30'bz;  // Controlled_Buffer controlled_buffer_2
  Shifter #(.width(30)) shifter_2 (.in(30'h1), .\dist (Tail_X_t), .out(shifter_2_out));
  Pull_Resistor pull_resistor_2 (.node(Tail_X));
endmodule

// HEAD
module Head (
  input  W,
  input  A,
  input  S,
  input  D,
  input  START,
  input  GameClock,
  input  EnH,
  output Turn,
  output [29:0] Head_Y,
  output [29:0] Head_X
);

  wire and_1_out, and_2_out, and_3_out, and_4_out, and_5_out, and_6_out, and_7_out, and_8_out, Down, Left,
       not_1_out, not_2_out, or_1_out, or_2_out, or_3_out, or_4_out, or_5_out, or_6_out, or_7_out, or_8_out,
       or_9_out, or_10_out, or_11_out, or_12_out, or_13_out, or_14_out, or_15_out, Right, Up;
  wire [4:0] Head_X_t, Head_Y_t;
  wire [29:0] shifter_1_out, shifter_2_out;

  or or_1 (or_1_out, Down, START);
  not not_1 (not_1_out, START);
  or or_2 (or_2_out, START, and_2_out);
  or or_3 (or_3_out, Up, Down);
  D_Flip_Flop d_ff_1 (.Q(Up), .preset(or_5_out), .reset(or_4_out));  // open: clk, D, Qn, en
  or or_4 (or_4_out, A, D);
  or or_5 (or_5_out, START, and_1_out);
  and and_1 (and_1_out, ~Down, W);  // AND_Gate
  Counter #(.width(5), .max('h1d)) counter_1 (
    .load(or_1_out), .D(5'b01111), .count(not_1_out), .Q(Head_Y_t), .clk(or_2_out));  // open: carry, clr
  and and_2 (and_2_out, or_3_out, GameClock);
  and and_3 (and_3_out, ~Up, S);  // AND_Gate
  D_Flip_Flop d_ff_2 (.Q(Down), .preset(and_3_out), .reset(or_6_out));  // open: clk, D, Qn, en
  and and_4 (and_4_out, ~Right, A);  // AND_Gate
  or or_6 (or_6_out, A, START, D);
  or or_7 (or_7_out, Right, START);
  Counter #(.width(5), .max('h1d)) counter_2 (
    .load(or_7_out), .D(5'b01111), .count(not_2_out), .Q(Head_X_t), .clk(or_8_out));  // open: carry, clr
  not not_2 (not_2_out, START);
  or or_8 (or_8_out, START, and_5_out);
  and and_5 (and_5_out, or_9_out, GameClock);
  or or_9 (or_9_out, Left, Right);
  D_Flip_Flop d_ff_3 (.Q(Left), .preset(and_4_out), .reset(or_10_out));  // open: clk, D, Qn, en
  and and_6 (and_6_out, ~Left, D);  // AND_Gate
  or or_10 (or_10_out, W, START, S);
  D_Flip_Flop d_ff_4 (.Q(Right), .preset(and_6_out), .reset(or_11_out));  // open: clk, D, Qn, en
  or or_11 (or_11_out, W, START, S);
  or or_12 (or_12_out, Down, Up);
  or or_13 (or_13_out, A, D);
  or or_14 (or_14_out, Left, Right);
  or or_15 (or_15_out, W, S);
  Shifter #(.width(30)) shifter_1 (.in(30'h1), .\dist (Head_Y_t), .out(shifter_1_out));
  Shifter #(.width(30)) shifter_2 (.in(30'h1), .\dist (Head_X_t), .out(shifter_2_out));
  and and_7 (and_7_out, or_12_out, or_13_out);
  or or_16 (Turn, and_7_out, and_8_out);
  and and_8 (and_8_out, or_14_out, or_15_out);
  assign Head_Y = EnH ? shifter_1_out : 30'bz;  // Controlled_Buffer controlled_buffer_1
  Pull_Resistor pull_resistor_1 (.node(Head_Y));
  assign Head_X = EnH ? shifter_2_out : 30'bz;  // Controlled_Buffer controlled_buffer_2
  Pull_Resistor pull_resistor_2 (.node(Head_X));
endmodule

module toMatrix (
  input  START,
  input  CLEAR,
  input  [29:0] Head_Y,
  input  [29:0] Tail_Y,
  input  [29:0] Head_X,
  input  [29:0] Tail_X,
  output Smash,
  output [29:0] _0,
  output [29:0] out_9,
  output [29:0] out_10,
  output [29:0] out_11,
  output [29:0] out_12,
  output [29:0] out_13,
  output [29:0] out_14,
  output [29:0] out_15,
  output [29:0] out_16,
  output [29:0] out_17,
  output [29:0] out_18,
  output [29:0] out_19,
  output [29:0] out_20,
  output [29:0] out_21,
  output [29:0] out_22,
  output [29:0] out_23,
  output [29:0] out_24,
  output [29:0] out_25,
  output [29:0] out_26,
  output [29:0] out_27,
  output [29:0] out_28,
  output [29:0] out_29,
  output [29:0] out_30,
  output [29:0] out_31,
  output [29:0] out_32,
  output [29:0] out_33,
  output [29:0] out_34,
  output [29:0] out_35,
  output [29:0] out_36,
  output [29:0] out_37
);

  wire H12, H13, H14, line_1_smash, line_2_smash, line_3_smash, line_4_smash, line_5_smash, line_6_smash,
       line_7_smash, line_8_smash, line_9_smash, line_10_smash, line_11_smash, line_12_smash, line_13_smash,
       line_14_smash, line_15_smash, line_16_smash, line_17_smash, line_18_smash, line_19_smash,
       line_20_smash, line_21_smash, line_22_smash, line_23_smash, line_24_smash, line_25_smash,
       line_26_smash, line_27_smash, line_28_smash, line_29_smash, line_30_smash;

  or or_1 (H13, START, Head_Y[13]);
  or or_2 (H12, START, Head_Y[12]);
  or or_3 (H14, START, Head_Y[14]);
  Line line_1 (
    .Out(_0), .Smash(line_1_smash), .CLEAR(CLEAR), .HeadOnLine(Head_X), .TailOnLine(Tail_X), .EnT(Tail_Y[0]),
    .EnH(Head_Y[0]));
  assign Smash = Head_Y[0] ? line_1_smash : 1'bz;  // Controlled_Buffer controlled_buffer_1
  Line line_2 (
    .Out(out_9), .Smash(line_2_smash), .CLEAR(CLEAR), .HeadOnLine(Head_X), .TailOnLine(Tail_X),
    .EnT(Tail_Y[1]), .EnH(Head_Y[1]));
  assign Smash = Head_Y[1] ? line_2_smash : 1'bz;  // Controlled_Buffer controlled_buffer_2
  Line line_3 (
    .Out(out_10), .Smash(line_3_smash), .CLEAR(CLEAR), .HeadOnLine(Head_X), .TailOnLine(Tail_X),
    .EnT(Tail_Y[2]), .EnH(Head_Y[2]));
  assign Smash = Head_Y[2] ? line_3_smash : 1'bz;  // Controlled_Buffer controlled_buffer_3
  Line line_4 (
    .Out(out_11), .Smash(line_4_smash), .CLEAR(CLEAR), .HeadOnLine(Head_X), .TailOnLine(Tail_X),
    .EnT(Tail_Y[3]), .EnH(Head_Y[3]));
  assign Smash = Head_Y[3] ? line_4_smash : 1'bz;  // Controlled_Buffer controlled_buffer_4
  Line line_5 (
    .Out(out_12), .Smash(line_5_smash), .CLEAR(CLEAR), .HeadOnLine(Head_X), .TailOnLine(Tail_X),
    .EnT(Tail_Y[4]), .EnH(Head_Y[4]));
  assign Smash = Head_Y[4] ? line_5_smash : 1'bz;  // Controlled_Buffer controlled_buffer_5
  Line line_6 (
    .Out(out_13), .Smash(line_6_smash), .CLEAR(CLEAR), .HeadOnLine(Head_X), .TailOnLine(Tail_X),
    .EnT(Tail_Y[5]), .EnH(Head_Y[5]));
  assign Smash = Head_Y[5] ? line_6_smash : 1'bz;  // Controlled_Buffer controlled_buffer_6
  assign Smash = Head_Y[6] ? line_7_smash : 1'bz;  // Controlled_Buffer controlled_buffer_7
  Line line_7 (
    .Out(out_14), .Smash(line_7_smash), .CLEAR(CLEAR), .HeadOnLine(Head_X), .TailOnLine(Tail_X),
    .EnT(Tail_Y[6]), .EnH(Head_Y[6]));
  Line line_8 (
    .Out(out_15), .Smash(line_8_smash), .CLEAR(CLEAR), .HeadOnLine(Head_X), .TailOnLine(Tail_X),
    .EnT(Tail_Y[7]), .EnH(Head_Y[7]));
  assign Smash = Head_Y[7] ? line_8_smash : 1'bz;  // Controlled_Buffer controlled_buffer_8
  Line line_9 (
    .Out(out_16), .Smash(line_9_smash), .CLEAR(CLEAR), .HeadOnLine(Head_X), .TailOnLine(Tail_X),
    .EnT(Tail_Y[8]), .EnH(Head_Y[8]));
  Line line_10 (
    .Out(out_17), .Smash(line_10_smash), .CLEAR(CLEAR), .HeadOnLine(Head_X), .TailOnLine(Tail_X),
    .EnT(Tail_Y[9]), .EnH(Head_Y[9]));
  Line line_11 (
    .Out(out_18), .Smash(line_11_smash), .CLEAR(CLEAR), .HeadOnLine(Head_X), .TailOnLine(Tail_X),
    .EnT(Tail_Y[10]), .EnH(Head_Y[10]));
  Line line_12 (
    .Out(out_19), .Smash(line_12_smash), .CLEAR(CLEAR), .HeadOnLine(Head_X), .TailOnLine(Tail_X),
    .EnT(Tail_Y[11]), .EnH(Head_Y[11]));
  Line line_13 (
    .Out(out_20), .Smash(line_13_smash), .CLEAR(CLEAR), .HeadOnLine(Head_X), .TailOnLine(Tail_X),
    .EnT(Tail_Y[12]), .EnH(H12));
  Line line_14 (
    .Out(out_21), .Smash(line_14_smash), .CLEAR(CLEAR), .HeadOnLine(Head_X), .TailOnLine(Tail_X),
    .EnT(Tail_Y[13]), .EnH(H13));
  Line line_15 (
    .Out(out_22), .Smash(line_15_smash), .CLEAR(CLEAR), .HeadOnLine(Head_X), .TailOnLine(Tail_X),
    .EnT(Tail_Y[14]), .EnH(H14));
  Line line_16 (
    .Out(out_23), .Smash(line_16_smash), .CLEAR(CLEAR), .HeadOnLine(Head_X), .TailOnLine(Tail_X),
    .EnT(Tail_Y[15]), .EnH(Head_Y[15]));
  assign Smash = Head_Y[8] ? line_9_smash : 1'bz;  // Controlled_Buffer controlled_buffer_9
  assign Smash = Head_Y[9] ? line_10_smash : 1'bz;  // Controlled_Buffer controlled_buffer_10
  assign Smash = Head_Y[10] ? line_11_smash : 1'bz;  // Controlled_Buffer controlled_buffer_11
  assign Smash = Head_Y[11] ? line_12_smash : 1'bz;  // Controlled_Buffer controlled_buffer_12
  assign Smash = H12 ? line_13_smash : 1'bz;  // Controlled_Buffer controlled_buffer_13
  assign Smash = H13 ? line_14_smash : 1'bz;  // Controlled_Buffer controlled_buffer_14
  assign Smash = H14 ? line_15_smash : 1'bz;  // Controlled_Buffer controlled_buffer_15
  assign Smash = Head_Y[15] ? line_16_smash : 1'bz;  // Controlled_Buffer controlled_buffer_16
  Line line_17 (
    .Out(out_24), .Smash(line_17_smash), .CLEAR(CLEAR), .HeadOnLine(Head_X), .TailOnLine(Tail_X),
    .EnT(Tail_Y[16]), .EnH(Head_Y[16]));
  Line line_18 (
    .Out(out_25), .Smash(line_18_smash), .CLEAR(CLEAR), .HeadOnLine(Head_X), .TailOnLine(Tail_X),
    .EnT(Tail_Y[17]), .EnH(Head_Y[17]));
  Line line_19 (
    .Out(out_26), .Smash(line_19_smash), .CLEAR(CLEAR), .HeadOnLine(Head_X), .TailOnLine(Tail_X),
    .EnT(Tail_Y[18]), .EnH(Head_Y[18]));
  Line line_20 (
    .Out(out_27), .Smash(line_20_smash), .CLEAR(CLEAR), .HeadOnLine(Head_X), .TailOnLine(Tail_X),
    .EnT(Tail_Y[19]), .EnH(Head_Y[19]));
  Line line_21 (
    .Out(out_28), .Smash(line_21_smash), .CLEAR(CLEAR), .HeadOnLine(Head_X), .TailOnLine(Tail_X),
    .EnT(Tail_Y[20]), .EnH(Head_Y[20]));
  Line line_22 (
    .Out(out_29), .Smash(line_22_smash), .CLEAR(CLEAR), .HeadOnLine(Head_X), .TailOnLine(Tail_X),
    .EnT(Tail_Y[21]), .EnH(Head_Y[21]));
  Line line_23 (
    .Out(out_30), .Smash(line_23_smash), .CLEAR(CLEAR), .HeadOnLine(Head_X), .TailOnLine(Tail_X),
    .EnT(Tail_Y[22]), .EnH(Head_Y[22]));
  Line line_24 (
    .Out(out_31), .Smash(line_24_smash), .CLEAR(CLEAR), .HeadOnLine(Head_X), .TailOnLine(Tail_X),
    .EnT(Tail_Y[23]), .EnH(Head_Y[23]));
  Pull_Resistor pull_resistor_1 (.node(Smash));
  assign Smash = Head_Y[16] ? line_17_smash : 1'bz;  // Controlled_Buffer controlled_buffer_17
  assign Smash = Head_Y[17] ? line_18_smash : 1'bz;  // Controlled_Buffer controlled_buffer_18
  assign Smash = Head_Y[18] ? line_19_smash : 1'bz;  // Controlled_Buffer controlled_buffer_19
  assign Smash = Head_Y[19] ? line_20_smash : 1'bz;  // Controlled_Buffer controlled_buffer_20
  assign Smash = Head_Y[20] ? line_21_smash : 1'bz;  // Controlled_Buffer controlled_buffer_21
  assign Smash = Head_Y[21] ? line_22_smash : 1'bz;  // Controlled_Buffer controlled_buffer_22
  assign Smash = Head_Y[22] ? line_23_smash : 1'bz;  // Controlled_Buffer controlled_buffer_23
  assign Smash = Head_Y[23] ? line_24_smash : 1'bz;  // Controlled_Buffer controlled_buffer_24
  Line line_25 (
    .Out(out_32), .Smash(line_25_smash), .CLEAR(CLEAR), .HeadOnLine(Head_X), .TailOnLine(Tail_X),
    .EnT(Tail_Y[24]), .EnH(Head_Y[24]));
  Line line_26 (
    .Out(out_33), .Smash(line_26_smash), .CLEAR(CLEAR), .HeadOnLine(Head_X), .TailOnLine(Tail_X),
    .EnT(Tail_Y[25]), .EnH(Head_Y[25]));
  Line line_27 (
    .Out(out_34), .Smash(line_27_smash), .CLEAR(CLEAR), .HeadOnLine(Head_X), .TailOnLine(Tail_X),
    .EnT(Tail_Y[26]), .EnH(Head_Y[26]));
  Line line_28 (
    .Out(out_35), .Smash(line_28_smash), .CLEAR(CLEAR), .HeadOnLine(Head_X), .TailOnLine(Tail_X),
    .EnT(Tail_Y[27]), .EnH(Head_Y[27]));
  Line line_29 (
    .Out(out_36), .Smash(line_29_smash), .CLEAR(CLEAR), .HeadOnLine(Head_X), .TailOnLine(Tail_X),
    .EnT(Tail_Y[28]), .EnH(Head_Y[28]));
  Line line_30 (
    .Out(out_37), .Smash(line_30_smash), .CLEAR(CLEAR), .HeadOnLine(Head_X), .TailOnLine(Tail_X),
    .EnT(Tail_Y[29]), .EnH(Head_Y[29]));
  assign Smash = Head_Y[24] ? line_25_smash : 1'bz;  // Controlled_Buffer controlled_buffer_25
  assign Smash = Head_Y[25] ? line_26_smash : 1'bz;  // Controlled_Buffer controlled_buffer_26
  assign Smash = Head_Y[26] ? line_27_smash : 1'bz;  // Controlled_Buffer controlled_buffer_27
  assign Smash = Head_Y[27] ? line_28_smash : 1'bz;  // Controlled_Buffer controlled_buffer_28
  assign Smash = Head_Y[28] ? line_29_smash : 1'bz;  // Controlled_Buffer controlled_buffer_29
  assign Smash = Head_Y[29] ? line_30_smash : 1'bz;  // Controlled_Buffer controlled_buffer_30

  // Other names for the same wires on the sheet: H0 = Head_Y[0]; H1 = Head_Y[1]; H2 = Head_Y[2]; H3 = Head_Y[3];
  //   H4 = Head_Y[4]; H5 = Head_Y[5]; H6 = Head_Y[6]; H7 = Head_Y[7]; H8 = Head_Y[8]; H9 = Head_Y[9];
  //   H10 = Head_Y[10]; H11 = Head_Y[11]; H15 = Head_Y[15]; H16 = Head_Y[16]; H17 = Head_Y[17]; H18 = Head_Y[18];
  //   H19 = Head_Y[19]; H20 = Head_Y[20]; H21 = Head_Y[21]; H22 = Head_Y[22]; H23 = Head_Y[23]; H24 = Head_Y[24];
  //   H25 = Head_Y[25]; H26 = Head_Y[26]; H27 = Head_Y[27]; H28 = Head_Y[28]; H29 = Head_Y[29];
  //   HeadOnLine[29:0] = Head_X; O0[29:0] = _0; O1[29:0] = out_9; O2[29:0] = out_10; O3[29:0] = out_11;
  //   O4[29:0] = out_12; O5[29:0] = out_13; O6[29:0] = out_14; O7[29:0] = out_15; O8[29:0] = out_16;
  //   O9[29:0] = out_17; O10[29:0] = out_18; O11[29:0] = out_19; O12[29:0] = out_20; O13[29:0] = out_21;
  //   O14[29:0] = out_22; O15[29:0] = out_23; O16[29:0] = out_24; O17[29:0] = out_25; O18[29:0] = out_26;
  //   O19[29:0] = out_27; O20[29:0] = out_28; O21[29:0] = out_29; O22[29:0] = out_30; O23[29:0] = out_31;
  //   O24[29:0] = out_32; O25[29:0] = out_33; O26[29:0] = out_34; O27[29:0] = out_35; O28[29:0] = out_36;
  //   O29[29:0] = out_37; T0 = Tail_Y[0]; T1 = Tail_Y[1]; T2 = Tail_Y[2]; T3 = Tail_Y[3]; T4 = Tail_Y[4];
  //   T5 = Tail_Y[5]; T6 = Tail_Y[6]; T7 = Tail_Y[7]; T8 = Tail_Y[8]; T9 = Tail_Y[9]; T10 = Tail_Y[10];
  //   T11 = Tail_Y[11]; T12 = Tail_Y[12]; T13 = Tail_Y[13]; T14 = Tail_Y[14]; T15 = Tail_Y[15]; T16 = Tail_Y[16];
  //   T17 = Tail_Y[17]; T18 = Tail_Y[18]; T19 = Tail_Y[19]; T20 = Tail_Y[20]; T21 = Tail_Y[21]; T22 = Tail_Y[22];
  //   T23 = Tail_Y[23]; T24 = Tail_Y[24]; T25 = Tail_Y[25]; T26 = Tail_Y[26]; T27 = Tail_Y[27]; T28 = Tail_Y[28];
  //   T29 = Tail_Y[29]; TailOnLine[29:0] = Tail_X
endmodule

// LINE
module Line (
  input  CLEAR,
  input  EnH,
  input  [29:0] HeadOnLine,
  input  EnT,
  input  [29:0] TailOnLine,
  output [29:0] Out,
  output Smash
);

  wire H0, H1, H2, H3, H4, H5, H6, H7, H8, H9, H10, H11, H12, H13, H14, H15, H16, H17, H18, H19, H20, H21,
       H22, H23, H24, H25, H26, H27, H28, H29, pixel_1_smash, pixel_2_smash, pixel_3_smash, pixel_4_smash,
       pixel_5_smash, pixel_6_smash, pixel_7_smash, pixel_8_smash, pixel_9_smash, pixel_10_smash,
       pixel_11_smash, pixel_12_smash, pixel_13_smash, pixel_14_smash, pixel_15_smash, pixel_16_smash,
       pixel_17_smash, pixel_18_smash, pixel_19_smash, pixel_20_smash, pixel_21_smash, pixel_22_smash,
       pixel_23_smash, pixel_24_smash, pixel_25_smash, pixel_26_smash, pixel_27_smash, pixel_28_smash,
       pixel_29_smash, pixel_30_smash, T0, T1, T2, T3, T4, T5, T6, T7, T8, T9, T10, T11, T12, T13, T14, T15,
       T16, T17, T18, T19, T20, T21, T22, T23, T24, T25, T26, T27, T28, T29;

  pixel pixel_1 (.Up(H0), .Down(T0), .Light(Out[0]), .Smash(pixel_1_smash), .CLEAR(CLEAR));
  assign Smash = H0 ? pixel_1_smash : 1'bz;  // Controlled_Buffer controlled_buffer_1
  pixel pixel_2 (.Up(H16), .Down(T16), .Light(Out[16]), .Smash(pixel_2_smash), .CLEAR(CLEAR));
  assign Smash = H16 ? pixel_2_smash : 1'bz;  // Controlled_Buffer controlled_buffer_2
  assign {H29, H28, H27, H26, H25, H24, H23, H22, H21, H20, H19, H18, H17, H16, H15, H14, H13, H12, H11, H10, H9, H8, H7, H6, H5, H4, H3, H2, H1, H0} = EnH ? HeadOnLine : 30'bz;  // Controlled_Buffer controlled_buffer_3
  assign {T29, T28, T27, T26, T25, T24, T23, T22, T21, T20, T19, T18, T17, T16, T15, T14, T13, T12, T11, T10, T9, T8, T7, T6, T5, T4, T3, T2, T1, T0} = EnT ? TailOnLine : 30'bz;  // Controlled_Buffer controlled_buffer_4
  pixel pixel_3 (.Up(H2), .Down(T2), .Light(Out[2]), .Smash(pixel_3_smash), .CLEAR(CLEAR));
  pixel pixel_4 (.Up(H1), .Down(T1), .Light(Out[1]), .Smash(pixel_4_smash), .CLEAR(CLEAR));
  assign Smash = H2 ? pixel_3_smash : 1'bz;  // Controlled_Buffer controlled_buffer_5
  assign Smash = H1 ? pixel_4_smash : 1'bz;  // Controlled_Buffer controlled_buffer_6
  pixel pixel_5 (.Up(H17), .Down(T17), .Light(Out[17]), .Smash(pixel_5_smash), .CLEAR(CLEAR));
  pixel pixel_6 (.Up(H18), .Down(T18), .Light(Out[18]), .Smash(pixel_6_smash), .CLEAR(CLEAR));
  assign Smash = H18 ? pixel_6_smash : 1'bz;  // Controlled_Buffer controlled_buffer_7
  assign Smash = H17 ? pixel_5_smash : 1'bz;  // Controlled_Buffer controlled_buffer_8
  Pull_Resistor pull_resistor_1 (.node({H29, H28, H27, H26, H25, H24, H23, H22, H21, H20, H19, H18, H17, H16, H15, H14, H13, H12, H11, H10, H9, H8, H7, H6, H5, H4, H3, H2, H1, H0}));
  Pull_Resistor pull_resistor_2 (.node({T29, T28, T27, T26, T25, T24, T23, T22, T21, T20, T19, T18, T17, T16, T15, T14, T13, T12, T11, T10, T9, T8, T7, T6, T5, T4, T3, T2, T1, T0}));
  pixel pixel_7 (.Up(H3), .Down(T3), .Light(Out[3]), .Smash(pixel_7_smash), .CLEAR(CLEAR));
  assign Smash = H3 ? pixel_7_smash : 1'bz;  // Controlled_Buffer controlled_buffer_9
  pixel pixel_8 (.Up(H19), .Down(T19), .Light(Out[19]), .Smash(pixel_8_smash), .CLEAR(CLEAR));
  assign Smash = H19 ? pixel_8_smash : 1'bz;  // Controlled_Buffer controlled_buffer_10
  pixel pixel_9 (.Up(H4), .Down(T4), .Light(Out[4]), .Smash(pixel_9_smash), .CLEAR(CLEAR));
  pixel pixel_10 (.Up(H5), .Down(T5), .Light(Out[5]), .Smash(pixel_10_smash), .CLEAR(CLEAR));
  assign Smash = H4 ? pixel_9_smash : 1'bz;  // Controlled_Buffer controlled_buffer_11
  assign Smash = H5 ? pixel_10_smash : 1'bz;  // Controlled_Buffer controlled_buffer_12
  pixel pixel_11 (.Up(H21), .Down(T21), .Light(Out[21]), .Smash(pixel_11_smash), .CLEAR(CLEAR));
  pixel pixel_12 (.Up(H20), .Down(T20), .Light(Out[20]), .Smash(pixel_12_smash), .CLEAR(CLEAR));
  assign Smash = H21 ? pixel_11_smash : 1'bz;  // Controlled_Buffer controlled_buffer_13
  assign Smash = H20 ? pixel_12_smash : 1'bz;  // Controlled_Buffer controlled_buffer_14
  pixel pixel_13 (.Up(H6), .Down(T6), .Light(Out[6]), .Smash(pixel_13_smash), .CLEAR(CLEAR));
  assign Smash = H7 ? pixel_15_smash : 1'bz;  // Controlled_Buffer controlled_buffer_15
  assign Smash = H6 ? pixel_13_smash : 1'bz;  // Controlled_Buffer controlled_buffer_16
  pixel pixel_14 (.Up(H22), .Down(T22), .Light(Out[22]), .Smash(pixel_14_smash), .CLEAR(CLEAR));
  assign Smash = H22 ? pixel_14_smash : 1'bz;  // Controlled_Buffer controlled_buffer_17
  assign Smash = H23 ? pixel_18_smash : 1'bz;  // Controlled_Buffer controlled_buffer_18
  pixel pixel_15 (.Up(H7), .Down(T7), .Light(Out[7]), .Smash(pixel_15_smash), .CLEAR(CLEAR));
  pixel pixel_16 (.Up(H8), .Down(T8), .Light(Out[8]), .Smash(pixel_16_smash), .CLEAR(CLEAR));
  assign Smash = H8 ? pixel_16_smash : 1'bz;  // Controlled_Buffer controlled_buffer_19
  pixel pixel_17 (.Up(H24), .Down(T24), .Light(Out[24]), .Smash(pixel_17_smash), .CLEAR(CLEAR));
  pixel pixel_18 (.Up(H23), .Down(T23), .Light(Out[23]), .Smash(pixel_18_smash), .CLEAR(CLEAR));
  assign Smash = H24 ? pixel_17_smash : 1'bz;  // Controlled_Buffer controlled_buffer_20
  pixel pixel_19 (.Up(H9), .Down(T9), .Light(Out[9]), .Smash(pixel_19_smash), .CLEAR(CLEAR));
  pixel pixel_20 (.Up(H10), .Down(T10), .Light(Out[10]), .Smash(pixel_20_smash), .CLEAR(CLEAR));
  assign Smash = H10 ? pixel_20_smash : 1'bz;  // Controlled_Buffer controlled_buffer_21
  assign Smash = H9 ? pixel_19_smash : 1'bz;  // Controlled_Buffer controlled_buffer_22
  pixel pixel_21 (.Up(H25), .Down(T25), .Light(Out[25]), .Smash(pixel_21_smash), .CLEAR(CLEAR));
  pixel pixel_22 (.Up(H26), .Down(T26), .Light(Out[26]), .Smash(pixel_22_smash), .CLEAR(CLEAR));
  assign Smash = H25 ? pixel_21_smash : 1'bz;  // Controlled_Buffer controlled_buffer_23
  assign Smash = H26 ? pixel_22_smash : 1'bz;  // Controlled_Buffer controlled_buffer_24
  pixel pixel_23 (.Up(H11), .Down(T11), .Light(Out[11]), .Smash(pixel_23_smash), .CLEAR(CLEAR));
  assign Smash = H11 ? pixel_23_smash : 1'bz;  // Controlled_Buffer controlled_buffer_25
  pixel pixel_24 (.Up(H27), .Down(T27), .Light(Out[27]), .Smash(pixel_24_smash), .CLEAR(CLEAR));
  assign Smash = H27 ? pixel_24_smash : 1'bz;  // Controlled_Buffer controlled_buffer_26
  pixel pixel_25 (.Up(H13), .Down(T13), .Light(Out[13]), .Smash(pixel_25_smash), .CLEAR(CLEAR));
  pixel pixel_26 (.Up(H12), .Down(T12), .Light(Out[12]), .Smash(pixel_26_smash), .CLEAR(CLEAR));
  assign Smash = H12 ? pixel_26_smash : 1'bz;  // Controlled_Buffer controlled_buffer_27
  assign Smash = H13 ? pixel_25_smash : 1'bz;  // Controlled_Buffer controlled_buffer_28
  pixel pixel_27 (.Up(H29), .Down(T29), .Light(Out[29]), .Smash(pixel_27_smash), .CLEAR(CLEAR));
  pixel pixel_28 (.Up(H28), .Down(T28), .Light(Out[28]), .Smash(pixel_28_smash), .CLEAR(CLEAR));
  assign Smash = H29 ? pixel_27_smash : 1'bz;  // Controlled_Buffer controlled_buffer_29
  assign Smash = H28 ? pixel_28_smash : 1'bz;  // Controlled_Buffer controlled_buffer_30
  pixel pixel_29 (.Up(H14), .Down(T14), .Light(Out[14]), .Smash(pixel_29_smash), .CLEAR(CLEAR));
  assign Smash = H14 ? pixel_29_smash : 1'bz;  // Controlled_Buffer controlled_buffer_31
  assign Smash = H15 ? pixel_30_smash : 1'bz;  // Controlled_Buffer controlled_buffer_32
  pixel pixel_30 (.Up(H15), .Down(T15), .Light(Out[15]), .Smash(pixel_30_smash), .CLEAR(CLEAR));
  Pull_Resistor pull_resistor_3 (.node(Smash));

  // Other names for the same wires on the sheet: L0 = Out[0]; L1 = Out[1]; L2 = Out[2]; L3 = Out[3]; L4 = Out[4];
  //   L5 = Out[5]; L6 = Out[6]; L7 = Out[7]; L8 = Out[8]; L9 = Out[9]; L10 = Out[10]; L11 = Out[11]; L12 = Out[12];
  //   L13 = Out[13]; L14 = Out[14]; L15 = Out[15]; L16 = Out[16]; L17 = Out[17]; L18 = Out[18]; L19 = Out[19];
  //   L20 = Out[20]; L21 = Out[21]; L22 = Out[22]; L23 = Out[23]; L24 = Out[24]; L25 = Out[25]; L26 = Out[26];
  //   L27 = Out[27]; L28 = Out[28]; L29 = Out[29]
endmodule

module pixel (
  input  CLEAR,
  input  Up,
  input  Down,
  output Light,
  output Smash
);

  wire and_2_out, or_1_out, Visited;

  D_Flip_Flop d_ff_1 (.clk(Up), .D(1'b1), .Q(Light), .reset(or_1_out));  // open: Qn, preset, en
  and and_1 (Smash, Visited, Up);
  or or_1 (or_1_out, and_2_out, CLEAR);
  and and_2 (and_2_out, ~Up, Down);  // AND_Gate
  D_Flip_Flop #(.trigger("falling")) d_ff_2 (
    .clk(Up), .D(1'b1), .Q(Visited), .reset(or_1_out));  // open: Qn, preset, en
endmodule

module Keyboard (
  input  GameClock,
  input  START,
  input  [6:0] In,
  output Pause,
  output [1:0] Where,
  output D,
  output S,
  output A,
  output W
);

  wire and_1_out, bitshrink_1_pause, or_1_out, pull_resistor_1_node;
  wire [1:0] bitshrink_1_where;

  bitShrink bitshrink_1 (.In(In), .W(W), .A(A), .S(S), .D(D), .Where(bitshrink_1_where), .Pause(bitshrink_1_pause));
  and and_1 (and_1_out, ~GameClock, bitshrink_1_pause);  // AND_Gate
  D_Flip_Flop d_ff_1 (.clk(and_1_out), .D(pull_resistor_1_node), .Q(Pause), .reset(START));  // open: Qn, preset, en
  Pull_Resistor #(.pull(1)) pull_resistor_1 (.node(pull_resistor_1_node));
  assign pull_resistor_1_node = bitshrink_1_pause ? ~bitshrink_1_pause : 1'bz;  // Controlled_Inverter controlled_inverter_1
  Register #(.width(2)) register_1 (.D(bitshrink_1_where), .Q(Where), .clk(or_1_out), .clr(START));  // open: en
  or or_1 (or_1_out, W, A, S, D);
endmodule

module bitShrink (
  input  [6:0] In,
  output W,
  output A,
  output [1:0] Where,
  output S,
  output D,
  output Pause
);

  wire [6:0] xnor_1_out, xnor_2_out, xnor_3_out, xnor_4_out, xnor_5_out;

  // Probe on 7'b1110111
  // Probe on 7'b1100001
  // Probe on 7'b1110011
  // Probe on 7'b1100100
  // Probe on 7'b0100000
  assign xnor_1_out = ~(In ^ 7'b1110111);  // XNOR_Gate xnor_1, 7 bits wide
  assign xnor_2_out = ~(In ^ 7'b1100001);  // XNOR_Gate xnor_2, 7 bits wide
  assign xnor_3_out = ~(In ^ 7'b1110011);  // XNOR_Gate xnor_3, 7 bits wide
  assign xnor_4_out = ~(In ^ 7'b1100100);  // XNOR_Gate xnor_4, 7 bits wide
  assign xnor_5_out = ~(In ^ 7'b0100000);  // XNOR_Gate xnor_5, 7 bits wide
  and and_1 (W, xnor_1_out[0], xnor_1_out[1], xnor_1_out[2], xnor_1_out[3], xnor_1_out[4], xnor_1_out[5], xnor_1_out[6]);
  and and_2 (A, xnor_2_out[0], xnor_2_out[1], xnor_2_out[2], xnor_2_out[3], xnor_2_out[4], xnor_2_out[5], xnor_2_out[6]);
  and and_3 (S, xnor_3_out[0], xnor_3_out[1], xnor_3_out[2], xnor_3_out[3], xnor_3_out[4], xnor_3_out[5], xnor_3_out[6]);
  and and_4 (D, xnor_4_out[0], xnor_4_out[1], xnor_4_out[2], xnor_4_out[3], xnor_4_out[4], xnor_4_out[5], xnor_4_out[6]);
  and and_5 (Pause, xnor_5_out[0], xnor_5_out[1], xnor_5_out[2], xnor_5_out[3], xnor_5_out[4], xnor_5_out[5], xnor_5_out[6]);
  assign Where = W ? 2'b00 : 2'bz;  // Controlled_Buffer controlled_buffer_1
  assign Where = A ? 2'b01 : 2'bz;  // Controlled_Buffer controlled_buffer_2
  assign Where = S ? 2'b10 : 2'bz;  // Controlled_Buffer controlled_buffer_3
  assign Where = D ? 2'b11 : 2'bz;  // Controlled_Buffer controlled_buffer_4
  Pull_Resistor pull_resistor_1 (.node(Where));
endmodule

module Apples (
  input  [31:0] L1,
  input  [31:0] L1_2
);

  wire or_1_out;
  wire [4:0] random_1_out, random_2_out;
  wire [31:0] and_1_out, multiplexer_1_out, shifter_1_out;

  Random #(.width(5)) random_1 (.clk(or_1_out), .out(random_1_out));  // open: next, clr
  Random #(.width(5)) random_2 (.clk(or_1_out), .out(random_2_out));  // open: next, clr
  Multiplexer #(.select(5), .width(32)) multiplexer_1 (
    .out(multiplexer_1_out), .sel(random_1_out));  // open: in0, in1, in2, in3, in4, in5, in6, in7, in8, in9, in10, in11, in12, in13, in14, in15, in16, in17, in18, in19, in20, in21, in22, in23, in24, in25, in26, in27, in28, in29, in30, in31, en
  Shifter #(.width(32)) shifter_1 (.in(32'h1), .\dist (random_2_out), .out(shifter_1_out));
  assign and_1_out = shifter_1_out & multiplexer_1_out;  // AND_Gate and_1, 32 bits wide
  or or_1 (or_1_out, and_1_out[0], and_1_out[1], and_1_out[2], and_1_out[3], and_1_out[4], and_1_out[5], and_1_out[6], and_1_out[7], and_1_out[8], and_1_out[9], and_1_out[10], and_1_out[11], and_1_out[12], and_1_out[13], and_1_out[14], and_1_out[15], and_1_out[16], and_1_out[17], and_1_out[18], and_1_out[19], and_1_out[20], and_1_out[21], and_1_out[22], and_1_out[23], and_1_out[24], and_1_out[25], and_1_out[26], and_1_out[27], and_1_out[28], and_1_out[29], and_1_out[30], and_1_out[31]);
endmodule

module Inc (
  input  [5:0] in,
  input  En,
  output [5:0] out
);

  wire not_1_out;
  wire [5:0] xor_1_out;
  wire [5:1] and_1_out;
  wire [5:5] and_1_out_2;

  // Probe on in
  assign {and_1_out_2[5], and_1_out} = in & {and_1_out, 1'b1};  // AND_Gate and_1, 6 bits wide
  assign xor_1_out = {and_1_out, 1'b1} ^ in;  // XOR_Gate xor_1, 6 bits wide
  // Probe on xor_1_out
  Multiplexer #(.width(6), .enable("false")) multiplexer_1 (.in0(xor_1_out), .in1(in), .out(out), .sel(not_1_out));
  not not_1 (not_1_out, En);
endmodule

module test (
  input  [1:0] EnT
);

  wire clock_1_out;
  wire [31:0] map_loader_1_p3, map_loader_1_p4, map_loader_1_p5, map_loader_1_p6, map_loader_1_p7,
       map_loader_1_p8, map_loader_1_p9, map_loader_1_p10, map_loader_1_p11, map_loader_1_p12,
       map_loader_1_p13, map_loader_1_p14, map_loader_1_p15, map_loader_1_p16, map_loader_1_p17,
       map_loader_1_p18, map_loader_1_p19, map_loader_1_p20, map_loader_1_p21, map_loader_1_p22,
       map_loader_1_p23, map_loader_1_p24, map_loader_1_p25, map_loader_1_p26, map_loader_1_p27,
       map_loader_1_p28, map_loader_1_p29, map_loader_1_p30, map_loader_1_p31, map_loader_1_p32,
       map_loader_1_p33, map_loader_1_p34;

  Clock clock_1 (.out(clock_1_out));
  // Probe on map_loader_1_p3
  DotMatrix #(.inputtype("row"), .matrixcols(32), .matrixrows(32)) dotmatrix_1 (
    .row0(map_loader_1_p3), .row1(map_loader_1_p4), .row2(map_loader_1_p5), .row3(map_loader_1_p6),
    .row4(map_loader_1_p7), .row5(map_loader_1_p8), .row6(map_loader_1_p9), .row7(map_loader_1_p10),
    .row8(map_loader_1_p11), .row9(map_loader_1_p12), .row10(map_loader_1_p13), .row11(map_loader_1_p14),
    .row12(map_loader_1_p15), .row13(map_loader_1_p16), .row14(map_loader_1_p17), .row15(map_loader_1_p18),
    .row16(map_loader_1_p19), .row17(map_loader_1_p20), .row18(map_loader_1_p21), .row19(map_loader_1_p22),
    .row20(map_loader_1_p23), .row21(map_loader_1_p24), .row22(map_loader_1_p25), .row23(map_loader_1_p26),
    .row24(map_loader_1_p27), .row25(map_loader_1_p28), .row26(map_loader_1_p29), .row27(map_loader_1_p30),
    .row28(map_loader_1_p31), .row29(map_loader_1_p32), .row30(map_loader_1_p33), .row31(map_loader_1_p34));
  // map_loader map_loader_1: pin names not known; wires that end beside it: EnT, clock_1_out, map_loader_1_p3, map_loader_1_p4, map_loader_1_p5, map_loader_1_p6, map_loader_1_p7, map_loader_1_p8, map_loader_1_p9, map_loader_1_p10, map_loader_1_p11, map_loader_1_p12, map_loader_1_p13, map_loader_1_p14, map_loader_1_p15, map_loader_1_p16, map_loader_1_p17, map_loader_1_p18, map_loader_1_p19, map_loader_1_p20, map_loader_1_p21, map_loader_1_p22, map_loader_1_p23, map_loader_1_p24, map_loader_1_p25, map_loader_1_p26, map_loader_1_p27, map_loader_1_p28, map_loader_1_p29, map_loader_1_p30, map_loader_1_p31, map_loader_1_p32, map_loader_1_p33, map_loader_1_p34
endmodule
