// Logisim project tikanie.circ as structural Verilog
module Proc (
);

  wire cdm_8_mark5_1_p1, cdm_8_mark5_1_p2, cdm_8_mark5_1_p4, cdm_8_mark5_1_p5, cdm_8_mark5_1_p6,
       cdm_8_mark5_1_p7, cdm_8_mark5_1_p8, CI, code, data, I_Osel, in_out_prime, mem, nand_1_out, not_1_out,
       not_2_out, RAM;
  wire [3:0] I_Oadr;
  wire [7:0] cdm_8_mark5_1_p12, cdm_8_mark5_1_p13, I_Odat;
  wire [7:4] cdm_8_mark5_1_p11;

  // Probe on cdm_8_mark5_1_p5
  // Probe on cdm_8_mark5_1_p4
  // Probe on cdm_8_mark5_1_p2
  // Probe on cdm_8_mark5_1_p1
  // Probe on cdm_8_mark5_1_p6
  // Probe on cdm_8_mark5_1_p7
  Clock clock_1 (.out(CI));
  and and_1 (I_Osel, not_2_out, CI, data);
  Decoder decoder_1 (.out0(code), .out1(data), .sel(cdm_8_mark5_1_p8), .en(mem));
  // CdM_8_mark5 cdm_8_mark5_1: pin names not known; wires that end beside it: cdm_8_mark5_1_p1, cdm_8_mark5_1_p2, CI, cdm_8_mark5_1_p4, cdm_8_mark5_1_p5, cdm_8_mark5_1_p6, cdm_8_mark5_1_p7, cdm_8_mark5_1_p8, mem, in_out_prime, {cdm_8_mark5_1_p11, I_Oadr}, cdm_8_mark5_1_p12, cdm_8_mark5_1_p13
  not not_1 (not_1_out, in_out_prime);
  assign cdm_8_mark5_1_p13 = in_out_prime ? I_Odat : 8'bz;  // Controlled_Buffer controlled_buffer_1
  not not_2 (not_2_out, nand_1_out);
  and and_2 (RAM, nand_1_out, data);
  assign I_Odat = not_1_out ? cdm_8_mark5_1_p12 : 8'bz;  // Controlled_Buffer controlled_buffer_2
  nand nand_1 (nand_1_out, cdm_8_mark5_1_p11[4], cdm_8_mark5_1_p11[5], cdm_8_mark5_1_p11[6], cdm_8_mark5_1_p11[7]);
  ROM rom_1 (.addr({cdm_8_mark5_1_p11, I_Oadr}), .data(I_Odat), .sel(code));
  RAM ram_1 (.addr({cdm_8_mark5_1_p11, I_Oadr}), .data(I_Odat), .sel(RAM), .clk(CI), .ld(in_out_prime));  // open: clr

  // Other names for the same wires on the sheet: rd_wr_prime = in_out_prime
endmodule

module Snake (
);

  wire clock_1_out, clock_2_out, to1bit_1_a, to1bit_1_d, to1bit_1_s, to1bit_1_w;
  wire [6:0] keyboard_1_data;
  wire [31:0] head_1__0, head_1_out_7, head_1_out_8, head_1_out_9, head_1_out_10, head_1_out_11,
       head_1_out_12, head_1_out_13, head_1_out_14, head_1_out_15, head_1_out_16, head_1_out_17,
       head_1_out_18, head_1_out_19, head_1_out_20, head_1_out_21, head_1_out_22, head_1_out_23,
       head_1_out_24, head_1_out_25, head_1_out_26, head_1_out_27, head_1_out_28, head_1_out_29,
       head_1_out_30, head_1_out_31, head_1_out_32, head_1_out_33, head_1_out_34, head_1_out_35,
       head_1_out_36, head_1_out_37;

  Keyboard keyboard_1 (.clk(clock_1_out), .data(keyboard_1_data));  // open: re, clr, avail
  Clock clock_1 (.out(clock_1_out));
  Head head_1 (
    ._0(head_1__0), .out_22(head_1_out_22), .out_7(head_1_out_7), .out_23(head_1_out_23),
    .out_8(head_1_out_8), .out_24(head_1_out_24), .out_9(head_1_out_9), .out_25(head_1_out_25),
    .out_10(head_1_out_10), .out_26(head_1_out_26), .out_11(head_1_out_11), .out_27(head_1_out_27),
    .out_12(head_1_out_12), .out_28(head_1_out_28), .out_13(head_1_out_13), .out_29(head_1_out_29),
    .out_14(head_1_out_14), .out_30(head_1_out_30), .out_15(head_1_out_15), .out_31(head_1_out_31),
    .out_16(head_1_out_16), .out_32(head_1_out_32), .out_17(head_1_out_17), .out_33(head_1_out_33),
    .out_18(head_1_out_18), .out_34(head_1_out_34), .out_19(head_1_out_19), .out_35(head_1_out_35),
    .out_20(head_1_out_20), .out_36(head_1_out_36), .out_21(head_1_out_21), .out_37(head_1_out_37),
    .W(to1bit_1_w), .A(to1bit_1_a), .S(to1bit_1_s), .D(to1bit_1_d), .Clock(clock_2_out));
  to1bit to1bit_1 (.W(to1bit_1_w), .A(to1bit_1_a), .S(to1bit_1_s), .D(to1bit_1_d), .In(keyboard_1_data));
  Clock #(.highDuration(6), .lowDuration(6)) clock_2 (.out(clock_2_out));
  DotMatrix #(.inputtype("row"), .matrixcols(32), .matrixrows(32)) dotmatrix_1 (
    .row0(head_1_out_37), .row1(head_1_out_36), .row2(head_1_out_35), .row3(head_1_out_34),
    .row4(head_1_out_33), .row5(head_1_out_32), .row6(head_1_out_31), .row7(head_1_out_30),
    .row8(head_1_out_29), .row9(head_1_out_28), .row10(head_1_out_27), .row11(head_1_out_26),
    .row12(head_1_out_25), .row13(head_1_out_24), .row14(head_1_out_23), .row15(head_1_out_22),
    .row16(head_1_out_21), .row17(head_1_out_20), .row18(head_1_out_19), .row19(head_1_out_18),
    .row20(head_1_out_17), .row21(head_1_out_16), .row22(head_1_out_15), .row23(head_1_out_14),
    .row24(head_1_out_13), .row25(head_1_out_12), .row26(head_1_out_11), .row27(head_1_out_10),
    .row28(head_1_out_9), .row29(head_1_out_8), .row30(head_1_out_7), .row31(head_1__0));
endmodule

module Head (
  input  Clock,
  input  W,
  input  A,
  input  S,
  input  D,
  output [31:0] _0,
  output [31:0] out_7,
  output [31:0] out_8,
  output [31:0] out_9,
  output [31:0] out_10,
  output [31:0] out_11,
  output [31:0] out_12,
  output [31:0] out_13,
  output [31:0] out_14,
  output [31:0] out_15,
  output [31:0] out_16,
  output [31:0] out_17,
  output [31:0] out_18,
  output [31:0] out_19,
  output [31:0] out_20,
  output [31:0] out_21,
  output [31:0] out_22,
  output [31:0] out_23,
  output [31:0] out_24,
  output [31:0] out_25,
  output [31:0] out_26,
  output [31:0] out_27,
  output [31:0] out_28,
  output [31:0] out_29,
  output [31:0] out_30,
  output [31:0] out_31,
  output [31:0] out_32,
  output [31:0] out_33,
  output [31:0] out_34,
  output [31:0] out_35,
  output [31:0] out_36,
  output [31:0] out_37
);

  wire and_1_out, and_2_out, and_3_out, and_4_out, Clock_t, decoder_1_out0, decoder_1_out1, decoder_1_out2,
       decoder_1_out3, decoder_1_out4, decoder_1_out5, decoder_1_out6, decoder_1_out7, decoder_1_out8,
       decoder_1_out9, decoder_1_out10, decoder_1_out11, decoder_1_out12, decoder_1_out13, decoder_1_out14,
       decoder_1_out15, decoder_1_out16, decoder_1_out17, decoder_1_out18, decoder_1_out19, decoder_1_out20,
       decoder_1_out21, decoder_1_out22, decoder_1_out23, decoder_1_out24, decoder_1_out25, decoder_1_out26,
       decoder_1_out27, decoder_1_out28, decoder_1_out29, decoder_1_out30, decoder_1_out31, Down, Left,
       or_1_out, or_2_out, or_3_out, or_4_out, or_5_out, or_6_out, or_7_out, pull_resistor_2_node,
       pull_resistor_3_node, Right, Up;
  wire [4:0] counter_1_q, counter_2_q;

  Transistor #(.\type ("n"), .gate("br")) transistor_1 (.in(Clock), .out(Clock_t), .gate(or_1_out));
  Pull_Resistor pull_resistor_1 (.node(Clock_t));
  or or_1 (or_1_out, Up, Down, Left, Right);
  D_Flip_Flop d_ff_1 (.Q(Up), .preset(and_1_out), .reset(or_2_out));  // open: clk, D, Qn, en
  and and_1 (and_1_out, ~Down, W);  // AND_Gate
  or or_2 (or_2_out, D, A);
  D_Flip_Flop d_ff_2 (.Q(Down), .preset(and_2_out), .reset(or_3_out));  // open: clk, D, Qn, en
  and and_2 (and_2_out, ~Up, S);  // AND_Gate
  or or_3 (or_3_out, D, A);
  D_Flip_Flop d_ff_3 (.Q(Left), .preset(and_3_out), .reset(or_4_out));  // open: clk, D, Qn, en
  or or_4 (or_4_out, S, W);
  and and_3 (and_3_out, ~Right, A);  // AND_Gate
  D_Flip_Flop d_ff_4 (.Q(Right), .preset(and_4_out), .reset(or_5_out));  // open: clk, D, Qn, en
  or or_5 (or_5_out, S, W);
  and and_4 (and_4_out, ~Left, D);  // AND_Gate
  Counter #(.width(5), .max('h1f)) counter_1 (
    .load(Down), .Q(counter_1_q), .clk(pull_resistor_2_node));  // open: D, count, carry, clr
  Pull_Resistor pull_resistor_2 (.node(pull_resistor_2_node));
  Transistor transistor_2 (.in(Clock_t), .out(pull_resistor_2_node), .gate(or_6_out));
  or or_6 (or_6_out, Right, Left);
  Counter #(.width(5), .max('h1f)) counter_2 (
    .load(Left), .Q(counter_2_q), .clk(pull_resistor_3_node));  // open: D, count, carry, clr
  Pull_Resistor pull_resistor_3 (.node(pull_resistor_3_node));
  Transistor transistor_3 (.in(Clock_t), .out(pull_resistor_3_node), .gate(or_7_out));
  or or_7 (or_7_out, Up, Down);
  Decoder #(.select(5)) decoder_1 (
    .out0(decoder_1_out0), .out1(decoder_1_out1), .out2(decoder_1_out2), .out3(decoder_1_out3),
    .out4(decoder_1_out4), .out5(decoder_1_out5), .out6(decoder_1_out6), .out7(decoder_1_out7),
    .out8(decoder_1_out8), .out9(decoder_1_out9), .out10(decoder_1_out10), .out11(decoder_1_out11),
    .out12(decoder_1_out12), .out13(decoder_1_out13), .out14(decoder_1_out14), .out15(decoder_1_out15),
    .out16(decoder_1_out16), .out17(decoder_1_out17), .out18(decoder_1_out18), .out19(decoder_1_out19),
    .out20(decoder_1_out20), .out21(decoder_1_out21), .out22(decoder_1_out22), .out23(decoder_1_out23),
    .out24(decoder_1_out24), .out25(decoder_1_out25), .out26(decoder_1_out26), .out27(decoder_1_out27),
    .out28(decoder_1_out28), .out29(decoder_1_out29), .out30(decoder_1_out30), .out31(decoder_1_out31),
    .sel(counter_1_q));  // open: en
  go_line go_line_1 (.Out(out_7), .in_1(decoder_1_out1), .In(counter_2_q));
  go_line go_line_2 (.Out(_0), .in_1(decoder_1_out0), .In(counter_2_q));
  go_line go_line_3 (.Out(out_9), .in_1(decoder_1_out3), .In(counter_2_q));
  go_line go_line_4 (.Out(out_10), .in_1(decoder_1_out4), .In(counter_2_q));
  go_line go_line_5 (.Out(out_8), .in_1(decoder_1_out2), .In(counter_2_q));
  go_line go_line_6 (.Out(out_11), .in_1(decoder_1_out5), .In(counter_2_q));
  go_line go_line_7 (.Out(out_14), .in_1(decoder_1_out8), .In(counter_2_q));
  go_line go_line_8 (.Out(out_13), .in_1(decoder_1_out7), .In(counter_2_q));
  go_line go_line_9 (.Out(out_15), .in_1(decoder_1_out9), .In(counter_2_q));
  go_line go_line_10 (.Out(out_12), .in_1(decoder_1_out6), .In(counter_2_q));
  go_line go_line_11 (.Out(out_16), .in_1(decoder_1_out10), .In(counter_2_q));
  go_line go_line_12 (.Out(out_18), .in_1(decoder_1_out12), .In(counter_2_q));
  go_line go_line_13 (.Out(out_19), .in_1(decoder_1_out13), .In(counter_2_q));
  go_line go_line_14 (.Out(out_17), .in_1(decoder_1_out11), .In(counter_2_q));
  go_line go_line_15 (.Out(out_20), .in_1(decoder_1_out14), .In(counter_2_q));
  go_line go_line_16 (.Out(out_23), .in_1(decoder_1_out17), .In(counter_2_q));
  go_line go_line_17 (.Out(out_22), .in_1(decoder_1_out16), .In(counter_2_q));
  go_line go_line_18 (.Out(out_21), .in_1(decoder_1_out15), .In(counter_2_q));
  go_line go_line_19 (.Out(out_25), .in_1(decoder_1_out19), .In(counter_2_q));
  go_line go_line_20 (.Out(out_27), .in_1(decoder_1_out21), .In(counter_2_q));
  go_line go_line_21 (.Out(out_24), .in_1(decoder_1_out18), .In(counter_2_q));
  go_line go_line_22 (.Out(out_26), .in_1(decoder_1_out20), .In(counter_2_q));
  go_line go_line_23 (.Out(out_30), .in_1(decoder_1_out24), .In(counter_2_q));
  go_line go_line_24 (.Out(out_29), .in_1(decoder_1_out23), .In(counter_2_q));
  go_line go_line_25 (.Out(out_31), .in_1(decoder_1_out25), .In(counter_2_q));
  go_line go_line_26 (.Out(out_28), .in_1(decoder_1_out22), .In(counter_2_q));
  go_line go_line_27 (.Out(out_33), .in_1(decoder_1_out27), .In(counter_2_q));
  go_line go_line_28 (.Out(out_34), .in_1(decoder_1_out28), .In(counter_2_q));
  go_line go_line_29 (.Out(out_35), .in_1(decoder_1_out29), .In(counter_2_q));
  go_line go_line_30 (.Out(out_32), .in_1(decoder_1_out26), .In(counter_2_q));
  go_line go_line_31 (.Out(out_36), .in_1(decoder_1_out30), .In(counter_2_q));
  go_line go_line_32 (.Out(out_37), .in_1(decoder_1_out31), .In(counter_2_q));

  // Other names for the same wires on the sheet: Line_0[31:0] = _0; Line_1[31:0] = out_7; Line_2[31:0] = out_8;
  //   Line_3[31:0] = out_9; Line_4[31:0] = out_10; Line_5[31:0] = out_11; Line_6[31:0] = out_12;
  //   Line_7[31:0] = out_13; Line_8[31:0] = out_14; Line_9[31:0] = out_15; Line_10[31:0] = out_16;
  //   Line_11[31:0] = out_17; Line_12[31:0] = out_18; Line_13[31:0] = out_19; Line_14[31:0] = out_20;
  //   Line_15[31:0] = out_21; Line_16[31:0] = out_22; Line_17[31:0] = out_23; Line_18[31:0] = out_24;
  //   Line_19[31:0] = out_25; Line_20[31:0] = out_26; Line_21[31:0] = out_27; Line_22[31:0] = out_28;
  //   Line_23[31:0] = out_29; Line_24[31:0] = out_30; Line_25[31:0] = out_31; Line_26[31:0] = out_32;
  //   Line_27[31:0] = out_33; Line_28[31:0] = out_34; Line_29[31:0] = out_35; Line_30[31:0] = out_36;
  //   Line_31[31:0] = out_37
endmodule

module go_line (
  input  in_1,
  input  [4:0] In,
  output [31:0] Out
);

  wire [31:0] decoder_1_out31;

  Decoder #(.select(5)) decoder_1 (
    .out0(decoder_1_out31[31]), .out1(decoder_1_out31[30]), .out2(decoder_1_out31[29]),
    .out3(decoder_1_out31[28]), .out4(decoder_1_out31[27]), .out5(decoder_1_out31[26]),
    .out6(decoder_1_out31[25]), .out7(decoder_1_out31[24]), .out8(decoder_1_out31[23]),
    .out9(decoder_1_out31[22]), .out10(decoder_1_out31[21]), .out11(decoder_1_out31[20]),
    .out12(decoder_1_out31[19]), .out13(decoder_1_out31[18]), .out14(decoder_1_out31[17]),
    .out15(decoder_1_out31[16]), .out16(decoder_1_out31[15]), .out17(decoder_1_out31[14]),
    .out18(decoder_1_out31[13]), .out19(decoder_1_out31[12]), .out20(decoder_1_out31[11]),
    .out21(decoder_1_out31[10]), .out22(decoder_1_out31[9]), .out23(decoder_1_out31[8]),
    .out24(decoder_1_out31[7]), .out25(decoder_1_out31[6]), .out26(decoder_1_out31[5]),
    .out27(decoder_1_out31[4]), .out28(decoder_1_out31[3]), .out29(decoder_1_out31[2]),
    .out30(decoder_1_out31[1]), .out31(decoder_1_out31[0]), .sel(In));  // open: en
  Transistor #(.\type ("n"), .width(32)) transistor_1 (.in(decoder_1_out31), .out(Out), .gate(in_1));
  Pull_Resistor pull_resistor_1 (.node(Out));
endmodule

module to1bit (
  input  [6:0] In,
  output W,
  output A,
  output S,
  output D
);

  wire [6:0] xnor_1_out, xnor_2_out, xnor_3_out, xnor_4_out;

  assign xnor_1_out = ~(In ^ 7'b1110111);  // XNOR_Gate xnor_1, 7 bits wide
  assign xnor_2_out = ~(In ^ 7'b1100001);  // XNOR_Gate xnor_2, 7 bits wide
  assign xnor_3_out = ~(In ^ 7'b1110011);  // XNOR_Gate xnor_3, 7 bits wide
  assign xnor_4_out = ~(In ^ 7'b1100100);  // XNOR_Gate xnor_4, 7 bits wide
  and and_1 (W, xnor_1_out[0], xnor_1_out[1], xnor_1_out[2], xnor_1_out[3], xnor_1_out[4], xnor_1_out[5], xnor_1_out[6]);
  and and_2 (A, xnor_2_out[0], xnor_2_out[1], xnor_2_out[2], xnor_2_out[3], xnor_2_out[4], xnor_2_out[5], xnor_2_out[6]);
  and and_3 (S, xnor_3_out[0], xnor_3_out[1], xnor_3_out[2], xnor_3_out[3], xnor_3_out[4], xnor_3_out[5], xnor_3_out[6]);
  and and_4 (D, xnor_4_out[0], xnor_4_out[1], xnor_4_out[2], xnor_4_out[3], xnor_4_out[4], xnor_4_out[5], xnor_4_out[6]);
endmodule

module Main (
  input  Clock,
  input  W,
  input  A,
  input  S,
  input  D
);

  HeadXY headxy_1 (.Clock(W), .W(W));  // open: A, S, D, X_Head, Y_Head
endmodule

module HeadXY (
  input  Clock,
  input  W,
  input  A,
  input  S,
  input  D,
  output [4:0] X_Head,
  output [4:0] Y_Head
);

  wire and_1_out, and_2_out, and_3_out, and_4_out, Clock_t, Down, Left, or_1_out, or_2_out, or_3_out,
       or_4_out, or_5_out, or_6_out, or_7_out, pull_resistor_2_node, pull_resistor_3_node, Right, Up;

  Transistor #(.\type ("n"), .gate("br")) transistor_1 (.in(Clock), .out(Clock_t), .gate(or_1_out));
  Pull_Resistor pull_resistor_1 (.node(Clock_t));
  or or_1 (or_1_out, Up, Down, Left, Right);
  D_Flip_Flop d_ff_1 (.Q(Up), .preset(and_1_out), .reset(or_2_out));  // open: clk, D, Qn, en
  and and_1 (and_1_out, ~Down, W);  // AND_Gate
  or or_2 (or_2_out, D, A);
  D_Flip_Flop d_ff_2 (.Q(Down), .preset(and_2_out), .reset(or_3_out));  // open: clk, D, Qn, en
  and and_2 (and_2_out, ~Up, S);  // AND_Gate
  or or_3 (or_3_out, D, A);
  D_Flip_Flop d_ff_3 (.Q(Left), .preset(and_3_out), .reset(or_4_out));  // open: clk, D, Qn, en
  or or_4 (or_4_out, S, W);
  and and_3 (and_3_out, ~Right, A);  // AND_Gate
  D_Flip_Flop d_ff_4 (.Q(Right), .preset(and_4_out), .reset(or_5_out));  // open: clk, D, Qn, en
  and and_4 (and_4_out, ~Left, D);  // AND_Gate
  or or_5 (or_5_out, S, W);
  or or_6 (or_6_out, Up, Down);
  Counter #(.width(5), .max('h1f)) counter_1 (
    .load(Left), .Q(X_Head), .clk(pull_resistor_2_node));  // open: D, count, carry, clr
  Pull_Resistor pull_resistor_2 (.node(pull_resistor_2_node));
  Transistor transistor_2 (.in(Clock_t), .out(pull_resistor_2_node), .gate(or_6_out));
  Counter #(.width(5), .max('h1f)) counter_2 (
    .load(Down), .Q(Y_Head), .clk(pull_resistor_3_node));  // open: D, count, carry, clr
  Pull_Resistor pull_resistor_3 (.node(pull_resistor_3_node));
  Transistor transistor_3 (.in(Clock_t), .out(pull_resistor_3_node), .gate(or_7_out));
  or or_7 (or_7_out, Right, Left);
endmodule
